// Logisim project CPU.circ as structural Verilog: 25 circuits, main circuit ◇单周期MIPS
module \单周期MIPS  (
);

  wire and_1_out, and_2_out, and_3_out, and_4_out, and_5_out, CLK, comparator_1_lt, comparator_2_eq,
       comparator_3_eq, comparator_4_eq, comparator_5_eq, comparator_6_eq, Go, JAL, JMP, JR,
       mips_alu_1_equal, not_1_out, not_2_out, not_3_out, not_4_out, RegDst, RST, sel, select, SignedExt,
       SRAV, sys, \硬布线控制器_1_alu_src , \硬布线控制器_1_beq , \硬布线控制器_1_bne , \硬布线控制器_1_memtoreg ,
       \硬布线控制器_1_memwrite , \硬布线控制器_1_regwrite ;
  wire [0:0] or_1_out;
  wire [3:0] PC31_28, \硬布线控制器_1_alu_op ;
  wire [4:0] multiplexer_4_out, multiplexer_5_out, multiplexer_6_out, multiplexer_7_out, multiplexer_8_out,
       multiplexer_11_out;
  wire [5:0] FUNC, OP;
  wire [15:0] multiplexer_14_out, \总周期数 , \无条件分支数 , \条件分支成功数 ;
  wire [25:6] Jaddress;
  wire [27:0] PC_q;
  wire [31:0] adder_1_out, adder_2_out, bit_extender_1_out, bit_extender_2_out, bit_extender_3_out, JLast,
       LedData, mips_alu_1_result, multiplexer_1_out, multiplexer_2_out, multiplexer_9_out,
       multiplexer_10_out, multiplexer_12_out, multiplexer_13_out, multiplexer_15_out, R1, R2, ram_1_data,
       shifter_1_out;

  Button \u_总复位  (.out(RST));
  Button u_Go (.out(Go));
  Clock clock_1 (.out(CLK));
  Comparator #(.width(32)) comparator_1 (.a(R1), .b({32{1'b0}}), .lt(comparator_1_lt));  // open: gt, eq
  Comparator #(.width(6)) comparator_2 (.a(OP), .b(6'b000001), .eq(comparator_2_eq));  // open: gt, lt
  Hex_Digit_Display hex_digit_display_1 (.value(LedData[27:24]));  // open: dp
  Hex_Digit_Display hex_digit_display_2 (.value(LedData[31:28]));  // open: dp
  Multiplexer #(.width(32), .enable("false")) multiplexer_1 (
    .in0(adder_1_out), .in1(adder_2_out), .out(multiplexer_1_out), .sel(and_1_out));
  and and_1 (and_1_out, ~comparator_1_lt, comparator_2_eq);  // AND_Gate
  Hex_Digit_Display hex_digit_display_3 (.value(LedData[19:16]));  // open: dp
  Hex_Digit_Display hex_digit_display_4 (.value(LedData[23:20]));  // open: dp
  Multiplexer #(.select(2), .width(32), .enable("false")) multiplexer_2 (
    .in0(multiplexer_1_out), .in1(adder_2_out), .in2(JLast), .out(multiplexer_2_out), .sel({JMP, or_1_out[0]}));  // open: in3
  Hex_Digit_Display hex_digit_display_5 (.value(LedData[15:12]));  // open: dp
  Hex_Digit_Display hex_digit_display_6 (.value(LedData[11:8]));  // open: dp
  Hex_Digit_Display hex_digit_display_7 (.value(LedData[3:0]));  // open: dp
  Hex_Digit_Display hex_digit_display_8 (.value(LedData[7:4]));  // open: dp
  Register #(.width(32)) PC (.D(multiplexer_2_out), .en(sel), .Q({PC31_28, PC_q}), .clk(CLK), .clr(RST));
  Adder #(.width(32)) adder_1 (.a({PC31_28, PC_q}), .b(32'h4), .out(adder_1_out));  // open: cin, cout
  Multiplexer #(.width(32), .enable("false")) multiplexer_3 (
    .in0({PC31_28, Jaddress, FUNC, 2'b00}), .in1(R1), .out(JLast), .sel(JR));
  // Probe on \总周期数 
  // Probe on \无条件分支数 
  // Probe on \条件分支成功数 
  ROM #(.addrWidth(10), .dataWidth(32)) rom_1 (.addr(PC_q[11:2]), .data({OP, Jaddress, FUNC}));  // open: sel
  assign bit_extender_1_out = {{16{Jaddress[15]}}, {Jaddress[15:6], FUNC}};  // Bit_Extender bit_extender_1
  assign bit_extender_2_out = {{16{1'b0}}, {Jaddress[15:6], FUNC}};  // Bit_Extender bit_extender_2
  \硬布线控制器  \u_硬布线控制器_1  (
    .Func(FUNC), .OP(OP), .ALU_OP(\硬布线控制器_1_alu_op ), .MemToReg(\硬布线控制器_1_memtoreg ),
    .MemWrite(\硬布线控制器_1_memwrite ), .ALU_SRC(\硬布线控制器_1_alu_src ), .RegWrite(\硬布线控制器_1_regwrite ),
    .SysCALL(sys), .SignedExt(SignedExt), .RegDst(RegDst), .JR(JR), .JMP(JMP), .Beq(\硬布线控制器_1_beq ),
    .JAL(JAL), .Bne(\硬布线控制器_1_bne ));
  Multiplexer #(.width(5), .enable("false")) multiplexer_4 (
    .in0(Jaddress[25:21]), .in1({5{1'b1}}), .out(multiplexer_4_out), .sel(JR));
  Multiplexer #(.width(5), .enable("false")) multiplexer_5 (
    .in0(multiplexer_4_out), .in1(5'b00010), .out(multiplexer_5_out), .sel(sys));
  Multiplexer #(.width(5), .enable("false")) multiplexer_6 (
    .in0(Jaddress[20:16]), .in1(5'b00100), .out(multiplexer_6_out), .sel(sys));
  Multiplexer #(.width(5), .enable("false")) multiplexer_7 (
    .in0(Jaddress[20:16]), .in1(Jaddress[15:11]), .out(multiplexer_7_out), .sel(RegDst));
  Multiplexer #(.width(5), .enable("false")) multiplexer_8 (
    .in0(multiplexer_7_out), .in1({5{1'b1}}), .out(multiplexer_8_out), .sel(JAL));
  Multiplexer #(.width(32), .enable("false")) multiplexer_9 (
    .in0(bit_extender_1_out), .in1(bit_extender_2_out), .out(multiplexer_9_out), .sel(SignedExt));
  Counter #(.width(16), .max('hffff)) counter_1 (
    .count(sel), .Q(\总周期数 ), .clk(CLK), .clr(RST));  // open: load, D, carry
  MIPS_Regifile mips_regifile_1 (
    .Din(multiplexer_12_out), .Clk(CLK), .R1(R1), .R2(R2), .WE(\硬布线控制器_1_regwrite ),
    .W_num(multiplexer_8_out), .R1_num(multiplexer_5_out), .R2_num(multiplexer_6_out));
  Multiplexer #(.width(32), .enable("false")) multiplexer_10 (
    .in0(R2), .in1(multiplexer_9_out), .out(multiplexer_10_out), .sel(\硬布线控制器_1_alu_src ));
  Multiplexer #(.width(5), .enable("false")) multiplexer_11 (
    .in0(Jaddress[10:6]), .in1(R1[4:0]), .out(multiplexer_11_out), .sel(SRAV));
  Shifter #(.width(32)) shifter_1 (.in(multiplexer_9_out), .\dist (5'b00010), .out(shifter_1_out));
  not not_1 (not_1_out, mips_alu_1_equal);
  MIPS_ALU mips_alu_1 (
    .X(R1), .Y(multiplexer_10_out), .AluOP(\硬布线控制器_1_alu_op ), .Equal(mips_alu_1_equal),
    .Result({mips_alu_1_result[31:2], select, mips_alu_1_result[0]}), .shamt(multiplexer_11_out));  // open: Result_2
  Comparator #(.width(32)) comparator_3 (.a(R1), .b(32'h32), .eq(comparator_3_eq));  // open: gt, lt
  not not_2 (not_2_out, comparator_3_eq);
  and and_2 (and_2_out, \硬布线控制器_1_beq , mips_alu_1_equal);
  or or_1 (or_1_out[0], and_2_out, and_3_out);
  and and_3 (and_3_out, \硬布线控制器_1_bne , not_1_out);
  Multiplexer #(.width(32), .enable("false")) multiplexer_12 (
    .in0(multiplexer_15_out), .in1(adder_1_out), .out(multiplexer_12_out), .sel(JAL));
  Adder #(.width(32)) adder_2 (.a(shifter_1_out), .b(adder_1_out), .out(adder_2_out));  // open: cin, cout
  and and_4 (and_4_out, comparator_3_eq, sys);
  and and_5 (and_5_out, not_2_out, sys);
  Counter #(.width(16), .max('hffff)) counter_2 (
    .count(or_1_out[0]), .Q(\条件分支成功数 ), .clk(CLK), .clr(RST));  // open: load, D, carry
  not not_3 (not_3_out, \硬布线控制器_1_memwrite );
  or or_2 (sel, Go, not_4_out);
  not not_4 (not_4_out, and_4_out);
  Register #(.width(32)) register_1 (.D(R2), .en(and_5_out), .Q(LedData), .clk(CLK), .clr(RST));
  Multiplexer #(.width(32), .enable("false")) multiplexer_13 (
    .in0({mips_alu_1_result[31:2], select, mips_alu_1_result[0]}), .in1(ram_1_data),
    .out(multiplexer_13_out), .sel(\硬布线控制器_1_memtoreg ));
  RAM #(.addrWidth(10), .dataWidth(32), .bus("separate")) ram_1 (
    .addr(mips_alu_1_result[11:2]), .din(R2), .data(ram_1_data), .str(\硬布线控制器_1_memwrite ), .sel(sel),
    .clk(CLK), .ld(not_3_out), .clr(RST));
  Comparator #(.width(6)) comparator_4 (.a(OP), .b({6{1'b0}}), .eq(comparator_4_eq));  // open: gt, lt
  Comparator #(.width(6)) comparator_5 (.a(FUNC), .b(6'b000111), .eq(comparator_5_eq));  // open: gt, lt
  Comparator #(.width(6)) comparator_6 (.a(OP), .b(6'b100001), .eq(comparator_6_eq));  // open: gt, lt
  Multiplexer #(.width(16), .enable("false")) multiplexer_14 (
    .in0(multiplexer_13_out[15:0]), .in1(multiplexer_13_out[31:16]), .out(multiplexer_14_out), .sel(select));
  and and_6 (SRAV, comparator_4_eq, comparator_5_eq);
  assign bit_extender_3_out = {{16{multiplexer_14_out[15]}}, multiplexer_14_out};  // Bit_Extender bit_extender_3
  Counter #(.width(16), .max('hffff)) counter_3 (
    .count(JMP), .Q(\无条件分支数 ), .clk(CLK), .clr(RST));  // open: load, D, carry
  Multiplexer #(.width(32), .enable("false")) multiplexer_15 (
    .in0(multiplexer_13_out), .in1(bit_extender_3_out), .out(multiplexer_15_out), .sel(comparator_6_eq));

  // Other names for the same wires on the sheet: Jaddress[5:0] = FUNC; shamt[4:0] = Jaddress[10:6]

  // Notes on the sheet:
  //   数码管输出应该用寄存器锁存，否则显示数据只能一闪而过
  //   可以通过项目增加Logisim库的方式将前几次实验完成的电路作为子电路引入到本电路中使用
  //   数码管输出
  //   指令存储器
  //   指令字
  //   contents of rom_1 (hex, n*v repeats v):
  //   20110001 8100005 20110001 20120002 20130003 8100009 20110001 20120002 20130003 810000d 20110001
  //   20120002 20130003 8100011 20110001 20120002 20130003 c1000f7 20100001 20110001 118fc0 112020
  //   20020022 c 118882 12200001 8100015 112020 20020022 c 20110001 118880 112020 20020022 c 12200001
  //   810001f 20110001 118fc0 112020 20020022 c 1188c3 112020 20020022 c 118903 112020 20020022 c 118903
  //   112020 20020022 c 118903 112020 20020022 c 118903 112020 20020022 c 118903 112020 20020022 c 118903
  //   112020 20020022 c 118903 112020 20020022 c 20100001 109fc0 139fc3 8021 2012000c 24160003 26100001
  //   3210000f 20080008 20090001 139900 2709825 132020 20020022 c 1094022 1500fff9 22100001 2018000f
  //   2188024 108700 20080008 20090001 139902 2709825 132021 20020022 c 1094022 1500fff9 108702 2c9b022
  //   12c00001 8100050 4020 1084027 84400 3508ffff 82021 20020022 c 2010ffff 20110000 ae300000 22100001
  //   22310004 ae300000 22100001 22310004 ae300000 22100001 22310004 ae300000 22100001 22310004 ae300000
  //   22100001 22310004 ae300000 22100001 22310004 ae300000 22100001 22310004 ae300000 22100001 22310004
  //   ae300000 22100001 22310004 ae300000 22100001 22310004 ae300000 22100001 22310004 ae300000 22100001
  //   22310004 ae300000 22100001 22310004 ae300000 22100001 22310004 ae300000 22100001 22310004 ae300000
  //   22100001 22310004 22100001 8020 2011003c 8e130000 8e340000 274402a 11000002 ae330000 ae140000
  //   2231fffc 1611fff8 102020 20020022 c 22100004 2011003c 1611fff2 20020032 c 20090000 200b0010 34118483
  //   20120404 118c00 129400 36318281 22520404 ad310000 2328820 21290004 216bffff 1560fffb 200b0020
  //   20090000 85310000 112020 20020022 c 21290002 216bffff 1560fff9 20020032 c 2011000f 112020 20020022 c
  //   2231ffff 621fffb 20020032 c 2008ffff 20117777 112020 20020022 c 200b0010 2288826 112020 20020022 c
  //   216bffff 1560fffa 20020032 c 20080001 20090003 20110876 118d00 112020 20020022 c 200b0008 1118807
  //   1318807 112020 20020022 c 216bffff 1560fff9 20020032 c 20100000 22100001 102020 20020022 c 22100002
  //   102020 20020022 c 22100003 102020 20020022 c 22100004 102020 20020022 c 22100005 102020 20020022 c
  //   22100006 102020 20020022 c 22100007 102020 20020022 c 22100008 102020 20020022 20020022 c 3e00008
  //   OP
  //   Func
  //   rs
  //   rt
  //   rd
  //   Beq
  //   JMP
  //   JR
  //   Bne
  //   OP
  //   JAL
  //   Func
  //   Syscall
  //   MemToReg
  //   MemWrite
  //   AluOP
  //   AluSrcB
  //   RegWrite
  //   RegDst
  //   总复位信号应将除ROM以外所有存储组件全部清零
endmodule

// 单周期硬布线控制器
module \硬布线控制器  (
  input  [5:0] OP,
  input  [5:0] Func,
  output [3:0] ALU_OP,
  output MemToReg,
  output MemWrite,
  output ALU_SRC,
  output RegWrite,
  output SysCALL,
  output SignedExt,
  output RegDst,
  output Beq,
  output Bne,
  output JR,
  output JMP,
  output JAL
);

  \运算控制器  \u_运算控制器_1  (
    .OP0(OP[0]), .OP1(OP[1]), .OP2(OP[2]), .OP3(OP[3]), .OP4(OP[4]), .OP5(OP[5]), .F0(Func[0]), .F1(Func[1]),
    .F2(Func[2]), .F3(Func[3]), .F4(Func[4]), .F5(Func[5]), .S0(ALU_OP[0]), .S1(ALU_OP[1]), .S2(ALU_OP[2]),
    .S3(ALU_OP[3]));
  \控制信号生成  \u_控制信号生成_1  (
    .OP0(OP[0]), .OP1(OP[1]), .OP2(OP[2]), .OP3(OP[3]), .OP4(OP[4]), .OP5(OP[5]), .F0(Func[0]), .F1(Func[1]),
    .F2(Func[2]), .F3(Func[3]), .F4(Func[4]), .F5(Func[5]), .MemToReg(MemToReg), .MemWrite(MemWrite),
    .ALU_SRC(ALU_SRC), .RegWrite(RegWrite), .SysCALL(SysCALL), .SignedExt(SignedExt), .RegDst(RegDst),
    .BEQ(Beq), .BNE(Bne), .JR(JR), .JMP(JMP), .JAL(JAL));

  // Other names for the same wires on the sheet: OP_CODE[5:0] = OP

  // Notes on the sheet:
  //   运算器控制器，根据指令生成运算器功能选择信号
  //   控制信号生成，产生数据通路需要的其他控制信号
endmodule

// 运算器控制器
module \运算控制器  (
  input  OP0,
  input  OP1,
  input  OP2,
  input  OP3,
  input  OP4,
  input  OP5,
  input  F0,
  input  F1,
  input  F2,
  input  F3,
  input  F4,
  input  F5,
  output S0,
  output S1,
  output S2,
  output S3
);

  wire and_1_out, and_2_out, and_3_out, and_4_out, and_5_out, and_6_out, and_7_out, and_8_out, and_9_out,
       and_10_out, and_11_out, and_12_out, and_13_out, and_14_out, and_15_out, and_16_out, and_17_out,
       and_18_out, and_19_out, and_20_out, and_21_out, and_22_out, and_23_out, and_24_out, and_25_out,
       and_26_out, and_27_out, and_28_out, and_29_out, and_30_out, and_31_out, and_32_out, and_33_out,
       and_34_out, and_35_out, and_36_out, and_37_out, and_38_out, and_39_out, not_1_out, not_2_out,
       not_3_out, not_4_out, not_5_out, not_6_out, not_7_out, not_8_out, not_9_out, not_10_out, not_11_out,
       not_12_out, not_13_out, not_14_out, not_15_out, not_16_out, not_17_out, not_18_out, not_19_out,
       not_20_out, not_21_out, not_22_out, not_23_out, not_24_out, not_25_out, not_26_out, not_27_out,
       not_28_out, not_29_out, not_30_out, not_31_out, not_32_out, not_33_out, not_34_out, not_35_out,
       not_36_out, not_37_out, not_38_out, not_39_out, not_40_out, not_41_out, not_42_out, not_43_out,
       not_44_out, not_45_out, not_46_out, not_47_out, not_48_out, not_49_out, not_50_out, not_51_out,
       not_52_out, not_53_out, not_54_out, not_55_out, not_56_out, not_57_out, not_58_out, not_59_out,
       not_60_out, not_61_out, not_62_out, not_63_out, not_64_out, not_65_out, not_66_out, not_67_out,
       not_68_out, not_69_out, not_70_out, not_71_out, not_72_out, not_73_out, not_74_out, not_75_out,
       not_76_out, not_77_out, not_78_out, not_79_out, not_80_out, not_81_out, not_82_out, not_83_out,
       not_84_out, not_85_out, not_86_out, not_87_out, not_88_out, not_89_out, not_90_out, not_91_out,
       not_92_out, not_93_out, not_94_out, not_95_out, not_96_out, not_97_out, not_98_out, not_99_out,
       not_100_out, not_101_out, not_102_out, not_103_out, not_104_out, not_105_out, not_106_out,
       not_107_out, not_108_out, not_109_out, not_110_out, not_111_out, not_112_out, not_113_out,
       not_114_out, not_115_out, not_116_out, not_117_out, not_118_out, not_119_out, not_120_out,
       not_121_out, not_122_out, not_123_out, not_124_out, not_125_out, not_126_out, not_127_out,
       not_128_out, not_129_out, not_130_out, not_131_out, not_132_out, not_133_out, not_134_out,
       not_135_out, not_136_out, not_137_out, not_138_out, not_139_out, not_140_out, not_141_out,
       not_142_out, not_143_out, not_144_out, not_145_out, not_146_out, not_147_out, not_148_out,
       not_149_out, not_150_out, not_151_out, not_152_out, not_153_out, not_154_out, not_155_out,
       not_156_out, not_157_out, not_158_out, not_159_out, not_160_out, not_161_out, not_162_out,
       not_163_out, not_164_out, not_165_out, not_166_out, not_167_out, not_168_out, not_169_out,
       not_170_out, not_171_out, not_172_out, not_173_out, not_174_out, not_175_out, not_176_out,
       not_177_out, not_178_out, not_179_out, not_180_out, not_181_out, not_182_out, not_183_out,
       not_184_out, not_185_out, not_186_out, not_187_out, not_188_out, not_189_out, not_190_out,
       not_191_out, not_192_out, not_193_out, not_194_out, not_195_out, not_196_out, not_197_out,
       not_198_out, not_199_out, not_200_out, not_201_out, not_202_out, not_203_out, not_204_out,
       not_205_out, not_206_out, not_207_out, not_208_out, not_209_out, not_210_out, not_211_out,
       not_212_out, not_213_out, not_214_out, not_215_out, not_216_out, not_217_out, not_218_out,
       not_219_out, not_220_out, not_221_out, not_222_out, not_223_out, not_224_out, not_225_out,
       not_226_out, not_227_out, not_228_out, not_229_out, not_230_out, not_231_out, not_232_out,
       not_233_out, not_234_out, not_235_out, not_236_out, not_237_out, not_238_out, not_239_out,
       not_240_out, not_241_out, not_242_out, not_243_out, not_244_out, not_245_out, not_246_out,
       not_247_out, not_248_out, not_249_out, not_250_out, not_251_out, not_252_out, not_253_out,
       not_254_out, not_255_out, not_256_out, not_257_out, not_258_out, not_259_out, not_260_out,
       not_261_out, not_262_out, not_263_out, not_264_out, not_265_out, not_266_out, not_267_out,
       not_268_out, not_269_out, not_270_out, not_271_out;

  not not_1 (not_1_out, OP5);
  not not_2 (not_2_out, OP4);
  not not_3 (not_3_out, OP3);
  not not_4 (not_4_out, OP2);
  not not_5 (not_5_out, OP1);
  not not_6 (not_6_out, OP0);
  not not_7 (not_7_out, F5);
  not not_8 (not_8_out, F4);
  not not_9 (not_9_out, F3);
  not not_10 (not_10_out, F2);
  not not_11 (not_11_out, OP5);
  not not_12 (not_12_out, OP4);
  not not_13 (not_13_out, OP3);
  not not_14 (not_14_out, OP2);
  not not_15 (not_15_out, OP1);
  not not_16 (not_16_out, OP0);
  not not_17 (not_17_out, F4);
  not not_18 (not_18_out, F3);
  not not_19 (not_19_out, F2);
  not not_20 (not_20_out, F1);
  not not_21 (not_21_out, F0);
  not not_22 (not_22_out, OP5);
  not not_23 (not_23_out, OP4);
  not not_24 (not_24_out, OP3);
  not not_25 (not_25_out, OP2);
  not not_26 (not_26_out, OP1);
  not not_27 (not_27_out, OP0);
  not not_28 (not_28_out, F4);
  not not_29 (not_29_out, F3);
  not not_30 (not_30_out, F2);
  not not_31 (not_31_out, F1);
  not not_32 (not_32_out, OP5);
  not not_33 (not_33_out, OP4);
  not not_34 (not_34_out, OP3);
  not not_35 (not_35_out, OP2);
  not not_36 (not_36_out, OP1);
  not not_37 (not_37_out, OP0);
  not not_38 (not_38_out, F4);
  not not_39 (not_39_out, F3);
  not not_40 (not_40_out, F1);
  not not_41 (not_41_out, F0);
  not not_42 (not_42_out, OP5);
  not not_43 (not_43_out, OP4);
  not not_44 (not_44_out, OP3);
  not not_45 (not_45_out, OP2);
  not not_46 (not_46_out, OP1);
  not not_47 (not_47_out, OP0);
  not not_48 (not_48_out, F4);
  not not_49 (not_49_out, F2);
  not not_50 (not_50_out, F0);
  not not_51 (not_51_out, OP5);
  not not_52 (not_52_out, OP4);
  not not_53 (not_53_out, OP2);
  not not_54 (not_54_out, OP1);
  not not_55 (not_55_out, OP0);
  not not_56 (not_56_out, OP5);
  not not_57 (not_57_out, OP4);
  not not_58 (not_58_out, OP1);
  not not_59 (not_59_out, OP0);
  not not_60 (not_60_out, OP5);
  not not_61 (not_61_out, OP4);
  not not_62 (not_62_out, OP2);
  not not_63 (not_63_out, OP1);
  not not_64 (not_64_out, OP5);
  not not_65 (not_65_out, OP4);
  not not_66 (not_66_out, OP2);
  not not_67 (not_67_out, OP0);
  not not_68 (not_68_out, OP4);
  not not_69 (not_69_out, OP3);
  not not_70 (not_70_out, OP2);
  not not_71 (not_71_out, OP4);
  not not_72 (not_72_out, OP2);
  not not_73 (not_73_out, OP5);
  not not_74 (not_74_out, OP4);
  not not_75 (not_75_out, OP3);
  not not_76 (not_76_out, OP2);
  not not_77 (not_77_out, OP1);
  not not_78 (not_78_out, OP0);
  not not_79 (not_79_out, F5);
  not not_80 (not_80_out, F4);
  not not_81 (not_81_out, F3);
  not not_82 (not_82_out, OP5);
  not not_83 (not_83_out, OP4);
  not not_84 (not_84_out, OP3);
  not not_85 (not_85_out, OP2);
  not not_86 (not_86_out, OP1);
  not not_87 (not_87_out, OP0);
  not not_88 (not_88_out, F4);
  not not_89 (not_89_out, F3);
  not not_90 (not_90_out, F0);
  not not_91 (not_91_out, OP4);
  not not_92 (not_92_out, OP3);
  not not_93 (not_93_out, OP2);
  not not_94 (not_94_out, OP1);
  not not_95 (not_95_out, OP5);
  not not_96 (not_96_out, OP4);
  not not_97 (not_97_out, OP3);
  not not_98 (not_98_out, OP2);
  not not_99 (not_99_out, OP1);
  not not_100 (not_100_out, OP0);
  not not_101 (not_101_out, F5);
  not not_102 (not_102_out, F4);
  not not_103 (not_103_out, F3);
  not not_104 (not_104_out, F2);
  not not_105 (not_105_out, F0);
  not not_106 (not_106_out, OP5);
  not not_107 (not_107_out, OP4);
  not not_108 (not_108_out, OP3);
  not not_109 (not_109_out, OP2);
  not not_110 (not_110_out, OP1);
  not not_111 (not_111_out, OP0);
  not not_112 (not_112_out, F4);
  not not_113 (not_113_out, F3);
  not not_114 (not_114_out, F2);
  not not_115 (not_115_out, F0);
  not not_116 (not_116_out, OP5);
  not not_117 (not_117_out, OP4);
  not not_118 (not_118_out, OP3);
  not not_119 (not_119_out, OP2);
  not not_120 (not_120_out, OP1);
  not not_121 (not_121_out, OP0);
  not not_122 (not_122_out, F4);
  not not_123 (not_123_out, F3);
  not not_124 (not_124_out, F1);
  not not_125 (not_125_out, F0);
  not not_126 (not_126_out, OP5);
  not not_127 (not_127_out, OP4);
  not not_128 (not_128_out, OP3);
  not not_129 (not_129_out, OP2);
  not not_130 (not_130_out, OP1);
  not not_131 (not_131_out, OP0);
  not not_132 (not_132_out, F4);
  not not_133 (not_133_out, F3);
  not not_134 (not_134_out, OP5);
  not not_135 (not_135_out, OP4);
  not not_136 (not_136_out, OP3);
  not not_137 (not_137_out, OP2);
  not not_138 (not_138_out, OP1);
  not not_139 (not_139_out, OP0);
  not not_140 (not_140_out, F4);
  not not_141 (not_141_out, F2);
  not not_142 (not_142_out, F0);
  not not_143 (not_143_out, OP5);
  not not_144 (not_144_out, OP4);
  not not_145 (not_145_out, OP1);
  not not_146 (not_146_out, OP0);
  not not_147 (not_147_out, OP5);
  not not_148 (not_148_out, OP4);
  not not_149 (not_149_out, OP2);
  not not_150 (not_150_out, OP0);
  not not_151 (not_151_out, OP5);
  not not_152 (not_152_out, OP4);
  not not_153 (not_153_out, OP3);
  not not_154 (not_154_out, OP2);
  not not_155 (not_155_out, OP1);
  not not_156 (not_156_out, OP0);
  not not_157 (not_157_out, F4);
  not not_158 (not_158_out, F3);
  not not_159 (not_159_out, F2);
  not not_160 (not_160_out, F1);
  not not_161 (not_161_out, F0);
  not not_162 (not_162_out, OP5);
  not not_163 (not_163_out, OP4);
  not not_164 (not_164_out, OP3);
  not not_165 (not_165_out, OP2);
  not not_166 (not_166_out, OP1);
  not not_167 (not_167_out, OP0);
  not not_168 (not_168_out, F4);
  not not_169 (not_169_out, F3);
  not not_170 (not_170_out, F2);
  not not_171 (not_171_out, F1);
  not not_172 (not_172_out, OP5);
  not not_173 (not_173_out, OP4);
  not not_174 (not_174_out, OP3);
  not not_175 (not_175_out, OP2);
  not not_176 (not_176_out, OP1);
  not not_177 (not_177_out, OP0);
  not not_178 (not_178_out, F4);
  not not_179 (not_179_out, F3);
  not not_180 (not_180_out, F2);
  not not_181 (not_181_out, F0);
  not not_182 (not_182_out, OP5);
  not not_183 (not_183_out, OP4);
  not not_184 (not_184_out, OP3);
  not not_185 (not_185_out, OP2);
  not not_186 (not_186_out, OP1);
  not not_187 (not_187_out, OP0);
  not not_188 (not_188_out, F4);
  not not_189 (not_189_out, F3);
  not not_190 (not_190_out, F1);
  not not_191 (not_191_out, F0);
  not not_192 (not_192_out, OP5);
  not not_193 (not_193_out, OP4);
  not not_194 (not_194_out, OP3);
  not not_195 (not_195_out, OP2);
  not not_196 (not_196_out, OP1);
  not not_197 (not_197_out, OP0);
  not not_198 (not_198_out, F4);
  not not_199 (not_199_out, F2);
  not not_200 (not_200_out, OP5);
  not not_201 (not_201_out, OP4);
  not not_202 (not_202_out, OP2);
  not not_203 (not_203_out, OP1);
  not not_204 (not_204_out, OP0);
  not not_205 (not_205_out, OP5);
  not not_206 (not_206_out, OP4);
  not not_207 (not_207_out, OP1);
  not not_208 (not_208_out, OP0);
  not not_209 (not_209_out, OP5);
  not not_210 (not_210_out, OP4);
  not not_211 (not_211_out, OP2);
  not not_212 (not_212_out, OP1);
  not not_213 (not_213_out, OP4);
  not not_214 (not_214_out, OP3);
  not not_215 (not_215_out, OP2);
  not not_216 (not_216_out, OP4);
  not not_217 (not_217_out, OP2);
  not not_218 (not_218_out, OP4);
  not not_219 (not_219_out, OP3);
  not not_220 (not_220_out, OP2);
  not not_221 (not_221_out, OP1);
  not not_222 (not_222_out, OP5);
  not not_223 (not_223_out, OP4);
  not not_224 (not_224_out, OP3);
  not not_225 (not_225_out, OP2);
  not not_226 (not_226_out, OP1);
  not not_227 (not_227_out, OP0);
  not not_228 (not_228_out, F4);
  not not_229 (not_229_out, F3);
  not not_230 (not_230_out, F1);
  not not_231 (not_231_out, OP5);
  not not_232 (not_232_out, OP4);
  not not_233 (not_233_out, OP3);
  not not_234 (not_234_out, OP2);
  not not_235 (not_235_out, OP1);
  not not_236 (not_236_out, OP0);
  not not_237 (not_237_out, F4);
  not not_238 (not_238_out, F3);
  not not_239 (not_239_out, OP5);
  not not_240 (not_240_out, OP4);
  not not_241 (not_241_out, OP3);
  not not_242 (not_242_out, OP2);
  not not_243 (not_243_out, OP1);
  not not_244 (not_244_out, OP0);
  not not_245 (not_245_out, F4);
  not not_246 (not_246_out, F2);
  not not_247 (not_247_out, F0);
  not not_248 (not_248_out, OP5);
  not not_249 (not_249_out, OP4);
  not not_250 (not_250_out, OP3);
  not not_251 (not_251_out, OP2);
  not not_252 (not_252_out, OP1);
  not not_253 (not_253_out, OP0);
  not not_254 (not_254_out, F4);
  not not_255 (not_255_out, F2);
  not not_256 (not_256_out, OP5);
  not not_257 (not_257_out, OP4);
  not not_258 (not_258_out, OP2);
  not not_259 (not_259_out, OP0);
  not not_260 (not_260_out, OP5);
  not not_261 (not_261_out, OP4);
  not not_262 (not_262_out, OP1);
  not not_263 (not_263_out, OP5);
  not not_264 (not_264_out, OP4);
  not not_265 (not_265_out, OP3);
  not not_266 (not_266_out, OP2);
  not not_267 (not_267_out, OP1);
  not not_268 (not_268_out, OP0);
  not not_269 (not_269_out, F4);
  not not_270 (not_270_out, F3);
  not not_271 (not_271_out, F0);
  and and_1 (and_1_out, not_1_out, not_2_out, not_3_out, not_4_out, not_5_out, not_6_out, not_7_out, not_8_out, not_9_out, not_10_out, F1, F0);
  and and_2 (and_2_out, not_11_out, not_12_out, not_13_out, not_14_out, not_15_out, not_16_out, F5, not_17_out, not_18_out, not_19_out, not_20_out, not_21_out);
  and and_3 (and_3_out, not_22_out, not_23_out, not_24_out, not_25_out, not_26_out, not_27_out, F5, not_28_out, not_29_out, not_30_out, not_31_out, F0);
  and and_4 (and_4_out, not_32_out, not_33_out, not_34_out, not_35_out, not_36_out, not_37_out, F5, not_38_out, not_39_out, F2, not_40_out, not_41_out);
  and and_5 (and_5_out, not_42_out, not_43_out, not_44_out, not_45_out, not_46_out, not_47_out, F5, not_48_out, F3, not_49_out, F1, not_50_out);
  and and_6 (and_6_out, not_51_out, not_52_out, OP3, not_53_out, not_54_out, not_55_out);
  and and_7 (and_7_out, not_56_out, not_57_out, OP3, OP2, not_58_out, not_59_out);
  and and_8 (and_8_out, not_60_out, not_61_out, OP3, not_62_out, not_63_out, OP0);
  and and_9 (and_9_out, not_64_out, not_65_out, OP3, not_66_out, OP1, not_67_out);
  and and_10 (and_10_out, OP5, not_68_out, not_69_out, not_70_out, OP1, OP0);
  and and_11 (and_11_out, OP5, not_71_out, OP3, not_72_out, OP1, OP0);
  and and_12 (and_12_out, not_73_out, not_74_out, not_75_out, not_76_out, not_77_out, not_78_out, not_79_out, not_80_out, not_81_out, F2, F1, F0);
  and and_13 (and_13_out, not_82_out, not_83_out, not_84_out, not_85_out, not_86_out, not_87_out, F5, not_88_out, not_89_out, F2, F1, not_90_out);
  and and_14 (and_14_out, OP5, not_91_out, not_92_out, not_93_out, not_94_out, OP0);
  and and_15 (and_15_out, not_95_out, not_96_out, not_97_out, not_98_out, not_99_out, not_100_out, not_101_out, not_102_out, not_103_out, not_104_out, F1, not_105_out);
  and and_16 (and_16_out, not_106_out, not_107_out, not_108_out, not_109_out, not_110_out, not_111_out, F5, not_112_out, not_113_out, not_114_out, F1, not_115_out);
  and and_17 (and_17_out, not_116_out, not_117_out, not_118_out, not_119_out, not_120_out, not_121_out, F5, not_122_out, not_123_out, F2, not_124_out, not_125_out);
  and and_18 (and_18_out, not_126_out, not_127_out, not_128_out, not_129_out, not_130_out, not_131_out, F5, not_132_out, not_133_out, F2, F1, F0);
  and and_19 (and_19_out, not_134_out, not_135_out, not_136_out, not_137_out, not_138_out, not_139_out, F5, not_140_out, F3, not_141_out, F1, not_142_out);
  and and_20 (and_20_out, not_143_out, not_144_out, OP3, OP2, not_145_out, not_146_out);
  and and_21 (and_21_out, not_147_out, not_148_out, OP3, not_149_out, OP1, not_150_out);
  and and_22 (and_22_out, not_151_out, not_152_out, not_153_out, not_154_out, not_155_out, not_156_out, F5, not_157_out, not_158_out, not_159_out, not_160_out, not_161_out);
  and and_23 (and_23_out, not_162_out, not_163_out, not_164_out, not_165_out, not_166_out, not_167_out, F5, not_168_out, not_169_out, not_170_out, not_171_out, F0);
  and and_24 (and_24_out, not_172_out, not_173_out, not_174_out, not_175_out, not_176_out, not_177_out, F5, not_178_out, not_179_out, not_180_out, F1, not_181_out);
  and and_25 (and_25_out, not_182_out, not_183_out, not_184_out, not_185_out, not_186_out, not_187_out, F5, not_188_out, not_189_out, F2, not_190_out, not_191_out);
  and and_26 (and_26_out, not_192_out, not_193_out, not_194_out, not_195_out, not_196_out, not_197_out, F5, not_198_out, F3, not_199_out, F1, F0);
  and and_27 (and_27_out, not_200_out, not_201_out, OP3, not_202_out, not_203_out, not_204_out);
  and and_28 (and_28_out, not_205_out, not_206_out, OP3, OP2, not_207_out, not_208_out);
  and and_29 (and_29_out, not_209_out, not_210_out, OP3, not_211_out, not_212_out, OP0);
  and and_30 (and_30_out, OP5, not_213_out, not_214_out, not_215_out, OP1, OP0);
  and and_31 (and_31_out, OP5, not_216_out, OP3, not_217_out, OP1, OP0);
  and and_32 (and_32_out, OP5, not_218_out, not_219_out, not_220_out, not_221_out, OP0);
  and and_33 (and_33_out, not_222_out, not_223_out, not_224_out, not_225_out, not_226_out, not_227_out, F5, not_228_out, not_229_out, F2, not_230_out, F0);
  and and_34 (and_34_out, not_231_out, not_232_out, not_233_out, not_234_out, not_235_out, not_236_out, F5, not_237_out, not_238_out, F2, F1, F0);
  and and_35 (and_35_out, not_239_out, not_240_out, not_241_out, not_242_out, not_243_out, not_244_out, F5, not_245_out, F3, not_246_out, F1, not_247_out);
  and and_36 (and_36_out, not_248_out, not_249_out, not_250_out, not_251_out, not_252_out, not_253_out, F5, not_254_out, F3, not_255_out, F1, F0);
  and and_37 (and_37_out, not_256_out, not_257_out, OP3, not_258_out, OP1, not_259_out);
  and and_38 (and_38_out, not_260_out, not_261_out, OP3, OP2, not_262_out, OP0);
  and and_39 (and_39_out, not_263_out, not_264_out, not_265_out, not_266_out, not_267_out, not_268_out, F5, not_269_out, not_270_out, F2, F1, not_271_out);
  or or_1 (S1, and_15_out, and_16_out, and_17_out, and_18_out, and_19_out, and_20_out, and_21_out);
  or or_2 (S2, and_22_out, and_23_out, and_24_out, and_25_out, and_26_out, and_27_out, and_28_out, and_29_out, and_30_out, and_31_out, and_32_out);
  or or_3 (S3, and_33_out, and_34_out, and_35_out, and_36_out, and_37_out, and_38_out, and_39_out);
  or or_4 (S0, and_1_out, and_2_out, and_3_out, and_4_out, and_5_out, and_6_out, and_7_out, and_8_out, and_9_out, and_10_out, and_11_out, and_12_out, and_13_out, and_14_out);
endmodule

// 控制信号生成
module \控制信号生成  (
  input  OP0,
  input  OP1,
  input  OP2,
  input  OP3,
  input  OP4,
  input  OP5,
  input  F0,
  input  F1,
  input  F2,
  input  F3,
  input  F4,
  input  F5,
  output MemToReg,
  output MemWrite,
  output ALU_SRC,
  output RegWrite,
  output SysCALL,
  output SignedExt,
  output RegDst,
  output BEQ,
  output BNE,
  output JR,
  output JMP,
  output JAL
);

  wire and_1_out, and_2_out, and_4_out, and_5_out, and_6_out, and_7_out, and_8_out, and_9_out, and_10_out,
       and_11_out, and_12_out, and_13_out, and_14_out, and_15_out, and_16_out, and_17_out, and_18_out,
       and_19_out, and_20_out, and_21_out, and_22_out, and_23_out, and_24_out, and_25_out, and_26_out,
       and_27_out, and_28_out, and_29_out, and_30_out, and_31_out, and_32_out, and_34_out, and_35_out,
       and_36_out, and_37_out, and_38_out, and_39_out, and_40_out, and_41_out, and_42_out, and_43_out,
       and_44_out, and_45_out, and_46_out, and_47_out, and_48_out, and_52_out, and_53_out, and_54_out,
       not_1_out, not_2_out, not_3_out, not_4_out, not_5_out, not_6_out, not_7_out, not_8_out, not_9_out,
       not_10_out, not_11_out, not_12_out, not_13_out, not_14_out, not_15_out, not_16_out, not_17_out,
       not_18_out, not_19_out, not_20_out, not_21_out, not_22_out, not_23_out, not_24_out, not_25_out,
       not_26_out, not_27_out, not_28_out, not_29_out, not_30_out, not_31_out, not_32_out, not_33_out,
       not_34_out, not_35_out, not_36_out, not_37_out, not_38_out, not_39_out, not_40_out, not_41_out,
       not_42_out, not_43_out, not_44_out, not_45_out, not_46_out, not_47_out, not_48_out, not_49_out,
       not_50_out, not_51_out, not_52_out, not_53_out, not_54_out, not_55_out, not_56_out, not_57_out,
       not_58_out, not_59_out, not_60_out, not_61_out, not_62_out, not_63_out, not_64_out, not_65_out,
       not_66_out, not_67_out, not_68_out, not_69_out, not_70_out, not_71_out, not_72_out, not_73_out,
       not_74_out, not_75_out, not_76_out, not_77_out, not_78_out, not_79_out, not_80_out, not_81_out,
       not_82_out, not_83_out, not_84_out, not_85_out, not_86_out, not_87_out, not_88_out, not_89_out,
       not_90_out, not_91_out, not_92_out, not_93_out, not_94_out, not_95_out, not_96_out, not_97_out,
       not_98_out, not_99_out, not_100_out, not_101_out, not_102_out, not_103_out, not_104_out, not_105_out,
       not_106_out, not_107_out, not_108_out, not_109_out, not_110_out, not_111_out, not_112_out,
       not_113_out, not_114_out, not_115_out, not_116_out, not_117_out, not_118_out, not_119_out,
       not_120_out, not_121_out, not_122_out, not_123_out, not_124_out, not_125_out, not_126_out,
       not_127_out, not_128_out, not_129_out, not_130_out, not_131_out, not_132_out, not_133_out,
       not_134_out, not_135_out, not_136_out, not_137_out, not_138_out, not_139_out, not_140_out,
       not_141_out, not_142_out, not_143_out, not_144_out, not_145_out, not_146_out, not_147_out,
       not_148_out, not_149_out, not_150_out, not_151_out, not_152_out, not_153_out, not_154_out,
       not_155_out, not_156_out, not_157_out, not_158_out, not_159_out, not_160_out, not_161_out,
       not_162_out, not_163_out, not_164_out, not_165_out, not_166_out, not_167_out, not_168_out,
       not_169_out, not_170_out, not_171_out, not_172_out, not_173_out, not_174_out, not_175_out,
       not_176_out, not_177_out, not_178_out, not_179_out, not_180_out, not_181_out, not_182_out,
       not_183_out, not_184_out, not_185_out, not_186_out, not_187_out, not_188_out, not_189_out,
       not_190_out, not_191_out, not_192_out, not_193_out, not_194_out, not_195_out, not_196_out,
       not_197_out, not_198_out, not_199_out, not_200_out, not_201_out, not_202_out, not_203_out,
       not_204_out, not_205_out, not_206_out, not_207_out, not_208_out, not_209_out, not_210_out,
       not_211_out, not_212_out, not_213_out, not_214_out, not_215_out, not_216_out, not_217_out,
       not_218_out, not_219_out, not_220_out, not_221_out, not_222_out, not_223_out, not_224_out,
       not_225_out, not_226_out, not_227_out, not_228_out, not_229_out, not_230_out, not_231_out,
       not_232_out, not_233_out, not_234_out, not_235_out, not_236_out, not_237_out, not_238_out,
       not_239_out, not_240_out, not_241_out, not_242_out, not_243_out, not_244_out, not_245_out,
       not_246_out, not_247_out, not_248_out, not_249_out, not_250_out, not_251_out, not_252_out,
       not_253_out, not_254_out, not_255_out, not_256_out, not_257_out, not_258_out, not_259_out,
       not_260_out, not_261_out, not_262_out, not_263_out, not_264_out, not_265_out, not_266_out,
       not_267_out, not_268_out, not_269_out, not_270_out, not_271_out, not_272_out, not_273_out,
       not_274_out, not_275_out, not_276_out, not_277_out, not_278_out, not_279_out, not_280_out,
       not_281_out, not_282_out, not_283_out, not_284_out, not_285_out, not_286_out, not_287_out,
       not_288_out, not_289_out, not_290_out, not_291_out, not_292_out, not_293_out, not_294_out,
       not_295_out, not_296_out, not_297_out, not_298_out, not_299_out, not_300_out, not_301_out,
       not_302_out, not_303_out, not_304_out, not_305_out, not_306_out, not_307_out, not_308_out,
       not_309_out, not_310_out, not_311_out, not_312_out, not_313_out, not_314_out, not_315_out,
       not_316_out, not_317_out, not_318_out, not_319_out, not_320_out, not_321_out, not_322_out,
       not_323_out, not_324_out, not_325_out, not_326_out, not_327_out, not_328_out, not_329_out,
       not_330_out, not_331_out, not_332_out, not_333_out, not_334_out, not_335_out, not_336_out,
       not_337_out, not_338_out, not_339_out, not_340_out, not_341_out, not_342_out, not_343_out,
       not_344_out, not_345_out, not_346_out, not_347_out, not_348_out, not_349_out, not_350_out,
       not_351_out, not_352_out, not_353_out, not_354_out, not_355_out, not_356_out, not_357_out,
       not_358_out, not_359_out, not_360_out, not_361_out, not_362_out, not_363_out, not_364_out,
       not_365_out, not_366_out, not_367_out, not_368_out, not_369_out, not_370_out, not_371_out,
       not_372_out, not_373_out, not_374_out, not_375_out, not_376_out, not_377_out, not_378_out,
       not_379_out, not_380_out, not_381_out, not_382_out;

  not not_1 (not_1_out, OP4);
  not not_2 (not_2_out, OP3);
  not not_3 (not_3_out, OP2);
  not not_4 (not_4_out, OP4);
  not not_5 (not_5_out, OP3);
  not not_6 (not_6_out, OP2);
  not not_7 (not_7_out, OP1);
  not not_8 (not_8_out, OP4);
  not not_9 (not_9_out, OP2);
  not not_10 (not_10_out, OP5);
  not not_11 (not_11_out, OP4);
  not not_12 (not_12_out, OP2);
  not not_13 (not_13_out, OP1);
  not not_14 (not_14_out, OP0);
  not not_15 (not_15_out, OP5);
  not not_16 (not_16_out, OP4);
  not not_17 (not_17_out, OP1);
  not not_18 (not_18_out, OP0);
  not not_19 (not_19_out, OP5);
  not not_20 (not_20_out, OP4);
  not not_21 (not_21_out, OP2);
  not not_22 (not_22_out, OP1);
  not not_23 (not_23_out, OP5);
  not not_24 (not_24_out, OP4);
  not not_25 (not_25_out, OP2);
  not not_26 (not_26_out, OP0);
  not not_27 (not_27_out, OP5);
  not not_28 (not_28_out, OP4);
  not not_29 (not_29_out, OP1);
  not not_30 (not_30_out, OP4);
  not not_31 (not_31_out, OP3);
  not not_32 (not_32_out, OP2);
  not not_33 (not_33_out, OP4);
  not not_34 (not_34_out, OP2);
  not not_35 (not_35_out, OP4);
  not not_36 (not_36_out, OP3);
  not not_37 (not_37_out, OP2);
  not not_38 (not_38_out, OP1);
  not not_39 (not_39_out, OP5);
  not not_40 (not_40_out, OP4);
  not not_41 (not_41_out, OP3);
  not not_42 (not_42_out, OP2);
  not not_43 (not_43_out, OP1);
  not not_44 (not_44_out, OP0);
  not not_45 (not_45_out, F5);
  not not_46 (not_46_out, F4);
  not not_47 (not_47_out, F3);
  not not_48 (not_48_out, F2);
  not not_49 (not_49_out, F1);
  not not_50 (not_50_out, F0);
  not not_51 (not_51_out, OP5);
  not not_52 (not_52_out, OP4);
  not not_53 (not_53_out, OP3);
  not not_54 (not_54_out, OP2);
  not not_55 (not_55_out, OP1);
  not not_56 (not_56_out, OP0);
  not not_57 (not_57_out, F5);
  not not_58 (not_58_out, F4);
  not not_59 (not_59_out, F3);
  not not_60 (not_60_out, F2);
  not not_61 (not_61_out, OP5);
  not not_62 (not_62_out, OP4);
  not not_63 (not_63_out, OP3);
  not not_64 (not_64_out, OP2);
  not not_65 (not_65_out, OP1);
  not not_66 (not_66_out, OP0);
  not not_67 (not_67_out, F5);
  not not_68 (not_68_out, F4);
  not not_69 (not_69_out, F3);
  not not_70 (not_70_out, F2);
  not not_71 (not_71_out, F0);
  not not_72 (not_72_out, OP5);
  not not_73 (not_73_out, OP4);
  not not_74 (not_74_out, OP3);
  not not_75 (not_75_out, OP2);
  not not_76 (not_76_out, OP1);
  not not_77 (not_77_out, OP0);
  not not_78 (not_78_out, F4);
  not not_79 (not_79_out, F3);
  not not_80 (not_80_out, F2);
  not not_81 (not_81_out, F1);
  not not_82 (not_82_out, F0);
  not not_83 (not_83_out, OP5);
  not not_84 (not_84_out, OP4);
  not not_85 (not_85_out, OP3);
  not not_86 (not_86_out, OP2);
  not not_87 (not_87_out, OP1);
  not not_88 (not_88_out, OP0);
  not not_89 (not_89_out, F4);
  not not_90 (not_90_out, F3);
  not not_91 (not_91_out, F2);
  not not_92 (not_92_out, F1);
  not not_93 (not_93_out, OP5);
  not not_94 (not_94_out, OP4);
  not not_95 (not_95_out, OP3);
  not not_96 (not_96_out, OP2);
  not not_97 (not_97_out, OP1);
  not not_98 (not_98_out, OP0);
  not not_99 (not_99_out, F4);
  not not_100 (not_100_out, F3);
  not not_101 (not_101_out, F2);
  not not_102 (not_102_out, F0);
  not not_103 (not_103_out, OP5);
  not not_104 (not_104_out, OP4);
  not not_105 (not_105_out, OP3);
  not not_106 (not_106_out, OP2);
  not not_107 (not_107_out, OP1);
  not not_108 (not_108_out, OP0);
  not not_109 (not_109_out, F4);
  not not_110 (not_110_out, F3);
  not not_111 (not_111_out, F1);
  not not_112 (not_112_out, F0);
  not not_113 (not_113_out, OP5);
  not not_114 (not_114_out, OP4);
  not not_115 (not_115_out, OP3);
  not not_116 (not_116_out, OP2);
  not not_117 (not_117_out, OP1);
  not not_118 (not_118_out, OP0);
  not not_119 (not_119_out, F4);
  not not_120 (not_120_out, F3);
  not not_121 (not_121_out, F1);
  not not_122 (not_122_out, OP5);
  not not_123 (not_123_out, OP4);
  not not_124 (not_124_out, OP3);
  not not_125 (not_125_out, OP2);
  not not_126 (not_126_out, OP1);
  not not_127 (not_127_out, OP0);
  not not_128 (not_128_out, F4);
  not not_129 (not_129_out, F3);
  not not_130 (not_130_out, OP5);
  not not_131 (not_131_out, OP4);
  not not_132 (not_132_out, OP3);
  not not_133 (not_133_out, OP2);
  not not_134 (not_134_out, OP1);
  not not_135 (not_135_out, OP0);
  not not_136 (not_136_out, F4);
  not not_137 (not_137_out, F2);
  not not_138 (not_138_out, F0);
  not not_139 (not_139_out, OP5);
  not not_140 (not_140_out, OP4);
  not not_141 (not_141_out, OP3);
  not not_142 (not_142_out, OP2);
  not not_143 (not_143_out, OP1);
  not not_144 (not_144_out, OP0);
  not not_145 (not_145_out, F4);
  not not_146 (not_146_out, F2);
  not not_147 (not_147_out, OP5);
  not not_148 (not_148_out, OP4);
  not not_149 (not_149_out, OP3);
  not not_150 (not_150_out, OP2);
  not not_151 (not_151_out, OP5);
  not not_152 (not_152_out, OP4);
  not not_153 (not_153_out, OP2);
  not not_154 (not_154_out, OP1);
  not not_155 (not_155_out, OP0);
  not not_156 (not_156_out, OP5);
  not not_157 (not_157_out, OP4);
  not not_158 (not_158_out, OP1);
  not not_159 (not_159_out, OP0);
  not not_160 (not_160_out, OP5);
  not not_161 (not_161_out, OP4);
  not not_162 (not_162_out, OP2);
  not not_163 (not_163_out, OP1);
  not not_164 (not_164_out, OP5);
  not not_165 (not_165_out, OP4);
  not not_166 (not_166_out, OP2);
  not not_167 (not_167_out, OP0);
  not not_168 (not_168_out, OP5);
  not not_169 (not_169_out, OP4);
  not not_170 (not_170_out, OP1);
  not not_171 (not_171_out, OP4);
  not not_172 (not_172_out, OP3);
  not not_173 (not_173_out, OP2);
  not not_174 (not_174_out, OP5);
  not not_175 (not_175_out, OP4);
  not not_176 (not_176_out, OP3);
  not not_177 (not_177_out, OP2);
  not not_178 (not_178_out, OP1);
  not not_179 (not_179_out, OP0);
  not not_180 (not_180_out, F5);
  not not_181 (not_181_out, F4);
  not not_182 (not_182_out, F3);
  not not_183 (not_183_out, OP5);
  not not_184 (not_184_out, OP4);
  not not_185 (not_185_out, OP3);
  not not_186 (not_186_out, OP2);
  not not_187 (not_187_out, OP1);
  not not_188 (not_188_out, OP0);
  not not_189 (not_189_out, F4);
  not not_190 (not_190_out, F3);
  not not_191 (not_191_out, F0);
  not not_192 (not_192_out, OP4);
  not not_193 (not_193_out, OP3);
  not not_194 (not_194_out, OP2);
  not not_195 (not_195_out, OP1);
  not not_196 (not_196_out, OP5);
  not not_197 (not_197_out, OP4);
  not not_198 (not_198_out, OP3);
  not not_199 (not_199_out, OP2);
  not not_200 (not_200_out, OP1);
  not not_201 (not_201_out, OP0);
  not not_202 (not_202_out, F5);
  not not_203 (not_203_out, F4);
  not not_204 (not_204_out, F1);
  not not_205 (not_205_out, F0);
  not not_206 (not_206_out, OP5);
  not not_207 (not_207_out, OP4);
  not not_208 (not_208_out, OP2);
  not not_209 (not_209_out, OP1);
  not not_210 (not_210_out, OP5);
  not not_211 (not_211_out, OP4);
  not not_212 (not_212_out, OP1);
  not not_213 (not_213_out, OP5);
  not not_214 (not_214_out, OP4);
  not not_215 (not_215_out, OP3);
  not not_216 (not_216_out, OP2);
  not not_217 (not_217_out, OP1);
  not not_218 (not_218_out, OP0);
  not not_219 (not_219_out, F5);
  not not_220 (not_220_out, F4);
  not not_221 (not_221_out, F3);
  not not_222 (not_222_out, F2);
  not not_223 (not_223_out, F1);
  not not_224 (not_224_out, F0);
  not not_225 (not_225_out, OP5);
  not not_226 (not_226_out, OP4);
  not not_227 (not_227_out, OP3);
  not not_228 (not_228_out, OP2);
  not not_229 (not_229_out, OP1);
  not not_230 (not_230_out, OP0);
  not not_231 (not_231_out, F5);
  not not_232 (not_232_out, F4);
  not not_233 (not_233_out, F3);
  not not_234 (not_234_out, F2);
  not not_235 (not_235_out, OP5);
  not not_236 (not_236_out, OP4);
  not not_237 (not_237_out, OP3);
  not not_238 (not_238_out, OP2);
  not not_239 (not_239_out, OP1);
  not not_240 (not_240_out, OP0);
  not not_241 (not_241_out, F5);
  not not_242 (not_242_out, F4);
  not not_243 (not_243_out, F3);
  not not_244 (not_244_out, F2);
  not not_245 (not_245_out, F0);
  not not_246 (not_246_out, OP5);
  not not_247 (not_247_out, OP4);
  not not_248 (not_248_out, OP3);
  not not_249 (not_249_out, OP2);
  not not_250 (not_250_out, OP1);
  not not_251 (not_251_out, OP0);
  not not_252 (not_252_out, F4);
  not not_253 (not_253_out, F3);
  not not_254 (not_254_out, F2);
  not not_255 (not_255_out, F1);
  not not_256 (not_256_out, F0);
  not not_257 (not_257_out, OP5);
  not not_258 (not_258_out, OP4);
  not not_259 (not_259_out, OP3);
  not not_260 (not_260_out, OP2);
  not not_261 (not_261_out, OP1);
  not not_262 (not_262_out, OP0);
  not not_263 (not_263_out, F4);
  not not_264 (not_264_out, F3);
  not not_265 (not_265_out, F2);
  not not_266 (not_266_out, F1);
  not not_267 (not_267_out, OP5);
  not not_268 (not_268_out, OP4);
  not not_269 (not_269_out, OP3);
  not not_270 (not_270_out, OP2);
  not not_271 (not_271_out, OP1);
  not not_272 (not_272_out, OP0);
  not not_273 (not_273_out, F4);
  not not_274 (not_274_out, F3);
  not not_275 (not_275_out, F2);
  not not_276 (not_276_out, F0);
  not not_277 (not_277_out, OP5);
  not not_278 (not_278_out, OP4);
  not not_279 (not_279_out, OP3);
  not not_280 (not_280_out, OP2);
  not not_281 (not_281_out, OP1);
  not not_282 (not_282_out, OP0);
  not not_283 (not_283_out, F4);
  not not_284 (not_284_out, F3);
  not not_285 (not_285_out, F1);
  not not_286 (not_286_out, F0);
  not not_287 (not_287_out, OP5);
  not not_288 (not_288_out, OP4);
  not not_289 (not_289_out, OP3);
  not not_290 (not_290_out, OP2);
  not not_291 (not_291_out, OP1);
  not not_292 (not_292_out, OP0);
  not not_293 (not_293_out, F4);
  not not_294 (not_294_out, F3);
  not not_295 (not_295_out, F1);
  not not_296 (not_296_out, OP5);
  not not_297 (not_297_out, OP4);
  not not_298 (not_298_out, OP3);
  not not_299 (not_299_out, OP2);
  not not_300 (not_300_out, OP1);
  not not_301 (not_301_out, OP0);
  not not_302 (not_302_out, F4);
  not not_303 (not_303_out, F3);
  not not_304 (not_304_out, OP5);
  not not_305 (not_305_out, OP4);
  not not_306 (not_306_out, OP3);
  not not_307 (not_307_out, OP2);
  not not_308 (not_308_out, OP1);
  not not_309 (not_309_out, OP0);
  not not_310 (not_310_out, F4);
  not not_311 (not_311_out, F2);
  not not_312 (not_312_out, F0);
  not not_313 (not_313_out, OP5);
  not not_314 (not_314_out, OP4);
  not not_315 (not_315_out, OP3);
  not not_316 (not_316_out, OP2);
  not not_317 (not_317_out, OP1);
  not not_318 (not_318_out, OP0);
  not not_319 (not_319_out, F4);
  not not_320 (not_320_out, F2);
  not not_321 (not_321_out, OP5);
  not not_322 (not_322_out, OP4);
  not not_323 (not_323_out, OP3);
  not not_324 (not_324_out, OP2);
  not not_325 (not_325_out, OP1);
  not not_326 (not_326_out, OP0);
  not not_327 (not_327_out, F5);
  not not_328 (not_328_out, F4);
  not not_329 (not_329_out, F3);
  not not_330 (not_330_out, OP5);
  not not_331 (not_331_out, OP4);
  not not_332 (not_332_out, OP3);
  not not_333 (not_333_out, OP2);
  not not_334 (not_334_out, OP1);
  not not_335 (not_335_out, OP0);
  not not_336 (not_336_out, F4);
  not not_337 (not_337_out, F3);
  not not_338 (not_338_out, F0);
  not not_339 (not_339_out, OP5);
  not not_340 (not_340_out, OP4);
  not not_341 (not_341_out, OP3);
  not not_342 (not_342_out, OP1);
  not not_343 (not_343_out, OP0);
  not not_344 (not_344_out, OP5);
  not not_345 (not_345_out, OP4);
  not not_346 (not_346_out, OP3);
  not not_347 (not_347_out, OP1);
  not not_348 (not_348_out, OP5);
  not not_349 (not_349_out, OP4);
  not not_350 (not_350_out, OP3);
  not not_351 (not_351_out, OP2);
  not not_352 (not_352_out, OP1);
  not not_353 (not_353_out, OP0);
  not not_354 (not_354_out, F5);
  not not_355 (not_355_out, F4);
  not not_356 (not_356_out, F2);
  not not_357 (not_357_out, F1);
  not not_358 (not_358_out, F0);
  not not_359 (not_359_out, OP5);
  not not_360 (not_360_out, OP4);
  not not_361 (not_361_out, OP3);
  not not_362 (not_362_out, OP2);
  not not_363 (not_363_out, OP1);
  not not_364 (not_364_out, OP0);
  not not_365 (not_365_out, F5);
  not not_366 (not_366_out, F4);
  not not_367 (not_367_out, F2);
  not not_368 (not_368_out, F1);
  not not_369 (not_369_out, F0);
  not not_370 (not_370_out, OP5);
  not not_371 (not_371_out, OP4);
  not not_372 (not_372_out, OP3);
  not not_373 (not_373_out, OP2);
  not not_374 (not_374_out, OP0);
  not not_375 (not_375_out, OP5);
  not not_376 (not_376_out, OP4);
  not not_377 (not_377_out, OP3);
  not not_378 (not_378_out, OP2);
  not not_379 (not_379_out, OP5);
  not not_380 (not_380_out, OP4);
  not not_381 (not_381_out, OP3);
  not not_382 (not_382_out, OP2);
  and and_1 (and_1_out, OP5, not_1_out, not_2_out, not_3_out, OP1, OP0);
  and and_2 (and_2_out, OP5, not_4_out, not_5_out, not_6_out, not_7_out, OP0);
  and and_3 (MemWrite, OP5, not_8_out, OP3, not_9_out, OP1, OP0);
  and and_4 (and_4_out, not_10_out, not_11_out, OP3, not_12_out, not_13_out, not_14_out);
  and and_5 (and_5_out, not_15_out, not_16_out, OP3, OP2, not_17_out, not_18_out);
  and and_6 (and_6_out, not_19_out, not_20_out, OP3, not_21_out, not_22_out, OP0);
  and and_7 (and_7_out, not_23_out, not_24_out, OP3, not_25_out, OP1, not_26_out);
  and and_8 (and_8_out, not_27_out, not_28_out, OP3, OP2, not_29_out, OP0);
  and and_9 (and_9_out, OP5, not_30_out, not_31_out, not_32_out, OP1, OP0);
  and and_10 (and_10_out, OP5, not_33_out, OP3, not_34_out, OP1, OP0);
  and and_11 (and_11_out, OP5, not_35_out, not_36_out, not_37_out, not_38_out, OP0);
  and and_12 (and_12_out, not_39_out, not_40_out, not_41_out, not_42_out, not_43_out, not_44_out, not_45_out, not_46_out, not_47_out, not_48_out, not_49_out, not_50_out);
  and and_13 (and_13_out, not_51_out, not_52_out, not_53_out, not_54_out, not_55_out, not_56_out, not_57_out, not_58_out, not_59_out, not_60_out, F1, F0);
  and and_14 (and_14_out, not_61_out, not_62_out, not_63_out, not_64_out, not_65_out, not_66_out, not_67_out, not_68_out, not_69_out, not_70_out, F1, not_71_out);
  and and_15 (and_15_out, not_72_out, not_73_out, not_74_out, not_75_out, not_76_out, not_77_out, F5, not_78_out, not_79_out, not_80_out, not_81_out, not_82_out);
  and and_16 (and_16_out, not_83_out, not_84_out, not_85_out, not_86_out, not_87_out, not_88_out, F5, not_89_out, not_90_out, not_91_out, not_92_out, F0);
  and and_17 (and_17_out, not_93_out, not_94_out, not_95_out, not_96_out, not_97_out, not_98_out, F5, not_99_out, not_100_out, not_101_out, F1, not_102_out);
  and and_18 (and_18_out, not_103_out, not_104_out, not_105_out, not_106_out, not_107_out, not_108_out, F5, not_109_out, not_110_out, F2, not_111_out, not_112_out);
  and and_19 (and_19_out, not_113_out, not_114_out, not_115_out, not_116_out, not_117_out, not_118_out, F5, not_119_out, not_120_out, F2, not_121_out, F0);
  and and_20 (and_20_out, not_122_out, not_123_out, not_124_out, not_125_out, not_126_out, not_127_out, F5, not_128_out, not_129_out, F2, F1, F0);
  and and_21 (and_21_out, not_130_out, not_131_out, not_132_out, not_133_out, not_134_out, not_135_out, F5, not_136_out, F3, not_137_out, F1, not_138_out);
  and and_22 (and_22_out, not_139_out, not_140_out, not_141_out, not_142_out, not_143_out, not_144_out, F5, not_145_out, F3, not_146_out, F1, F0);
  and and_23 (and_23_out, not_147_out, not_148_out, not_149_out, not_150_out, OP1, OP0);
  and and_24 (and_24_out, not_151_out, not_152_out, OP3, not_153_out, not_154_out, not_155_out);
  and and_25 (and_25_out, not_156_out, not_157_out, OP3, OP2, not_158_out, not_159_out);
  and and_26 (and_26_out, not_160_out, not_161_out, OP3, not_162_out, not_163_out, OP0);
  and and_27 (and_27_out, not_164_out, not_165_out, OP3, not_166_out, OP1, not_167_out);
  and and_28 (and_28_out, not_168_out, not_169_out, OP3, OP2, not_170_out, OP0);
  and and_29 (and_29_out, OP5, not_171_out, not_172_out, not_173_out, OP1, OP0);
  and and_30 (and_30_out, not_174_out, not_175_out, not_176_out, not_177_out, not_178_out, not_179_out, not_180_out, not_181_out, not_182_out, F2, F1, F0);
  and and_31 (and_31_out, not_183_out, not_184_out, not_185_out, not_186_out, not_187_out, not_188_out, F5, not_189_out, not_190_out, F2, F1, not_191_out);
  and and_32 (and_32_out, OP5, not_192_out, not_193_out, not_194_out, not_195_out, OP0);
  and and_33 (SysCALL, not_196_out, not_197_out, not_198_out, not_199_out, not_200_out, not_201_out, not_202_out, not_203_out, F3, F2, not_204_out, not_205_out);
  and and_34 (and_34_out, not_206_out, not_207_out, OP3, not_208_out, not_209_out, OP0);
  and and_35 (and_35_out, not_210_out, not_211_out, OP3, OP2, not_212_out, OP0);
  and and_36 (and_36_out, not_213_out, not_214_out, not_215_out, not_216_out, not_217_out, not_218_out, not_219_out, not_220_out, not_221_out, not_222_out, not_223_out, not_224_out);
  and and_37 (and_37_out, not_225_out, not_226_out, not_227_out, not_228_out, not_229_out, not_230_out, not_231_out, not_232_out, not_233_out, not_234_out, F1, F0);
  and and_38 (and_38_out, not_235_out, not_236_out, not_237_out, not_238_out, not_239_out, not_240_out, not_241_out, not_242_out, not_243_out, not_244_out, F1, not_245_out);
  and and_39 (and_39_out, not_246_out, not_247_out, not_248_out, not_249_out, not_250_out, not_251_out, F5, not_252_out, not_253_out, not_254_out, not_255_out, not_256_out);
  and and_40 (and_40_out, not_257_out, not_258_out, not_259_out, not_260_out, not_261_out, not_262_out, F5, not_263_out, not_264_out, not_265_out, not_266_out, F0);
  and and_41 (and_41_out, not_267_out, not_268_out, not_269_out, not_270_out, not_271_out, not_272_out, F5, not_273_out, not_274_out, not_275_out, F1, not_276_out);
  and and_42 (and_42_out, not_277_out, not_278_out, not_279_out, not_280_out, not_281_out, not_282_out, F5, not_283_out, not_284_out, F2, not_285_out, not_286_out);
  and and_43 (and_43_out, not_287_out, not_288_out, not_289_out, not_290_out, not_291_out, not_292_out, F5, not_293_out, not_294_out, F2, not_295_out, F0);
  and and_44 (and_44_out, not_296_out, not_297_out, not_298_out, not_299_out, not_300_out, not_301_out, F5, not_302_out, not_303_out, F2, F1, F0);
  and and_45 (and_45_out, not_304_out, not_305_out, not_306_out, not_307_out, not_308_out, not_309_out, F5, not_310_out, F3, not_311_out, F1, not_312_out);
  and and_46 (and_46_out, not_313_out, not_314_out, not_315_out, not_316_out, not_317_out, not_318_out, F5, not_319_out, F3, not_320_out, F1, F0);
  and and_47 (and_47_out, not_321_out, not_322_out, not_323_out, not_324_out, not_325_out, not_326_out, not_327_out, not_328_out, not_329_out, F2, F1, F0);
  and and_48 (and_48_out, not_330_out, not_331_out, not_332_out, not_333_out, not_334_out, not_335_out, F5, not_336_out, not_337_out, F2, F1, not_338_out);
  and and_49 (BEQ, not_339_out, not_340_out, not_341_out, OP2, not_342_out, not_343_out);
  and and_50 (BNE, not_344_out, not_345_out, not_346_out, OP2, not_347_out, OP0);
  and and_51 (JR, not_348_out, not_349_out, not_350_out, not_351_out, not_352_out, not_353_out, not_354_out, not_355_out, F3, not_356_out, not_357_out, not_358_out);
  and and_52 (and_52_out, not_359_out, not_360_out, not_361_out, not_362_out, not_363_out, not_364_out, not_365_out, not_366_out, F3, not_367_out, not_368_out, not_369_out);
  and and_53 (and_53_out, not_370_out, not_371_out, not_372_out, not_373_out, OP1, not_374_out);
  and and_54 (and_54_out, not_375_out, not_376_out, not_377_out, not_378_out, OP1, OP0);
  and and_55 (JAL, not_379_out, not_380_out, not_381_out, not_382_out, OP1, OP0);
  or or_1 (MemToReg, and_1_out, and_2_out);
  or or_2 (ALU_SRC, and_4_out, and_5_out, and_6_out, and_7_out, and_8_out, and_9_out, and_10_out, and_11_out);
  or or_3 (SignedExt, and_34_out, and_35_out);
  or or_4 (JMP, and_52_out, and_53_out, and_54_out);
  or or_5 (RegWrite, and_12_out, and_13_out, and_14_out, and_15_out, and_16_out, and_17_out, and_18_out, and_19_out, and_20_out, and_21_out, and_22_out, and_23_out, and_24_out, and_25_out, and_26_out, and_27_out, and_28_out, and_29_out, and_30_out, and_31_out, and_32_out);
  or or_6 (RegDst, and_36_out, and_37_out, and_38_out, and_39_out, and_40_out, and_41_out, and_42_out, and_43_out, and_44_out, and_45_out, and_46_out, and_47_out, and_48_out);
endmodule

// ALU
module MIPS_ALU (
  input  [4:0] shamt,
  input  [31:0] X,
  input  [31:0] Y,
  input  [3:0] AluOP,
  output Equal,
  output [31:0] Result,
  output [31:0] Result_2
);

  wire [0:0] comparator_1_lt, comparator_2_lt;
  wire [31:0] adder_1_out, AND_out, divider_1_out, divider_1_rem, multiplier_1_cout, multiplier_1_out,
       NOR_out, OR_out, shifter_1_out, shifter_2_out, shifter_3_out, subtractor_1_out, XOR_out;

  assign AND_out = X & Y;  // AND_Gate AND, 32 bits wide
  assign OR_out = X | Y;  // OR_Gate OR, 32 bits wide
  Shifter #(.width(32)) shifter_1 (.in(Y), .\dist (shamt), .out(shifter_1_out));
  Shifter #(.width(32), .shift("ar")) shifter_2 (.in(Y), .\dist (shamt), .out(shifter_2_out));
  Shifter #(.width(32), .shift("lr")) shifter_3 (.in(Y), .\dist (shamt), .out(shifter_3_out));
  Multiplier #(.width(32)) multiplier_1 (.a(X), .b(Y), .out(multiplier_1_out), .cout(multiplier_1_cout));  // open: cin
  Divider #(.width(32)) divider_1 (.a(X), .b(Y), .out(divider_1_out), .rem(divider_1_rem));  // open: upper
  Adder #(.width(32)) adder_1 (.a(X), .b(Y), .out(adder_1_out));  // open: cin, cout
  Subtractor #(.width(32)) subtractor_1 (.a(X), .b(Y), .out(subtractor_1_out));  // open: bin, bout
  assign XOR_out = X ^ Y;  // XOR_Gate XOR, 32 bits wide
  assign NOR_out = ~(X | Y);  // NOR_Gate NOR, 32 bits wide
  Comparator #(.width(32)) comparator_1 (.a(X), .b(Y), .eq(Equal), .lt(comparator_1_lt[0]));  // open: gt
  Comparator #(.width(32), .mode("unsigned")) comparator_2 (.a(X), .b(Y), .lt(comparator_2_lt[0]));  // open: gt, eq
  Multiplexer #(.select(4), .width(32), .enable("false")) multiplexer_1 (
    .in0(shifter_1_out), .in1(shifter_2_out), .in2(shifter_3_out), .in3(multiplier_1_out),
    .in4(divider_1_out), .in5(adder_1_out), .in6(subtractor_1_out), .in7(AND_out), .in8(OR_out),
    .in9(XOR_out), .in10(NOR_out), .in11({{31{1'b0}}, comparator_1_lt[0]}),
    .in12({{31{1'b0}}, comparator_2_lt[0]}), .in13({32{1'b0}}), .in14({32{1'b0}}), .in15({32{1'b0}}),
    .out(Result), .sel(AluOP));
  Multiplexer #(.select(4), .width(32), .enable("false")) multiplexer_2 (
    .in0({32{1'b0}}), .in1({32{1'b0}}), .in2({32{1'b0}}), .in3(multiplier_1_cout), .in4(divider_1_rem),
    .in5({32{1'b0}}), .in6({32{1'b0}}), .in7({32{1'b0}}), .in8({32{1'b0}}), .in9({32{1'b0}}),
    .in10({32{1'b0}}), .in11({32{1'b0}}), .in12({32{1'b0}}), .in13({32{1'b0}}), .in14({32{1'b0}}),
    .in15({32{1'b0}}), .out(Result_2), .sel(AluOP));

  // Other names for the same wires on the sheet: Result2[31:0] = Result_2; S[3:0] = AluOP

  // Notes on the sheet:
  //   不要改变此引脚区域内容，也不要改变ALU封装形式
  //   输入引脚
  //   输出引脚
endmodule

module MIPS_Regifile (
  input  [31:0] Din,
  input  Clk,
  input  WE,
  input  [4:0] R1_num,
  input  [4:0] W_num,
  input  [4:0] R2_num,
  output [31:0] R1,
  output [31:0] R2
);

  // RegisterFile registerfile_1: pin names not known; wires that end beside it: Din, Clk, WE, W_num, R1_num, R2_num, R1, R2
endmodule

module \理想流水线  (
);

  wire and_1_out, and_2_out, and_3_out, CLK, comparator_1_eq, EQUL, \ex_mem_1_传输状态out_表明当前传输数据有效 , Go,
       \id_ex_1_传输状态out_表明当前传输数据有效 , \if_id_1_传输状态out_表明当前传输数据有效 , IR1, IR2, IR3, JMP, JR, not_1_out,
       not_2_out, or_1_out, RST, sel, SignedExt, sys, W1, W2, W3, WE;
  wire [2:0] MEM;
  wire [3:0] mem_wb_1_wb_2;
  wire [4:0] EX, ex_mem_1_mem_2, ex_mem_1_wb_2, id_ex_1_ex_2, id_ex_1_mem_2, id_ex_1_wb_2, multiplexer_1_out,
       multiplexer_3_out, multiplexer_4_out, multiplexer_7_out, shamt, WB, WR;
  wire [11:0] EX_PC, ID_PC, IF_PC, MEM_PC, WB_PC;
  wire [15:0] \LoadUse次数 , \总周期数 , \插入气泡数 , \无条件分支数 , \条件分支成功数 ;
  wire [31:0] adder_1_out, bit_extender_1_out, bit_extender_2_out, ex_mem_1_a_2, ex_mem_1_alu_2,
       ex_mem_1_b_2, ex_mem_1_ir_2, ex_mem_1_pc_2, id_ex_1_a_2, id_ex_1_b_2, id_ex_1_ir_2, id_ex_1_pc_2,
       id_ex_1_shmat_2, if_id_1_ir_2, if_id_1_pc_2, im, LedData, mem_wb_1_alu_2, mem_wb_1_ir_2,
       mem_wb_1_md_2, mips_alu_1_result, mips_regifile_1_r1, mips_regifile_1_r2, multiplexer_5_out, PC_q, R1,
       R2, ram_1_data, RD, rom_1_data;

  Button \u_总复位  (.out(RST));
  Button _1 (.out(IR1));
  Button _2 (.out(IR2));
  Button _3 (.out(IR3));
  Button \u_继续运行  (.out(Go));
  LED led_1 (.in(W1));
  LED led_2 (.in(W2));
  LED led_3 (.in(W3));
  Hex_Digit_Display hex_digit_display_1 (.value(LedData[31:28]));  // open: dp
  Hex_Digit_Display hex_digit_display_2 (.value(LedData[23:20]));  // open: dp
  Hex_Digit_Display hex_digit_display_3 (.value(LedData[27:24]));  // open: dp
  Register #(.width(32)) PC (.D(adder_1_out), .en(sel), .Q(PC_q), .clk(CLK), .clr(RST));
  Hex_Digit_Display hex_digit_display_4 (.value(LedData[15:12]));  // open: dp
  Hex_Digit_Display hex_digit_display_5 (.value(LedData[19:16]));  // open: dp
  Hex_Digit_Display hex_digit_display_6 (.value(LedData[11:8]));  // open: dp
  Hex_Digit_Display hex_digit_display_7 (.value(LedData[7:4]));  // open: dp
  Clock clock_1 (.out(CLK));
  Adder #(.width(32)) adder_1 (.a(PC_q), .b(32'h4), .out(adder_1_out));  // open: cin, cout
  Hex_Digit_Display hex_digit_display_8 (.value(LedData[3:0]));  // open: dp
  ROM #(.addrWidth(10), .dataWidth(32)) rom_1 (.addr(PC_q[11:2]), .data(rom_1_data));  // open: sel
  IF_ID if_id_1 (
    .IR(rom_1_data), .PC(PC_q), .\传输状态In_表明当前传输数据有效 (1'b1), .CLK(CLK), .IR_2(if_id_1_ir_2),
    .PC_2(if_id_1_pc_2), .\传输状态Out_表明当前传输数据有效 (\if_id_1_传输状态out_表明当前传输数据有效 ));  // open: 同步清零_气泡_高电平有效, 使能端_低电平有效_stall_高电平有效, miss, miss_2, dataout, dataout_2
  // Probe on \总周期数 
  // Probe on \无条件分支数 
  // Probe on \条件分支成功数 
  // Probe on \插入气泡数 
  // Probe on \LoadUse次数 
  assign bit_extender_1_out = {{16{if_id_1_ir_2[15]}}, if_id_1_ir_2[15:0]};  // Bit_Extender bit_extender_1
  assign bit_extender_2_out = {{16{1'b0}}, if_id_1_ir_2[15:0]};  // Bit_Extender bit_extender_2
  // Probe on IF_PC
  Multiplexer #(.width(5), .enable("false")) multiplexer_1 (
    .in0(if_id_1_ir_2[25:21]), .in1({5{1'b1}}), .out(multiplexer_1_out), .sel(JR));
  \分支相关流水线  \u_分支相关流水线_1  ();
  Multiplexer #(.width(32), .enable("false")) multiplexer_2 (
    .in0(bit_extender_1_out), .in1(bit_extender_2_out), .out(im), .sel(SignedExt));
  // Probe on ID_PC
  \硬布线控制器  \u_硬布线控制器_1  (
    .Func(if_id_1_ir_2[5:0]), .OP(if_id_1_ir_2[31:26]), .ALU_OP(EX[3:0]), .MemToReg(WB[0]),
    .MemWrite(MEM[2]), .ALU_SRC(EX[4]), .RegWrite(WB[1]), .SysCALL(WB[4]), .SignedExt(SignedExt),
    .RegDst(WB[3]), .JR(JR), .JMP(JMP), .Beq(MEM[0]), .JAL(WB[2]), .Bne(MEM[1]));
  Multiplexer #(.width(5), .enable("false")) multiplexer_3 (
    .in0(multiplexer_1_out), .in1(5'b00010), .out(multiplexer_3_out), .sel(WB[4]));
  Multiplexer #(.width(5), .enable("false")) multiplexer_4 (
    .in0(if_id_1_ir_2[20:16]), .in1(5'b00100), .out(multiplexer_4_out), .sel(WB[4]));
  // Probe on MEM_PC
  // Probe on EX_PC
  // Probe on WB_PC
  MIPS_Regifile mips_regifile_1 (
    .Din(RD), .Clk(CLK), .R1(mips_regifile_1_r1), .R2(mips_regifile_1_r2), .WE(WE), .W_num(WR),
    .R1_num(multiplexer_3_out), .R2_num(multiplexer_4_out));
  ID_EX id_ex_1 (
    .WB(WB), .MEM({JR, JMP, MEM}), .EX(EX), .IR(if_id_1_ir_2), .PC(if_id_1_pc_2), .A(mips_regifile_1_r1),
    .B(mips_regifile_1_r2), .SHMAT(im), .\传输状态In_表明当前传输数据有效 (\if_id_1_传输状态out_表明当前传输数据有效 ), .CLK(CLK),
    .WB_2(id_ex_1_wb_2), .MEM_2(id_ex_1_mem_2), .EX_2(id_ex_1_ex_2),
    .IR_2({id_ex_1_ir_2[31:11], shamt, id_ex_1_ir_2[5:0]}), .PC_2(id_ex_1_pc_2), .A_2(id_ex_1_a_2),
    .B_2(id_ex_1_b_2), .SHMAT_2(id_ex_1_shmat_2), .\传输状态Out_表明当前传输数据有效 (\id_ex_1_传输状态out_表明当前传输数据有效 ));  // open: 同步清零_气泡_高电平有效, 使能端_低电平有效_stall_高电平有效, R1, R1_2, R2, R2_2, miss, miss_2, dataout, dataout_2
  Multiplexer #(.width(32), .enable("false")) multiplexer_5 (
    .in0(id_ex_1_b_2), .in1(id_ex_1_shmat_2), .out(multiplexer_5_out), .sel(id_ex_1_ex_2[4]));
  not not_1 (not_1_out, EQUL);
  MIPS_ALU mips_alu_1 (
    .X(id_ex_1_a_2), .Y(multiplexer_5_out), .AluOP(id_ex_1_ex_2[3:0]), .Equal(EQUL),
    .Result(mips_alu_1_result), .shamt(shamt));  // open: Result_2
  and and_1 (and_1_out, id_ex_1_mem_2[0], EQUL);
  and and_2 (and_2_out, id_ex_1_mem_2[1], not_1_out);
  or or_1 (or_1_out, and_1_out, and_2_out);
  EX_MEM ex_mem_1 (
    .WB(id_ex_1_wb_2), .MEM(id_ex_1_mem_2), .IR({id_ex_1_ir_2[31:11], shamt, id_ex_1_ir_2[5:0]}),
    .PC(id_ex_1_pc_2), .B(id_ex_1_b_2), .ALU(mips_alu_1_result),
    .\传输状态In_表明当前传输数据有效 (\id_ex_1_传输状态out_表明当前传输数据有效 ), .CLK(CLK), .WB_2(ex_mem_1_wb_2),
    .MEM_2(ex_mem_1_mem_2), .IR_2(ex_mem_1_ir_2), .PC_2(ex_mem_1_pc_2), .B_2(ex_mem_1_b_2),
    .ALU_2(ex_mem_1_alu_2), .\传输状态Out_表明当前传输数据有效 (\ex_mem_1_传输状态out_表明当前传输数据有效 ), .A(id_ex_1_a_2),
    .A_2(ex_mem_1_a_2));  // open: 同步清零_气泡_高电平有效, 使能端_低电平有效_stall_高电平有效
  Comparator #(.width(32)) comparator_1 (.a(R1), .b(32'h32), .eq(comparator_1_eq));  // open: gt, lt
  and and_3 (and_3_out, comparator_1_eq, sys);
  not not_2 (not_2_out, and_3_out);
  RAM #(.addrWidth(10), .dataWidth(32), .bus("separate")) ram_1 (
    .addr(ex_mem_1_alu_2[11:2]), .din(ex_mem_1_b_2), .data(ram_1_data), .str(ex_mem_1_mem_2[2]), .sel(sel),
    .clk(CLK), .clr(RST));  // open: ld
  or or_2 (sel, Go, not_2_out);
  MEM_WB mem_wb_1 (
    .WB(ex_mem_1_wb_2), .IR(ex_mem_1_ir_2), .PC(ex_mem_1_pc_2), .ALU(ex_mem_1_alu_2), .MD(ram_1_data),
    .\传输状态In_表明当前传输数据有效 (\ex_mem_1_传输状态out_表明当前传输数据有效 ), .CLK(CLK),
    .WB_2({sys, mem_wb_1_wb_2[3:2], WE, mem_wb_1_wb_2[0]}), .IR_2(mem_wb_1_ir_2), .ALU_2(mem_wb_1_alu_2),
    .MD_2(mem_wb_1_md_2), .A(ex_mem_1_a_2), .A_2(R1), .B(ex_mem_1_b_2), .B_2(R2));  // open: PC_2, 传输状态Out_表明当前传输数据有效, 同步清零_气泡_高电平有效, 使能端_低电平有效_stall_高电平有效
  Multiplexer #(.width(32)) multiplexer_6 (
    .in0(mem_wb_1_alu_2), .in1(mem_wb_1_md_2), .out(RD), .sel(mem_wb_1_wb_2[0]));  // open: en
  Multiplexer #(.width(5), .enable("false")) multiplexer_7 (
    .in0(mem_wb_1_ir_2[20:16]), .in1(mem_wb_1_ir_2[15:11]), .out(multiplexer_7_out), .sel(mem_wb_1_wb_2[3]));
  Multiplexer #(.width(5), .enable("false")) multiplexer_8 (
    .in0(multiplexer_7_out), .out(WR), .sel(mem_wb_1_wb_2[2]));  // open: in1

  // Other names for the same wires on the sheet: MEM[4:3] = {JR, JMP}

  // Notes on the sheet:
  //   中断源
  //   中断等待指示
  //   数码管输出
  //   contents of rom_1 (hex, n*v repeats v):
  //   20100000 20110000 20120000 20130000 36100000 36310001 36520002 36730003 ae100000 ae110004 ae120008
  //   ae13000c 2002000a 20110000 20120000 20130000 c
  //   指令字
  //   JMP
  //   JR
  //   OP
  //   OP
  //   Func
  //   Func
  //   rs
  //   rt
  //   rd
  //   Bne
  //   MemToReg
  //   MemWrite
  //   AluOP
  //   AluSrcB
  //   RegWrite
  //   JAL
  //   RegDst
  //   流水调试日志用
  //   rt
  //   rd
endmodule

// 源寄存器使用情况
module \源寄存器使用情况  (
  input  OP0,
  input  OP1,
  input  OP2,
  input  OP3,
  input  OP4,
  input  OP5,
  input  F0,
  input  F1,
  input  F2,
  input  F3,
  input  F4,
  input  F5,
  output R1_Used,
  output R2_Used
);

  wire and_1_out, and_2_out, and_3_out, and_4_out, and_5_out, and_6_out, and_7_out, and_8_out, and_9_out,
       and_10_out, and_11_out, and_12_out, and_13_out, and_14_out, and_15_out, and_16_out, and_17_out,
       and_18_out, and_19_out, and_20_out, and_21_out, and_22_out, and_23_out, and_24_out, and_25_out,
       and_26_out, and_27_out, and_28_out, and_29_out, and_30_out, and_31_out, and_32_out, and_33_out,
       and_34_out, and_35_out, and_36_out, and_37_out, and_38_out, and_39_out, not_1_out, not_2_out,
       not_3_out, not_4_out, not_5_out, not_6_out, not_7_out, not_8_out, not_9_out, not_10_out, not_11_out,
       not_12_out, not_13_out, not_14_out, not_15_out, not_16_out, not_17_out, not_18_out, not_19_out,
       not_20_out, not_21_out, not_22_out, not_23_out, not_24_out, not_25_out, not_26_out, not_27_out,
       not_28_out, not_29_out, not_30_out, not_31_out, not_32_out, not_33_out, not_34_out, not_35_out,
       not_36_out, not_37_out, not_38_out, not_39_out, not_40_out, not_41_out, not_42_out, not_43_out,
       not_44_out, not_45_out, not_46_out, not_47_out, not_48_out, not_49_out, not_50_out, not_51_out,
       not_52_out, not_53_out, not_54_out, not_55_out, not_56_out, not_57_out, not_58_out, not_59_out,
       not_60_out, not_61_out, not_62_out, not_63_out, not_64_out, not_65_out, not_66_out, not_67_out,
       not_68_out, not_69_out, not_70_out, not_71_out, not_72_out, not_73_out, not_74_out, not_75_out,
       not_76_out, not_77_out, not_78_out, not_79_out, not_80_out, not_81_out, not_82_out, not_83_out,
       not_84_out, not_85_out, not_86_out, not_87_out, not_88_out, not_89_out, not_90_out, not_91_out,
       not_92_out, not_93_out, not_94_out, not_95_out, not_96_out, not_97_out, not_98_out, not_99_out,
       not_100_out, not_101_out, not_102_out, not_103_out, not_104_out, not_105_out, not_106_out,
       not_107_out, not_108_out, not_109_out, not_110_out, not_111_out, not_112_out, not_113_out,
       not_114_out, not_115_out, not_116_out, not_117_out, not_118_out, not_119_out, not_120_out,
       not_121_out, not_122_out, not_123_out, not_124_out, not_125_out, not_126_out, not_127_out,
       not_128_out, not_129_out, not_130_out, not_131_out, not_132_out, not_133_out, not_134_out,
       not_135_out, not_136_out, not_137_out, not_138_out, not_139_out, not_140_out, not_141_out,
       not_142_out, not_143_out, not_144_out, not_145_out, not_146_out, not_147_out, not_148_out,
       not_149_out, not_150_out, not_151_out, not_152_out, not_153_out, not_154_out, not_155_out,
       not_156_out, not_157_out, not_158_out, not_159_out, not_160_out, not_161_out, not_162_out,
       not_163_out, not_164_out, not_165_out, not_166_out, not_167_out, not_168_out, not_169_out,
       not_170_out, not_171_out, not_172_out, not_173_out, not_174_out, not_175_out, not_176_out,
       not_177_out, not_178_out, not_179_out, not_180_out, not_181_out, not_182_out, not_183_out,
       not_184_out, not_185_out, not_186_out, not_187_out, not_188_out, not_189_out, not_190_out,
       not_191_out, not_192_out, not_193_out, not_194_out, not_195_out, not_196_out, not_197_out,
       not_198_out, not_199_out, not_200_out, not_201_out, not_202_out, not_203_out, not_204_out,
       not_205_out, not_206_out, not_207_out, not_208_out, not_209_out, not_210_out, not_211_out,
       not_212_out, not_213_out, not_214_out, not_215_out, not_216_out, not_217_out, not_218_out,
       not_219_out, not_220_out, not_221_out, not_222_out, not_223_out, not_224_out, not_225_out,
       not_226_out, not_227_out, not_228_out, not_229_out, not_230_out, not_231_out, not_232_out,
       not_233_out, not_234_out, not_235_out, not_236_out, not_237_out, not_238_out, not_239_out,
       not_240_out, not_241_out, not_242_out, not_243_out, not_244_out, not_245_out, not_246_out,
       not_247_out, not_248_out, not_249_out, not_250_out, not_251_out, not_252_out, not_253_out,
       not_254_out, not_255_out, not_256_out, not_257_out, not_258_out, not_259_out, not_260_out,
       not_261_out, not_262_out, not_263_out, not_264_out, not_265_out, not_266_out, not_267_out,
       not_268_out, not_269_out, not_270_out, not_271_out, not_272_out, not_273_out, not_274_out,
       not_275_out, not_276_out, not_277_out, not_278_out, not_279_out, not_280_out, not_281_out,
       not_282_out, not_283_out, not_284_out, not_285_out, not_286_out, not_287_out, not_288_out,
       not_289_out, not_290_out, not_291_out, not_292_out, not_293_out, not_294_out, not_295_out, not_296_out;

  not not_1 (not_1_out, OP5);
  not not_2 (not_2_out, OP4);
  not not_3 (not_3_out, OP3);
  not not_4 (not_4_out, OP2);
  not not_5 (not_5_out, OP1);
  not not_6 (not_6_out, OP0);
  not not_7 (not_7_out, F4);
  not not_8 (not_8_out, F3);
  not not_9 (not_9_out, F2);
  not not_10 (not_10_out, F1);
  not not_11 (not_11_out, F0);
  not not_12 (not_12_out, OP5);
  not not_13 (not_13_out, OP4);
  not not_14 (not_14_out, OP3);
  not not_15 (not_15_out, OP2);
  not not_16 (not_16_out, OP1);
  not not_17 (not_17_out, OP0);
  not not_18 (not_18_out, F4);
  not not_19 (not_19_out, F3);
  not not_20 (not_20_out, F2);
  not not_21 (not_21_out, F1);
  not not_22 (not_22_out, OP5);
  not not_23 (not_23_out, OP4);
  not not_24 (not_24_out, OP3);
  not not_25 (not_25_out, OP2);
  not not_26 (not_26_out, OP1);
  not not_27 (not_27_out, OP0);
  not not_28 (not_28_out, F4);
  not not_29 (not_29_out, F3);
  not not_30 (not_30_out, F2);
  not not_31 (not_31_out, F0);
  not not_32 (not_32_out, OP5);
  not not_33 (not_33_out, OP4);
  not not_34 (not_34_out, OP3);
  not not_35 (not_35_out, OP2);
  not not_36 (not_36_out, OP1);
  not not_37 (not_37_out, OP0);
  not not_38 (not_38_out, F4);
  not not_39 (not_39_out, F3);
  not not_40 (not_40_out, F1);
  not not_41 (not_41_out, F0);
  not not_42 (not_42_out, OP5);
  not not_43 (not_43_out, OP4);
  not not_44 (not_44_out, OP3);
  not not_45 (not_45_out, OP2);
  not not_46 (not_46_out, OP1);
  not not_47 (not_47_out, OP0);
  not not_48 (not_48_out, F4);
  not not_49 (not_49_out, F3);
  not not_50 (not_50_out, F1);
  not not_51 (not_51_out, OP5);
  not not_52 (not_52_out, OP4);
  not not_53 (not_53_out, OP3);
  not not_54 (not_54_out, OP2);
  not not_55 (not_55_out, OP1);
  not not_56 (not_56_out, OP0);
  not not_57 (not_57_out, F4);
  not not_58 (not_58_out, F3);
  not not_59 (not_59_out, OP5);
  not not_60 (not_60_out, OP4);
  not not_61 (not_61_out, OP3);
  not not_62 (not_62_out, OP2);
  not not_63 (not_63_out, OP1);
  not not_64 (not_64_out, OP0);
  not not_65 (not_65_out, F4);
  not not_66 (not_66_out, F2);
  not not_67 (not_67_out, F0);
  not not_68 (not_68_out, OP5);
  not not_69 (not_69_out, OP4);
  not not_70 (not_70_out, OP3);
  not not_71 (not_71_out, OP2);
  not not_72 (not_72_out, OP1);
  not not_73 (not_73_out, OP0);
  not not_74 (not_74_out, F4);
  not not_75 (not_75_out, F2);
  not not_76 (not_76_out, OP5);
  not not_77 (not_77_out, OP4);
  not not_78 (not_78_out, OP3);
  not not_79 (not_79_out, OP2);
  not not_80 (not_80_out, OP1);
  not not_81 (not_81_out, OP0);
  not not_82 (not_82_out, F5);
  not not_83 (not_83_out, F4);
  not not_84 (not_84_out, F2);
  not not_85 (not_85_out, F1);
  not not_86 (not_86_out, F0);
  not not_87 (not_87_out, OP5);
  not not_88 (not_88_out, OP4);
  not not_89 (not_89_out, OP3);
  not not_90 (not_90_out, OP2);
  not not_91 (not_91_out, OP1);
  not not_92 (not_92_out, OP0);
  not not_93 (not_93_out, F5);
  not not_94 (not_94_out, F4);
  not not_95 (not_95_out, F1);
  not not_96 (not_96_out, F0);
  not not_97 (not_97_out, OP5);
  not not_98 (not_98_out, OP4);
  not not_99 (not_99_out, OP3);
  not not_100 (not_100_out, OP1);
  not not_101 (not_101_out, OP0);
  not not_102 (not_102_out, OP5);
  not not_103 (not_103_out, OP4);
  not not_104 (not_104_out, OP3);
  not not_105 (not_105_out, OP1);
  not not_106 (not_106_out, OP5);
  not not_107 (not_107_out, OP4);
  not not_108 (not_108_out, OP2);
  not not_109 (not_109_out, OP1);
  not not_110 (not_110_out, OP0);
  not not_111 (not_111_out, OP5);
  not not_112 (not_112_out, OP4);
  not not_113 (not_113_out, OP1);
  not not_114 (not_114_out, OP0);
  not not_115 (not_115_out, OP5);
  not not_116 (not_116_out, OP4);
  not not_117 (not_117_out, OP2);
  not not_118 (not_118_out, OP1);
  not not_119 (not_119_out, OP5);
  not not_120 (not_120_out, OP4);
  not not_121 (not_121_out, OP2);
  not not_122 (not_122_out, OP0);
  not not_123 (not_123_out, OP5);
  not not_124 (not_124_out, OP4);
  not not_125 (not_125_out, OP1);
  not not_126 (not_126_out, OP4);
  not not_127 (not_127_out, OP3);
  not not_128 (not_128_out, OP2);
  not not_129 (not_129_out, OP4);
  not not_130 (not_130_out, OP2);
  not not_131 (not_131_out, OP5);
  not not_132 (not_132_out, OP4);
  not not_133 (not_133_out, OP3);
  not not_134 (not_134_out, OP2);
  not not_135 (not_135_out, OP1);
  not not_136 (not_136_out, OP0);
  not not_137 (not_137_out, F5);
  not not_138 (not_138_out, F4);
  not not_139 (not_139_out, F3);
  not not_140 (not_140_out, OP5);
  not not_141 (not_141_out, OP4);
  not not_142 (not_142_out, OP3);
  not not_143 (not_143_out, OP2);
  not not_144 (not_144_out, OP1);
  not not_145 (not_145_out, OP0);
  not not_146 (not_146_out, F4);
  not not_147 (not_147_out, F3);
  not not_148 (not_148_out, F0);
  not not_149 (not_149_out, OP4);
  not not_150 (not_150_out, OP3);
  not not_151 (not_151_out, OP2);
  not not_152 (not_152_out, OP1);
  not not_153 (not_153_out, OP5);
  not not_154 (not_154_out, OP4);
  not not_155 (not_155_out, OP3);
  not not_156 (not_156_out, OP2);
  not not_157 (not_157_out, OP1);
  not not_158 (not_158_out, OP5);
  not not_159 (not_159_out, OP4);
  not not_160 (not_160_out, OP3);
  not not_161 (not_161_out, OP2);
  not not_162 (not_162_out, OP1);
  not not_163 (not_163_out, OP0);
  not not_164 (not_164_out, F5);
  not not_165 (not_165_out, F4);
  not not_166 (not_166_out, F3);
  not not_167 (not_167_out, F2);
  not not_168 (not_168_out, F1);
  not not_169 (not_169_out, F0);
  not not_170 (not_170_out, OP5);
  not not_171 (not_171_out, OP4);
  not not_172 (not_172_out, OP3);
  not not_173 (not_173_out, OP2);
  not not_174 (not_174_out, OP1);
  not not_175 (not_175_out, OP0);
  not not_176 (not_176_out, F5);
  not not_177 (not_177_out, F4);
  not not_178 (not_178_out, F3);
  not not_179 (not_179_out, F2);
  not not_180 (not_180_out, OP5);
  not not_181 (not_181_out, OP4);
  not not_182 (not_182_out, OP3);
  not not_183 (not_183_out, OP2);
  not not_184 (not_184_out, OP1);
  not not_185 (not_185_out, OP0);
  not not_186 (not_186_out, F5);
  not not_187 (not_187_out, F4);
  not not_188 (not_188_out, F3);
  not not_189 (not_189_out, F2);
  not not_190 (not_190_out, F0);
  not not_191 (not_191_out, OP5);
  not not_192 (not_192_out, OP4);
  not not_193 (not_193_out, OP3);
  not not_194 (not_194_out, OP2);
  not not_195 (not_195_out, OP1);
  not not_196 (not_196_out, OP0);
  not not_197 (not_197_out, F4);
  not not_198 (not_198_out, F3);
  not not_199 (not_199_out, F2);
  not not_200 (not_200_out, F1);
  not not_201 (not_201_out, F0);
  not not_202 (not_202_out, OP5);
  not not_203 (not_203_out, OP4);
  not not_204 (not_204_out, OP3);
  not not_205 (not_205_out, OP2);
  not not_206 (not_206_out, OP1);
  not not_207 (not_207_out, OP0);
  not not_208 (not_208_out, F4);
  not not_209 (not_209_out, F3);
  not not_210 (not_210_out, F2);
  not not_211 (not_211_out, F1);
  not not_212 (not_212_out, OP5);
  not not_213 (not_213_out, OP4);
  not not_214 (not_214_out, OP3);
  not not_215 (not_215_out, OP2);
  not not_216 (not_216_out, OP1);
  not not_217 (not_217_out, OP0);
  not not_218 (not_218_out, F4);
  not not_219 (not_219_out, F3);
  not not_220 (not_220_out, F2);
  not not_221 (not_221_out, F0);
  not not_222 (not_222_out, OP5);
  not not_223 (not_223_out, OP4);
  not not_224 (not_224_out, OP3);
  not not_225 (not_225_out, OP2);
  not not_226 (not_226_out, OP1);
  not not_227 (not_227_out, OP0);
  not not_228 (not_228_out, F4);
  not not_229 (not_229_out, F3);
  not not_230 (not_230_out, F1);
  not not_231 (not_231_out, F0);
  not not_232 (not_232_out, OP5);
  not not_233 (not_233_out, OP4);
  not not_234 (not_234_out, OP3);
  not not_235 (not_235_out, OP2);
  not not_236 (not_236_out, OP1);
  not not_237 (not_237_out, OP0);
  not not_238 (not_238_out, F4);
  not not_239 (not_239_out, F3);
  not not_240 (not_240_out, F1);
  not not_241 (not_241_out, OP5);
  not not_242 (not_242_out, OP4);
  not not_243 (not_243_out, OP3);
  not not_244 (not_244_out, OP2);
  not not_245 (not_245_out, OP1);
  not not_246 (not_246_out, OP0);
  not not_247 (not_247_out, F4);
  not not_248 (not_248_out, F3);
  not not_249 (not_249_out, OP5);
  not not_250 (not_250_out, OP4);
  not not_251 (not_251_out, OP3);
  not not_252 (not_252_out, OP2);
  not not_253 (not_253_out, OP1);
  not not_254 (not_254_out, OP0);
  not not_255 (not_255_out, F4);
  not not_256 (not_256_out, F2);
  not not_257 (not_257_out, F0);
  not not_258 (not_258_out, OP5);
  not not_259 (not_259_out, OP4);
  not not_260 (not_260_out, OP3);
  not not_261 (not_261_out, OP2);
  not not_262 (not_262_out, OP1);
  not not_263 (not_263_out, OP0);
  not not_264 (not_264_out, F5);
  not not_265 (not_265_out, F4);
  not not_266 (not_266_out, F1);
  not not_267 (not_267_out, F0);
  not not_268 (not_268_out, OP5);
  not not_269 (not_269_out, OP4);
  not not_270 (not_270_out, OP3);
  not not_271 (not_271_out, OP1);
  not not_272 (not_272_out, OP0);
  not not_273 (not_273_out, OP5);
  not not_274 (not_274_out, OP4);
  not not_275 (not_275_out, OP3);
  not not_276 (not_276_out, OP1);
  not not_277 (not_277_out, OP4);
  not not_278 (not_278_out, OP2);
  not not_279 (not_279_out, OP5);
  not not_280 (not_280_out, OP4);
  not not_281 (not_281_out, OP3);
  not not_282 (not_282_out, OP2);
  not not_283 (not_283_out, OP1);
  not not_284 (not_284_out, OP0);
  not not_285 (not_285_out, F5);
  not not_286 (not_286_out, F4);
  not not_287 (not_287_out, F3);
  not not_288 (not_288_out, OP5);
  not not_289 (not_289_out, OP4);
  not not_290 (not_290_out, OP3);
  not not_291 (not_291_out, OP2);
  not not_292 (not_292_out, OP1);
  not not_293 (not_293_out, OP0);
  not not_294 (not_294_out, F4);
  not not_295 (not_295_out, F3);
  not not_296 (not_296_out, F0);
  and and_1 (and_1_out, not_1_out, not_2_out, not_3_out, not_4_out, not_5_out, not_6_out, F5, not_7_out, not_8_out, not_9_out, not_10_out, not_11_out);
  and and_2 (and_2_out, not_12_out, not_13_out, not_14_out, not_15_out, not_16_out, not_17_out, F5, not_18_out, not_19_out, not_20_out, not_21_out, F0);
  and and_3 (and_3_out, not_22_out, not_23_out, not_24_out, not_25_out, not_26_out, not_27_out, F5, not_28_out, not_29_out, not_30_out, F1, not_31_out);
  and and_4 (and_4_out, not_32_out, not_33_out, not_34_out, not_35_out, not_36_out, not_37_out, F5, not_38_out, not_39_out, F2, not_40_out, not_41_out);
  and and_5 (and_5_out, not_42_out, not_43_out, not_44_out, not_45_out, not_46_out, not_47_out, F5, not_48_out, not_49_out, F2, not_50_out, F0);
  and and_6 (and_6_out, not_51_out, not_52_out, not_53_out, not_54_out, not_55_out, not_56_out, F5, not_57_out, not_58_out, F2, F1, F0);
  and and_7 (and_7_out, not_59_out, not_60_out, not_61_out, not_62_out, not_63_out, not_64_out, F5, not_65_out, F3, not_66_out, F1, not_67_out);
  and and_8 (and_8_out, not_68_out, not_69_out, not_70_out, not_71_out, not_72_out, not_73_out, F5, not_74_out, F3, not_75_out, F1, F0);
  and and_9 (and_9_out, not_76_out, not_77_out, not_78_out, not_79_out, not_80_out, not_81_out, not_82_out, not_83_out, F3, not_84_out, not_85_out, not_86_out);
  and and_10 (and_10_out, not_87_out, not_88_out, not_89_out, not_90_out, not_91_out, not_92_out, not_93_out, not_94_out, F3, F2, not_95_out, not_96_out);
  and and_11 (and_11_out, not_97_out, not_98_out, not_99_out, OP2, not_100_out, not_101_out);
  and and_12 (and_12_out, not_102_out, not_103_out, not_104_out, OP2, not_105_out, OP0);
  and and_13 (and_13_out, not_106_out, not_107_out, OP3, not_108_out, not_109_out, not_110_out);
  and and_14 (and_14_out, not_111_out, not_112_out, OP3, OP2, not_113_out, not_114_out);
  and and_15 (and_15_out, not_115_out, not_116_out, OP3, not_117_out, not_118_out, OP0);
  and and_16 (and_16_out, not_119_out, not_120_out, OP3, not_121_out, OP1, not_122_out);
  and and_17 (and_17_out, not_123_out, not_124_out, OP3, OP2, not_125_out, OP0);
  and and_18 (and_18_out, OP5, not_126_out, not_127_out, not_128_out, OP1, OP0);
  and and_19 (and_19_out, OP5, not_129_out, OP3, not_130_out, OP1, OP0);
  and and_20 (and_20_out, not_131_out, not_132_out, not_133_out, not_134_out, not_135_out, not_136_out, not_137_out, not_138_out, not_139_out, F2, F1, F0);
  and and_21 (and_21_out, not_140_out, not_141_out, not_142_out, not_143_out, not_144_out, not_145_out, F5, not_146_out, not_147_out, F2, F1, not_148_out);
  and and_22 (and_22_out, OP5, not_149_out, not_150_out, not_151_out, not_152_out, OP0);
  and and_23 (and_23_out, not_153_out, not_154_out, not_155_out, not_156_out, not_157_out, OP0);
  and and_24 (and_24_out, not_158_out, not_159_out, not_160_out, not_161_out, not_162_out, not_163_out, not_164_out, not_165_out, not_166_out, not_167_out, not_168_out, not_169_out);
  and and_25 (and_25_out, not_170_out, not_171_out, not_172_out, not_173_out, not_174_out, not_175_out, not_176_out, not_177_out, not_178_out, not_179_out, F1, F0);
  and and_26 (and_26_out, not_180_out, not_181_out, not_182_out, not_183_out, not_184_out, not_185_out, not_186_out, not_187_out, not_188_out, not_189_out, F1, not_190_out);
  and and_27 (and_27_out, not_191_out, not_192_out, not_193_out, not_194_out, not_195_out, not_196_out, F5, not_197_out, not_198_out, not_199_out, not_200_out, not_201_out);
  and and_28 (and_28_out, not_202_out, not_203_out, not_204_out, not_205_out, not_206_out, not_207_out, F5, not_208_out, not_209_out, not_210_out, not_211_out, F0);
  and and_29 (and_29_out, not_212_out, not_213_out, not_214_out, not_215_out, not_216_out, not_217_out, F5, not_218_out, not_219_out, not_220_out, F1, not_221_out);
  and and_30 (and_30_out, not_222_out, not_223_out, not_224_out, not_225_out, not_226_out, not_227_out, F5, not_228_out, not_229_out, F2, not_230_out, not_231_out);
  and and_31 (and_31_out, not_232_out, not_233_out, not_234_out, not_235_out, not_236_out, not_237_out, F5, not_238_out, not_239_out, F2, not_240_out, F0);
  and and_32 (and_32_out, not_241_out, not_242_out, not_243_out, not_244_out, not_245_out, not_246_out, F5, not_247_out, not_248_out, F2, F1, F0);
  and and_33 (and_33_out, not_249_out, not_250_out, not_251_out, not_252_out, not_253_out, not_254_out, F5, not_255_out, F3, not_256_out, F1, not_257_out);
  and and_34 (and_34_out, not_258_out, not_259_out, not_260_out, not_261_out, not_262_out, not_263_out, not_264_out, not_265_out, F3, F2, not_266_out, not_267_out);
  and and_35 (and_35_out, not_268_out, not_269_out, not_270_out, OP2, not_271_out, not_272_out);
  and and_36 (and_36_out, not_273_out, not_274_out, not_275_out, OP2, not_276_out, OP0);
  and and_37 (and_37_out, OP5, not_277_out, OP3, not_278_out, OP1, OP0);
  and and_38 (and_38_out, not_279_out, not_280_out, not_281_out, not_282_out, not_283_out, not_284_out, not_285_out, not_286_out, not_287_out, F2, F1, F0);
  and and_39 (and_39_out, not_288_out, not_289_out, not_290_out, not_291_out, not_292_out, not_293_out, F5, not_294_out, not_295_out, F2, F1, not_296_out);
  or or_1 (R1_Used, and_1_out, and_2_out, and_3_out, and_4_out, and_5_out, and_6_out, and_7_out, and_8_out, and_9_out, and_10_out, and_11_out, and_12_out, and_13_out, and_14_out, and_15_out, and_16_out, and_17_out, and_18_out, and_19_out, and_20_out, and_21_out, and_22_out, and_23_out);
  or or_2 (R2_Used, and_24_out, and_25_out, and_26_out, and_27_out, and_28_out, and_29_out, and_30_out, and_31_out, and_32_out, and_33_out, and_34_out, and_35_out, and_36_out, and_37_out, and_38_out, and_39_out);
endmodule

module \数据相关检测  (
  input  [5:0] OP,
  input  [4:0] EX_WriteReg_num,
  input  EX_RegWrite,
  input  [4:0] MEM_WriteReg_num,
  input  MEM_RegWrite,
  input  [5:0] Func,
  input  [4:0] ID_R1_num,
  input  [4:0] ID_R2_num,
  output \数据相关 
);

  wire and_1_out, and_2_out, and_3_out, and_4_out, and_5_out, and_6_out, comparator_1_eq, comparator_2_eq,
       comparator_3_eq, comparator_4_eq, comparator_5_eq, comparator_6_eq, or_1_out, or_2_out,
       \源寄存器使用情况_1_r1_used , \源寄存器使用情况_1_r2_used ;

  \源寄存器使用情况  \u_源寄存器使用情况_1  (
    .OP0(OP[0]), .OP1(OP[1]), .OP2(OP[2]), .OP3(OP[3]), .OP4(OP[4]), .OP5(OP[5]), .F0(Func[0]), .F1(Func[1]),
    .F2(Func[2]), .F3(Func[3]), .F4(Func[4]), .F5(Func[5]), .R1_Used(\源寄存器使用情况_1_r1_used ),
    .R2_Used(\源寄存器使用情况_1_r2_used ));
  Comparator #(.width(5)) comparator_1 (.a(EX_WriteReg_num), .b(ID_R2_num), .eq(comparator_1_eq));  // open: gt, lt
  Comparator #(.width(5)) comparator_2 (.a(EX_WriteReg_num), .b(ID_R1_num), .eq(comparator_2_eq));  // open: gt, lt
  Comparator #(.width(5)) comparator_3 (.a(MEM_WriteReg_num), .b(ID_R1_num), .eq(comparator_3_eq));  // open: gt, lt
  Comparator #(.width(5)) comparator_4 (.a(MEM_WriteReg_num), .b(ID_R2_num), .eq(comparator_4_eq));  // open: gt, lt
  Comparator #(.width(5)) comparator_5 (.a({5{1'b0}}), .b(ID_R2_num), .eq(comparator_5_eq));  // open: gt, lt
  Comparator #(.width(5)) comparator_6 (.a({5{1'b0}}), .b(ID_R1_num), .eq(comparator_6_eq));  // open: gt, lt
  and and_1 (and_1_out, ~comparator_5_eq, \源寄存器使用情况_1_r2_used , comparator_1_eq);  // AND_Gate
  or or_1 (or_1_out, and_1_out, and_2_out);
  and and_2 (and_2_out, ~comparator_6_eq, \源寄存器使用情况_1_r1_used , comparator_2_eq);  // AND_Gate
  and and_3 (and_3_out, ~comparator_6_eq, \源寄存器使用情况_1_r1_used , comparator_3_eq);  // AND_Gate
  or or_2 (or_2_out, and_3_out, and_4_out);
  and and_4 (and_4_out, ~comparator_5_eq, \源寄存器使用情况_1_r2_used , comparator_4_eq);  // AND_Gate
  and and_5 (and_5_out, EX_RegWrite, or_1_out);
  or or_3 (\数据相关 , and_5_out, and_6_out);
  and and_6 (and_6_out, MEM_RegWrite, or_2_out);

  // Other names for the same wires on the sheet: OP_CODE[5:0] = OP
endmodule

module IF_ID (
  input  miss,
  input  [31:0] dataout,
  input  [31:0] IR,
  input  [31:0] PC,
  input  \传输状态In_表明当前传输数据有效 ,
  input  CLK,
  input  \同步清零_气泡_高电平有效 ,
  input  \使能端_低电平有效_stall_高电平有效 ,
  output miss_2,
  output [31:0] dataout_2,
  output [31:0] IR_2,
  output [31:0] PC_2,
  output \传输状态Out_表明当前传输数据有效 
);

  wire multiplexer_1_out, multiplexer_5_out, not_1_out;
  wire [31:0] multiplexer_2_out, multiplexer_3_out, multiplexer_4_out;

  Multiplexer #(.enable("false")) multiplexer_1 (
    .in0(miss), .in1(1'b0), .out(multiplexer_1_out), .sel(\同步清零_气泡_高电平有效 ));
  Multiplexer #(.width(32), .enable("false")) multiplexer_2 (
    .in0(dataout), .in1({32{1'b0}}), .out(multiplexer_2_out), .sel(\同步清零_气泡_高电平有效 ));
  Multiplexer #(.width(32), .enable("false")) multiplexer_3 (
    .in0(IR), .in1({32{1'b0}}), .out(multiplexer_3_out), .sel(\同步清零_气泡_高电平有效 ));
  Multiplexer #(.width(32), .enable("false")) multiplexer_4 (
    .in0(PC), .in1({32{1'b0}}), .out(multiplexer_4_out), .sel(\同步清零_气泡_高电平有效 ));
  Multiplexer #(.enable("false")) multiplexer_5 (
    .in0(\传输状态In_表明当前传输数据有效 ), .in1(1'b0), .out(multiplexer_5_out), .sel(\同步清零_气泡_高电平有效 ));
  Register #(.width(1)) register_1 (.D(multiplexer_1_out), .en(not_1_out), .Q(miss_2), .clk(CLK));  // open: clr
  Register #(.width(32)) register_2 (.D(multiplexer_2_out), .en(not_1_out), .Q(dataout_2), .clk(CLK));  // open: clr
  Register #(.width(32)) register_3 (.D(multiplexer_3_out), .en(not_1_out), .Q(IR_2), .clk(CLK));  // open: clr
  Register #(.width(32)) register_4 (.D(multiplexer_4_out), .en(not_1_out), .Q(PC_2), .clk(CLK));  // open: clr
  Register #(.width(1)) register_5 (
    .D(multiplexer_5_out), .en(not_1_out), .Q(\传输状态Out_表明当前传输数据有效 ), .clk(CLK));  // open: clr
  not not_1 (not_1_out, \使能端_低电平有效_stall_高电平有效 );

  // Notes on the sheet:
  //   同步清零_气泡_高电平有效: pull=down
  //   使能端_低电平有效_stall_高电平有效: pull=down
endmodule

module ID_EX (
  input  [4:0] WB,
  input  [4:0] MEM,
  input  [4:0] EX,
  input  [1:0] R1,
  input  [1:0] R2,
  input  miss,
  input  [31:0] dataout,
  input  [31:0] IR,
  input  [31:0] PC,
  input  [31:0] A,
  input  [31:0] B,
  input  [31:0] SHMAT,
  input  \传输状态In_表明当前传输数据有效 ,
  input  CLK,
  input  \同步清零_气泡_高电平有效 ,
  input  \使能端_低电平有效_stall_高电平有效 ,
  output [4:0] WB_2,
  output [4:0] MEM_2,
  output [4:0] EX_2,
  output [1:0] R1_2,
  output [1:0] R2_2,
  output miss_2,
  output [31:0] dataout_2,
  output [31:0] IR_2,
  output [31:0] PC_2,
  output [31:0] A_2,
  output [31:0] B_2,
  output [31:0] SHMAT_2,
  output \传输状态Out_表明当前传输数据有效 
);

  wire multiplexer_6_out, multiplexer_13_out, not_1_out;
  wire [1:0] multiplexer_4_out, multiplexer_5_out;
  wire [4:0] multiplexer_1_out, multiplexer_2_out, multiplexer_3_out;
  wire [31:0] multiplexer_7_out, multiplexer_8_out, multiplexer_9_out, multiplexer_10_out,
       multiplexer_11_out, multiplexer_12_out;

  Multiplexer #(.width(5), .enable("false")) multiplexer_1 (
    .in0(WB), .in1({5{1'b0}}), .out(multiplexer_1_out), .sel(\同步清零_气泡_高电平有效 ));
  Multiplexer #(.width(5), .enable("false")) multiplexer_2 (
    .in0(MEM), .in1({5{1'b0}}), .out(multiplexer_2_out), .sel(\同步清零_气泡_高电平有效 ));
  Multiplexer #(.width(5), .enable("false")) multiplexer_3 (
    .in0(EX), .in1({5{1'b0}}), .out(multiplexer_3_out), .sel(\同步清零_气泡_高电平有效 ));
  Multiplexer #(.width(2), .enable("false")) multiplexer_4 (
    .in0(R1), .in1(2'b00), .out(multiplexer_4_out), .sel(\同步清零_气泡_高电平有效 ));
  Multiplexer #(.width(2), .enable("false")) multiplexer_5 (
    .in0(R2), .in1(2'b00), .out(multiplexer_5_out), .sel(\同步清零_气泡_高电平有效 ));
  Multiplexer #(.enable("false")) multiplexer_6 (
    .in0(miss), .in1(1'b0), .out(multiplexer_6_out), .sel(\同步清零_气泡_高电平有效 ));
  Multiplexer #(.width(32), .enable("false")) multiplexer_7 (
    .in0(dataout), .in1({32{1'b0}}), .out(multiplexer_7_out), .sel(\同步清零_气泡_高电平有效 ));
  Multiplexer #(.width(32), .enable("false")) multiplexer_8 (
    .in0(IR), .in1({32{1'b0}}), .out(multiplexer_8_out), .sel(\同步清零_气泡_高电平有效 ));
  Multiplexer #(.width(32), .enable("false")) multiplexer_9 (
    .in0(PC), .in1({32{1'b0}}), .out(multiplexer_9_out), .sel(\同步清零_气泡_高电平有效 ));
  Multiplexer #(.width(32), .enable("false")) multiplexer_10 (
    .in0(A), .in1({32{1'b0}}), .out(multiplexer_10_out), .sel(\同步清零_气泡_高电平有效 ));
  Multiplexer #(.width(32), .enable("false")) multiplexer_11 (
    .in0(B), .in1({32{1'b0}}), .out(multiplexer_11_out), .sel(\同步清零_气泡_高电平有效 ));
  Multiplexer #(.width(32), .enable("false")) multiplexer_12 (
    .in0(SHMAT), .in1({32{1'b0}}), .out(multiplexer_12_out), .sel(\同步清零_气泡_高电平有效 ));
  Multiplexer #(.enable("false")) multiplexer_13 (
    .in0(\传输状态In_表明当前传输数据有效 ), .in1(1'b0), .out(multiplexer_13_out), .sel(\同步清零_气泡_高电平有效 ));
  not not_1 (not_1_out, \使能端_低电平有效_stall_高电平有效 );
  Register #(.width(5)) register_1 (.D(multiplexer_1_out), .en(not_1_out), .Q(WB_2), .clk(CLK));  // open: clr
  Register #(.width(5)) register_2 (.D(multiplexer_2_out), .en(not_1_out), .Q(MEM_2), .clk(CLK));  // open: clr
  Register #(.width(5)) register_3 (.D(multiplexer_3_out), .en(not_1_out), .Q(EX_2), .clk(CLK));  // open: clr
  Register #(.width(2)) register_4 (.D(multiplexer_4_out), .en(not_1_out), .Q(R1_2), .clk(CLK));  // open: clr
  Register #(.width(2)) register_5 (.D(multiplexer_5_out), .en(not_1_out), .Q(R2_2), .clk(CLK));  // open: clr
  Register #(.width(1)) register_6 (.D(multiplexer_6_out), .en(not_1_out), .Q(miss_2), .clk(CLK));  // open: clr
  Register #(.width(32)) register_7 (.D(multiplexer_7_out), .en(not_1_out), .Q(dataout_2), .clk(CLK));  // open: clr
  Register #(.width(32)) register_8 (.D(multiplexer_8_out), .en(not_1_out), .Q(IR_2), .clk(CLK));  // open: clr
  Register #(.width(32)) register_9 (.D(multiplexer_9_out), .en(not_1_out), .Q(PC_2), .clk(CLK));  // open: clr
  Register #(.width(32)) register_10 (.D(multiplexer_10_out), .en(not_1_out), .Q(A_2), .clk(CLK));  // open: clr
  Register #(.width(32)) register_11 (.D(multiplexer_11_out), .en(not_1_out), .Q(B_2), .clk(CLK));  // open: clr
  Register #(.width(32)) register_12 (.D(multiplexer_12_out), .en(not_1_out), .Q(SHMAT_2), .clk(CLK));  // open: clr
  Register #(.width(1)) register_13 (
    .D(multiplexer_13_out), .en(not_1_out), .Q(\传输状态Out_表明当前传输数据有效 ), .clk(CLK));  // open: clr

  // Notes on the sheet:
  //   使能端_低电平有效_stall_高电平有效: pull=down
  //   同步清零_气泡_高电平有效: pull=down
endmodule

module EX_MEM (
  input  [4:0] WB,
  input  [4:0] MEM,
  input  [31:0] IR,
  input  [31:0] PC,
  input  [31:0] A,
  input  [31:0] B,
  input  [31:0] ALU,
  input  \传输状态In_表明当前传输数据有效 ,
  input  CLK,
  input  \同步清零_气泡_高电平有效 ,
  input  \使能端_低电平有效_stall_高电平有效 ,
  output [4:0] WB_2,
  output [4:0] MEM_2,
  output [31:0] IR_2,
  output [31:0] PC_2,
  output [31:0] A_2,
  output [31:0] B_2,
  output [31:0] ALU_2,
  output \传输状态Out_表明当前传输数据有效 
);

  wire multiplexer_8_out, not_1_out;
  wire [4:0] multiplexer_1_out, multiplexer_2_out;
  wire [31:0] multiplexer_3_out, multiplexer_4_out, multiplexer_5_out, multiplexer_6_out, multiplexer_7_out;

  Multiplexer #(.width(5), .enable("false")) multiplexer_1 (
    .in0(WB), .in1({5{1'b0}}), .out(multiplexer_1_out), .sel(\同步清零_气泡_高电平有效 ));
  Multiplexer #(.width(5), .enable("false")) multiplexer_2 (
    .in0(MEM), .in1({5{1'b0}}), .out(multiplexer_2_out), .sel(\同步清零_气泡_高电平有效 ));
  Multiplexer #(.width(32), .enable("false")) multiplexer_3 (
    .in0(IR), .in1({32{1'b0}}), .out(multiplexer_3_out), .sel(\同步清零_气泡_高电平有效 ));
  Multiplexer #(.width(32), .enable("false")) multiplexer_4 (
    .in0(PC), .in1({32{1'b0}}), .out(multiplexer_4_out), .sel(\同步清零_气泡_高电平有效 ));
  Multiplexer #(.width(32), .enable("false")) multiplexer_5 (
    .in0(A), .in1({32{1'b0}}), .out(multiplexer_5_out), .sel(\同步清零_气泡_高电平有效 ));
  Multiplexer #(.width(32), .enable("false")) multiplexer_6 (
    .in0(B), .in1({32{1'b0}}), .out(multiplexer_6_out), .sel(\同步清零_气泡_高电平有效 ));
  Multiplexer #(.width(32), .enable("false")) multiplexer_7 (
    .in0(ALU), .in1({32{1'b0}}), .out(multiplexer_7_out), .sel(\同步清零_气泡_高电平有效 ));
  Multiplexer #(.enable("false")) multiplexer_8 (
    .in0(\传输状态In_表明当前传输数据有效 ), .in1(1'b0), .out(multiplexer_8_out), .sel(\同步清零_气泡_高电平有效 ));
  not not_1 (not_1_out, \使能端_低电平有效_stall_高电平有效 );
  Register #(.width(5)) register_1 (.D(multiplexer_1_out), .en(not_1_out), .Q(WB_2), .clk(CLK));  // open: clr
  Register #(.width(5)) register_2 (.D(multiplexer_2_out), .en(not_1_out), .Q(MEM_2), .clk(CLK));  // open: clr
  Register #(.width(32)) register_3 (.D(multiplexer_3_out), .en(not_1_out), .Q(IR_2), .clk(CLK));  // open: clr
  Register #(.width(32)) register_4 (.D(multiplexer_4_out), .en(not_1_out), .Q(PC_2), .clk(CLK));  // open: clr
  Register #(.width(32)) register_5 (.D(multiplexer_5_out), .en(not_1_out), .Q(A_2), .clk(CLK));  // open: clr
  Register #(.width(32)) register_6 (.D(multiplexer_6_out), .en(not_1_out), .Q(B_2), .clk(CLK));  // open: clr
  Register #(.width(32)) register_7 (.D(multiplexer_7_out), .en(not_1_out), .Q(ALU_2), .clk(CLK));  // open: clr
  Register #(.width(1)) register_8 (
    .D(multiplexer_8_out), .en(not_1_out), .Q(\传输状态Out_表明当前传输数据有效 ), .clk(CLK));  // open: clr

  // Notes on the sheet:
  //   同步清零_气泡_高电平有效: pull=down
  //   使能端_低电平有效_stall_高电平有效: pull=down
endmodule
module MEM_WB (
  input  [4:0] WB,
  input  [31:0] IR,
  input  [31:0] PC,
  input  [31:0] ALU,
  input  [31:0] MD,
  input  [31:0] A,
  input  [31:0] B,
  input  \传输状态In_表明当前传输数据有效 ,
  input  CLK,
  input  \同步清零_气泡_高电平有效 ,
  input  \使能端_低电平有效_stall_高电平有效 ,
  output [4:0] WB_2,
  output [31:0] IR_2,
  output [31:0] PC_2,
  output [31:0] ALU_2,
  output [31:0] MD_2,
  output [31:0] A_2,
  output [31:0] B_2,
  output \传输状态Out_表明当前传输数据有效 
);

  wire multiplexer_8_out, not_1_out;
  wire [4:0] multiplexer_1_out;
  wire [31:0] multiplexer_2_out, multiplexer_3_out, multiplexer_4_out, multiplexer_5_out, multiplexer_6_out,
       multiplexer_7_out;

  Multiplexer #(.width(5), .enable("false")) multiplexer_1 (
    .in0(WB), .in1({5{1'b0}}), .out(multiplexer_1_out), .sel(\同步清零_气泡_高电平有效 ));
  Multiplexer #(.width(32), .enable("false")) multiplexer_2 (
    .in0(IR), .in1({32{1'b0}}), .out(multiplexer_2_out), .sel(\同步清零_气泡_高电平有效 ));
  Multiplexer #(.width(32), .enable("false")) multiplexer_3 (
    .in0(PC), .in1({32{1'b0}}), .out(multiplexer_3_out), .sel(\同步清零_气泡_高电平有效 ));
  Multiplexer #(.width(32), .enable("false")) multiplexer_4 (
    .in0(ALU), .in1({32{1'b0}}), .out(multiplexer_4_out), .sel(\同步清零_气泡_高电平有效 ));
  Multiplexer #(.width(32), .enable("false")) multiplexer_5 (
    .in0(MD), .in1({32{1'b0}}), .out(multiplexer_5_out), .sel(\同步清零_气泡_高电平有效 ));
  Multiplexer #(.width(32), .enable("false")) multiplexer_6 (
    .in0(A), .in1({32{1'b0}}), .out(multiplexer_6_out), .sel(\同步清零_气泡_高电平有效 ));
  Multiplexer #(.width(32), .enable("false")) multiplexer_7 (
    .in0(B), .in1({32{1'b0}}), .out(multiplexer_7_out), .sel(\同步清零_气泡_高电平有效 ));
  Multiplexer #(.enable("false")) multiplexer_8 (
    .in0(\传输状态In_表明当前传输数据有效 ), .in1(1'b0), .out(multiplexer_8_out), .sel(\同步清零_气泡_高电平有效 ));
  not not_1 (not_1_out, \使能端_低电平有效_stall_高电平有效 );
  Register #(.width(5)) register_1 (.D(multiplexer_1_out), .en(not_1_out), .Q(WB_2), .clk(CLK));  // open: clr
  Register #(.width(32)) register_2 (.D(multiplexer_2_out), .en(not_1_out), .Q(IR_2), .clk(CLK));  // open: clr
  Register #(.width(32)) register_3 (.D(multiplexer_3_out), .en(not_1_out), .Q(PC_2), .clk(CLK));  // open: clr
  Register #(.width(32)) register_4 (.D(multiplexer_4_out), .en(not_1_out), .Q(ALU_2), .clk(CLK));  // open: clr
  Register #(.width(32)) register_5 (.D(multiplexer_5_out), .en(not_1_out), .Q(MD_2), .clk(CLK));  // open: clr
  Register #(.width(32)) register_6 (.D(multiplexer_6_out), .en(not_1_out), .Q(A_2), .clk(CLK));  // open: clr
  Register #(.width(32)) register_7 (.D(multiplexer_7_out), .en(not_1_out), .Q(B_2), .clk(CLK));  // open: clr
  Register #(.width(1)) register_8 (
    .D(multiplexer_8_out), .en(not_1_out), .Q(\传输状态Out_表明当前传输数据有效 ), .clk(CLK));  // open: clr

  // Notes on the sheet:
  //   使能端_低电平有效_stall_高电平有效: pull=down
  //   同步清零_气泡_高电平有效: pull=down
endmodule

module \分支相关流水线  (
);

  wire and_1_out, and_2_out, and_3_out, and_4_out, and_5_out, CLK, comparator_1_eq, EQUL,
       \ex_mem_1_传输状态out_表明当前传输数据有效 , Go, \id_ex_1_传输状态out_表明当前传输数据有效 , \if_id_1_传输状态out_表明当前传输数据有效 , IR1,
       IR2, IR3, JMP, JMPp, JR, JRr, not_1_out, not_2_out, not_3_out, not_4_out, RST, sel, SignedExt, sys,
       W1, W2, W3, WE, \分支 ;
  wire [2:0] id_ex_1_mem_2, MEM;
  wire [3:0] mem_wb_1_wb_2;
  wire [4:0] EX, ex_mem_1_mem_2, ex_mem_1_wb_2, id_ex_1_ex_2, id_ex_1_wb_2, multiplexer_3_out,
       multiplexer_5_out, multiplexer_6_out, multiplexer_10_out, shamt, WB, WR;
  wire [9:0] ex_mem_1_alu_2_2;
  wire [11:0] EX_PC, ID_PC, IF_PC, MEM_PC, WB_PC;
  wire [15:0] counter_4_q, counter_5_q, if_id_1_ir_2, \LoadUse次数 , \总周期数 , \插入气泡数 , \无条件分支数 , \条件分支成功数 ;
  wire [31:0] adder_1_out, bit_extender_1_out, bit_extender_2_out, ex_mem_1_a_2, ex_mem_1_alu_2,
       ex_mem_1_b_2, ex_mem_1_ir_2, ex_mem_1_pc_2, id_ex_1_a_2, id_ex_1_b_2, id_ex_1_ir_2, id_ex_1_pc_2,
       id_ex_1_shmat_2, if_id_1_pc_2, im, JMPA, LedData, mem_wb_1_alu_2, mem_wb_1_ir_2, mem_wb_1_md_2,
       mips_alu_1_result, mips_regifile_1_r1, mips_regifile_1_r2, multiplexer_1_out, multiplexer_2_out,
       multiplexer_7_out, pc_4, PC_q, R1, R2, ram_1_data, RD, rom_1_data, shifter_1_out, \分支a ;
  wire [31:16] if_id_1_ir_2_2;

  Button \u_总复位  (.out(RST));
  Button _1 (.out(IR1));
  Button _2 (.out(IR2));
  Button _3 (.out(IR3));
  Button \u_继续运行  (.out(Go));
  LED led_1 (.in(W1));
  LED led_2 (.in(W2));
  LED led_3 (.in(W3));
  Multiplexer #(.width(32), .enable("false")) multiplexer_1 (
    .in0(adder_1_out), .in1(\分支a ), .out(multiplexer_1_out), .sel(\分支 ));
  Hex_Digit_Display hex_digit_display_1 (.value(LedData[31:28]));  // open: dp
  Multiplexer #(.width(32), .enable("false")) multiplexer_2 (
    .in0(multiplexer_1_out), .in1(JMPA), .out(multiplexer_2_out), .sel(JMPp));
  Hex_Digit_Display hex_digit_display_2 (.value(LedData[23:20]));  // open: dp
  Hex_Digit_Display hex_digit_display_3 (.value(LedData[27:24]));  // open: dp
  Register #(.width(32)) PC (.D(multiplexer_2_out), .en(sel), .Q(PC_q), .clk(CLK), .clr(RST));
  Hex_Digit_Display hex_digit_display_4 (.value(LedData[19:16]));  // open: dp
  Hex_Digit_Display hex_digit_display_5 (.value(LedData[15:12]));  // open: dp
  Hex_Digit_Display hex_digit_display_6 (.value(LedData[7:4]));  // open: dp
  Hex_Digit_Display hex_digit_display_7 (.value(LedData[11:8]));  // open: dp
  Clock clock_1 (.out(CLK));
  Counter #(.width(16), .max('hffff)) counter_1 (
    .count(sel), .Q(\总周期数 ), .clk(CLK), .clr(RST));  // open: load, D, carry
  Adder #(.width(32)) adder_1 (.a(PC_q), .b(32'h4), .out(adder_1_out));  // open: cin, cout
  Hex_Digit_Display hex_digit_display_8 (.value(LedData[3:0]));  // open: dp
  ROM #(.addrWidth(10), .dataWidth(32)) rom_1 (.addr(PC_q[11:2]), .data(rom_1_data));  // open: sel
  IF_ID if_id_1 (
    .IR(rom_1_data), .PC(PC_q), .\传输状态In_表明当前传输数据有效 (1'b1), .CLK(CLK), .IR_2({if_id_1_ir_2_2, if_id_1_ir_2}),
    .PC_2(if_id_1_pc_2), .\传输状态Out_表明当前传输数据有效 (\if_id_1_传输状态out_表明当前传输数据有效 ), .\同步清零_气泡_高电平有效 (\分支 ));  // open: 使能端_低电平有效_stall_高电平有效, miss, miss_2, dataout, dataout_2
  // Probe on \总周期数 
  // Probe on \无条件分支数 
  // Probe on \条件分支成功数 
  // Probe on \插入气泡数 
  // Probe on \LoadUse次数 
  assign bit_extender_1_out = {{16{if_id_1_ir_2[15]}}, if_id_1_ir_2};  // Bit_Extender bit_extender_1
  assign bit_extender_2_out = {{16{1'b0}}, if_id_1_ir_2};  // Bit_Extender bit_extender_2
  // Probe on IF_PC
  and and_1 (and_1_out, \分支 , not_1_out);
  not not_1 (not_1_out, JMPp);
  Multiplexer #(.width(5), .enable("false")) multiplexer_3 (
    .in0(if_id_1_ir_2_2[25:21]), .in1({5{1'b1}}), .out(multiplexer_3_out), .sel(JR));
  Multiplexer #(.width(32), .enable("false")) multiplexer_4 (
    .in0(bit_extender_1_out), .in1(bit_extender_2_out), .out(im), .sel(SignedExt));
  // Probe on ID_PC
  Counter #(.width(16), .max('hffff)) counter_2 (
    .count(and_1_out), .Q(\条件分支成功数 ), .clk(CLK), .clr(RST));  // open: load, D, carry
  \硬布线控制器  \u_硬布线控制器_1  (
    .Func(if_id_1_ir_2[5:0]), .OP(if_id_1_ir_2_2[31:26]), .ALU_OP(EX[3:0]), .MemToReg(WB[0]),
    .MemWrite(MEM[2]), .ALU_SRC(EX[4]), .RegWrite(WB[1]), .SysCALL(WB[4]), .SignedExt(SignedExt),
    .RegDst(WB[3]), .JR(JR), .JMP(JMP), .Beq(MEM[0]), .JAL(WB[2]), .Bne(MEM[1]));
  Multiplexer #(.width(5), .enable("false")) multiplexer_5 (
    .in0(multiplexer_3_out), .in1(5'b00010), .out(multiplexer_5_out), .sel(WB[4]));
  Multiplexer #(.width(5), .enable("false")) multiplexer_6 (
    .in0(if_id_1_ir_2_2[20:16]), .in1(5'b00100), .out(multiplexer_6_out), .sel(WB[4]));
  // Probe on MEM_PC
  // Probe on EX_PC
  // Probe on WB_PC
  MIPS_Regifile mips_regifile_1 (
    .Din(RD), .Clk(CLK), .R1(mips_regifile_1_r1), .R2(mips_regifile_1_r2), .WE(WE), .W_num(WR),
    .R1_num(multiplexer_5_out), .R2_num(multiplexer_6_out));
  ID_EX id_ex_1 (
    .WB(WB), .MEM({JR, JMP, MEM}), .EX(EX), .IR({if_id_1_ir_2_2, if_id_1_ir_2}), .PC(if_id_1_pc_2),
    .A(mips_regifile_1_r1), .B(mips_regifile_1_r2), .SHMAT(im),
    .\传输状态In_表明当前传输数据有效 (\if_id_1_传输状态out_表明当前传输数据有效 ), .CLK(CLK), .WB_2(id_ex_1_wb_2),
    .MEM_2({JRr, JMPp, id_ex_1_mem_2}), .EX_2(id_ex_1_ex_2),
    .IR_2({id_ex_1_ir_2[31:11], shamt, id_ex_1_ir_2[5:0]}), .PC_2(id_ex_1_pc_2), .A_2(id_ex_1_a_2),
    .B_2(id_ex_1_b_2), .SHMAT_2(id_ex_1_shmat_2), .\传输状态Out_表明当前传输数据有效 (\id_ex_1_传输状态out_表明当前传输数据有效 ),
    .\同步清零_气泡_高电平有效 (\分支 ));  // open: 使能端_低电平有效_stall_高电平有效, R1, R1_2, R2, R2_2, miss, miss_2, dataout, dataout_2
  Counter #(.width(16), .max('hffff)) counter_3 (
    .count(JMPp), .Q(\无条件分支数 ), .clk(CLK), .clr(RST));  // open: load, D, carry
  Multiplexer #(.width(32), .enable("false")) multiplexer_7 (
    .in0(id_ex_1_b_2), .in1(id_ex_1_shmat_2), .out(multiplexer_7_out), .sel(id_ex_1_ex_2[4]));
  Shifter #(.width(32)) shifter_1 (.in(id_ex_1_shmat_2), .\dist (5'b00010), .out(shifter_1_out));
  not not_2 (not_2_out, EQUL);
  Multiplexer #(.width(32), .enable("false")) multiplexer_8 (
    .in0({pc_4[31:28], id_ex_1_ir_2[25:11], shamt, id_ex_1_ir_2[5:0], 2'b00}), .in1(id_ex_1_a_2), .out(JMPA),
    .sel(JRr));
  MIPS_ALU mips_alu_1 (
    .X(id_ex_1_a_2), .Y(multiplexer_7_out), .AluOP(id_ex_1_ex_2[3:0]), .Equal(EQUL),
    .Result(mips_alu_1_result), .shamt(shamt));  // open: Result_2
  Adder #(.width(32)) adder_2 (.a(shifter_1_out), .b(pc_4), .out(\分支a ));  // open: cin, cout
  and and_2 (and_2_out, id_ex_1_mem_2[0], EQUL);
  and and_3 (and_3_out, id_ex_1_mem_2[1], not_2_out);
  Adder #(.width(32)) adder_3 (.a(32'h4), .b(id_ex_1_pc_2), .out(pc_4));  // open: cin, cout
  or or_1 (\分支 , and_2_out, JMPp, and_3_out);
  Counter #(.width(16), .max('hffff)) counter_4 (
    .count(\分支 ), .Q(counter_4_q), .clk(CLK), .clr(RST));  // open: load, D, carry
  Counter #(.width(16), .max('hffff)) counter_5 (
    .count(\分支 ), .Q(counter_5_q), .clk(CLK), .clr(RST));  // open: load, D, carry
  EX_MEM ex_mem_1 (
    .WB(id_ex_1_wb_2), .MEM({JRr, JMPp, id_ex_1_mem_2}),
    .IR({id_ex_1_ir_2[31:11], shamt, id_ex_1_ir_2[5:0]}), .PC(id_ex_1_pc_2), .B(id_ex_1_b_2),
    .ALU(mips_alu_1_result), .\传输状态In_表明当前传输数据有效 (\id_ex_1_传输状态out_表明当前传输数据有效 ), .CLK(CLK),
    .WB_2(ex_mem_1_wb_2), .MEM_2(ex_mem_1_mem_2), .IR_2(ex_mem_1_ir_2), .PC_2(ex_mem_1_pc_2),
    .B_2(ex_mem_1_b_2), .ALU_2({ex_mem_1_alu_2[31:12], ex_mem_1_alu_2_2, ex_mem_1_alu_2[1:0]}),
    .\传输状态Out_表明当前传输数据有效 (\ex_mem_1_传输状态out_表明当前传输数据有效 ), .A(id_ex_1_a_2), .A_2(ex_mem_1_a_2));  // open: 同步清零_气泡_高电平有效, 使能端_低电平有效_stall_高电平有效
  Adder #(.width(16)) adder_4 (.a(counter_4_q), .b(counter_5_q), .out(\插入气泡数 ));  // open: cin, cout
  Comparator #(.width(32)) comparator_1 (.a(R1), .b(32'h32), .eq(comparator_1_eq));  // open: gt, lt
  and and_4 (and_4_out, comparator_1_eq, sys);
  not not_3 (not_3_out, comparator_1_eq);
  not not_4 (not_4_out, and_4_out);
  and and_5 (and_5_out, not_3_out, sys);
  RAM #(.addrWidth(10), .dataWidth(32), .bus("separate")) ram_1 (
    .addr(ex_mem_1_alu_2_2), .din(ex_mem_1_b_2), .data(ram_1_data), .str(ex_mem_1_mem_2[2]), .sel(sel),
    .clk(CLK), .clr(RST));  // open: ld
  or or_2 (sel, Go, not_4_out);
  Register #(.width(32)) register_1 (.D(R2), .en(and_5_out), .Q(LedData), .clk(CLK), .clr(RST));
  MEM_WB mem_wb_1 (
    .WB(ex_mem_1_wb_2), .IR(ex_mem_1_ir_2), .PC(ex_mem_1_pc_2),
    .ALU({ex_mem_1_alu_2[31:12], ex_mem_1_alu_2_2, ex_mem_1_alu_2[1:0]}), .MD(ram_1_data),
    .\传输状态In_表明当前传输数据有效 (\ex_mem_1_传输状态out_表明当前传输数据有效 ), .CLK(CLK),
    .WB_2({sys, mem_wb_1_wb_2[3:2], WE, mem_wb_1_wb_2[0]}), .IR_2(mem_wb_1_ir_2), .ALU_2(mem_wb_1_alu_2),
    .MD_2(mem_wb_1_md_2), .A(ex_mem_1_a_2), .A_2(R1), .B(ex_mem_1_b_2), .B_2(R2));  // open: PC_2, 传输状态Out_表明当前传输数据有效, 同步清零_气泡_高电平有效, 使能端_低电平有效_stall_高电平有效
  Multiplexer #(.width(32)) multiplexer_9 (
    .in0(mem_wb_1_alu_2), .in1(mem_wb_1_md_2), .out(RD), .sel(mem_wb_1_wb_2[0]));  // open: en
  Multiplexer #(.width(5), .enable("false")) multiplexer_10 (
    .in0(mem_wb_1_ir_2[20:16]), .in1(mem_wb_1_ir_2[15:11]), .out(multiplexer_10_out), .sel(mem_wb_1_wb_2[3]));
  Multiplexer #(.width(5), .enable("false")) multiplexer_11 (
    .in0(multiplexer_10_out), .in1({5{1'b1}}), .out(WR), .sel(mem_wb_1_wb_2[2]));

  // Other names for the same wires on the sheet: MEM[4:3] = {JR, JMP}

  // Notes on the sheet:
  //   中断源
  //   中断等待指示
  //   数码管输出
  //   contents of rom_1 (hex, n*v repeats v):
  //   20110020 20020022 8000c06 20110000 20110000 2002000a 10000003 20110000 20110000 2002000a 14110003
  //   20110000 20110000 2002000a c000c14 2002000a 0 0 0 c 2231ffff 0 0 0 112020 0 0 0 c 1620fff6 3e00008
  //   指令字
  //   JMP
  //   JR
  //   OP
  //   OP
  //   Func
  //   Func
  //   rs
  //   rt
  //   rd
  //   Bne
  //   MemToReg
  //   MemWrite
  //   AluOP
  //   AluSrcB
  //   RegWrite
  //   JAL
  //   RegDst
  //   流水调试日志用
  //   rt
  //   rd
endmodule

module \气泡流水线  (
);

  wire and_1_out, and_2_out, and_3_out, and_4_out, and_5_out, and_6_out, and_7_out, CLK, comparator_1_eq,
       EQUL, EX_MEM, EX_WE, Go, ID_EX, IF_ID, IR1, IR2, IR3, JMP, JMPp, JR, JRr, MEM_WE, not_1_out,
       not_2_out, not_3_out, not_4_out, not_5_out, not_6_out, or_1_out, or_2_out, RST, sel, SignedExt, sys,
       W1, W2, W3, WE, \分支 , \数据相关 ;
  wire [2:0] id_ex_1_mem_2, MEM;
  wire [3:0] mem_wb_1_wb_2;
  wire [4:0] EX, ex_mem_1_mem_2, ex_mem_1_wb_2, EX_WR, id_ex_1_ex_2, id_ex_1_wb_2, ID_R1, ID_R2, MEM_WR,
       multiplexer_3_out, multiplexer_9_out, multiplexer_11_out, multiplexer_15_out, shamt, WB, WR;
  wire [5:0] FUNC, OP;
  wire [9:0] ex_mem_1_alu_2_2;
  wire [11:0] EX_PC, ID_PC, IF_PC, MEM_PC, WB_PC;
  wire [15:0] \LoadUse次数 , \总周期数 , \插入气泡数 , \无条件分支数 , \条件分支成功数 ;
  wire [15:6] if_id_1_ir_2;
  wire [25:16] if_id_1_ir_2_2;
  wire [31:0] adder_1_out, adder_4_out, bit_extender_1_out, bit_extender_2_out, ex_mem_1_a_2, ex_mem_1_alu_2,
       ex_mem_1_b_2, ex_mem_1_ir_2, ex_mem_1_pc_2, id_ex_1_a_2, id_ex_1_b_2, id_ex_1_ir_2, id_ex_1_pc_2,
       id_ex_1_shmat_2, if_id_1_pc_2, im, JMPA, LedData, mem_wb_1_alu_2, mem_wb_1_ir_2, mem_wb_1_md_2,
       mem_wb_1_pc_2, mips_alu_1_result, mips_regifile_1_r1, mips_regifile_1_r2, multiplexer_1_out,
       multiplexer_2_out, multiplexer_7_out, multiplexer_13_out, pc_4, PC_q, R1, R2, ram_1_data, RD,
       rom_1_data, shifter_1_out, \分支a ;

  Button \u_总复位  (.out(RST));
  Button _1 (.out(IR1));
  Button _2 (.out(IR2));
  Button _3 (.out(IR3));
  Button \u_继续运行  (.out(Go));
  LED led_1 (.in(W1));
  LED led_2 (.in(W2));
  LED led_3 (.in(W3));
  Multiplexer #(.width(32), .enable("false")) multiplexer_1 (
    .in0(adder_1_out), .in1(\分支a ), .out(multiplexer_1_out), .sel(\分支 ));
  Hex_Digit_Display hex_digit_display_1 (.value(LedData[31:28]));  // open: dp
  Multiplexer #(.width(32), .enable("false")) multiplexer_2 (
    .in0(multiplexer_1_out), .in1(JMPA), .out(multiplexer_2_out), .sel(JMPp));
  and and_1 (and_1_out, sel, not_1_out);
  not not_1 (not_1_out, \数据相关 );
  Hex_Digit_Display hex_digit_display_2 (.value(LedData[27:24]));  // open: dp
  Hex_Digit_Display hex_digit_display_3 (.value(LedData[23:20]));  // open: dp
  Register #(.width(32)) PC (.D(multiplexer_2_out), .en(and_1_out), .Q(PC_q), .clk(CLK), .clr(RST));
  Hex_Digit_Display hex_digit_display_4 (.value(LedData[15:12]));  // open: dp
  Hex_Digit_Display hex_digit_display_5 (.value(LedData[19:16]));  // open: dp
  Hex_Digit_Display hex_digit_display_6 (.value(LedData[11:8]));  // open: dp
  Hex_Digit_Display hex_digit_display_7 (.value(LedData[7:4]));  // open: dp
  Clock clock_1 (.out(CLK));
  Counter #(.width(16), .max('hffff)) counter_1 (
    .count(sel), .Q(\总周期数 ), .clk(CLK), .clr(RST));  // open: load, D, carry
  \数据相关检测  \u_数据相关检测_1  (
    .OP(OP), .EX_WriteReg_num(EX_WR), .EX_RegWrite(EX_WE), .MEM_WriteReg_num(MEM_WR), .MEM_RegWrite(MEM_WE),
    .\数据相关 (\数据相关 ), .Func(FUNC), .ID_R1_num(ID_R1), .ID_R2_num(ID_R2));
  Adder #(.width(32)) adder_1 (.a(PC_q), .b(32'h4), .out(adder_1_out));  // open: cin, cout
  Hex_Digit_Display hex_digit_display_8 (.value(LedData[3:0]));  // open: dp
  ROM #(.addrWidth(10), .dataWidth(32)) rom_1 (.addr(PC_q[11:2]), .data(rom_1_data));  // open: sel
  IF_ID if_id_1 (
    .IR(rom_1_data), .PC(PC_q), .\传输状态In_表明当前传输数据有效 (1'b1), .CLK(CLK),
    .IR_2({OP, if_id_1_ir_2_2, if_id_1_ir_2, FUNC}), .PC_2(if_id_1_pc_2), .\传输状态Out_表明当前传输数据有效 (IF_ID),
    .\同步清零_气泡_高电平有效 (\分支 ), .\使能端_低电平有效_stall_高电平有效 (or_1_out));  // open: miss, miss_2, dataout, dataout_2
  or or_1 (or_1_out, not_3_out, \数据相关 );
  // Probe on \总周期数 
  // Probe on \无条件分支数 
  // Probe on \条件分支成功数 
  // Probe on \插入气泡数 
  // Probe on \LoadUse次数 
  and and_2 (and_2_out, \分支 , not_2_out);
  not not_2 (not_2_out, JMPp);
  assign bit_extender_1_out = {{16{if_id_1_ir_2[15]}}, {if_id_1_ir_2, FUNC}};  // Bit_Extender bit_extender_1
  assign bit_extender_2_out = {{16{1'b0}}, {if_id_1_ir_2, FUNC}};  // Bit_Extender bit_extender_2
  // Probe on IF_PC
  Counter #(.width(16), .max('hffff)) counter_2 (
    .count(and_2_out), .Q(\条件分支成功数 ), .clk(CLK), .clr(RST));  // open: load, D, carry
  Multiplexer #(.width(5), .enable("false")) multiplexer_3 (
    .in0(if_id_1_ir_2_2[25:21]), .in1({5{1'b1}}), .out(multiplexer_3_out), .sel(JR));
  Multiplexer #(.width(32), .enable("false")) multiplexer_4 (
    .in0(bit_extender_1_out), .in1(bit_extender_2_out), .out(im), .sel(SignedExt));
  not not_3 (not_3_out, sel);
  // Probe on ID_PC
  \硬布线控制器  \u_硬布线控制器_1  (
    .Func(FUNC), .OP(OP), .ALU_OP(EX[3:0]), .MemToReg(WB[0]), .MemWrite(MEM[2]), .ALU_SRC(EX[4]),
    .RegWrite(WB[1]), .SysCALL(WB[4]), .SignedExt(SignedExt), .RegDst(WB[3]), .JR(JR), .JMP(JMP),
    .Beq(MEM[0]), .JAL(WB[2]), .Bne(MEM[1]));
  Multiplexer #(.width(5), .enable("false")) multiplexer_5 (
    .in0(multiplexer_3_out), .in1(5'b00010), .out(ID_R1), .sel(WB[4]));
  Multiplexer #(.width(5), .enable("false")) multiplexer_6 (
    .in0(if_id_1_ir_2_2[20:16]), .in1(5'b00100), .out(ID_R2), .sel(WB[4]));
  // Probe on MEM_PC
  // Probe on EX_PC
  // Probe on WB_PC
  MIPS_Regifile mips_regifile_1 (
    .Din(RD), .Clk(CLK), .R1(mips_regifile_1_r1), .R2(mips_regifile_1_r2), .WE(WE), .W_num(WR),
    .R1_num(ID_R1), .R2_num(ID_R2));
  Counter #(.width(16), .max('hffff)) counter_3 (
    .count(JMPp), .Q(\无条件分支数 ), .clk(CLK), .clr(RST));  // open: load, D, carry
  ID_EX id_ex_1 (
    .WB(WB), .MEM({JR, JMP, MEM}), .EX(EX), .IR({OP, if_id_1_ir_2_2, if_id_1_ir_2, FUNC}), .PC(if_id_1_pc_2),
    .A(mips_regifile_1_r1), .B(mips_regifile_1_r2), .SHMAT(im), .\传输状态In_表明当前传输数据有效 (IF_ID), .CLK(CLK),
    .WB_2({id_ex_1_wb_2[4:2], EX_WE, id_ex_1_wb_2[0]}), .MEM_2({JRr, JMPp, id_ex_1_mem_2}),
    .EX_2(id_ex_1_ex_2), .IR_2({id_ex_1_ir_2[31:11], shamt, id_ex_1_ir_2[5:0]}), .PC_2(id_ex_1_pc_2),
    .A_2(id_ex_1_a_2), .B_2(id_ex_1_b_2), .SHMAT_2(id_ex_1_shmat_2), .\传输状态Out_表明当前传输数据有效 (ID_EX),
    .\同步清零_气泡_高电平有效 (or_2_out), .\使能端_低电平有效_stall_高电平有效 (not_3_out));  // open: R1, R1_2, R2, R2_2, miss, miss_2, dataout, dataout_2
  or or_2 (or_2_out, \数据相关 , \分支 );
  Multiplexer #(.width(32), .enable("false")) multiplexer_7 (
    .in0(id_ex_1_b_2), .in1(id_ex_1_shmat_2), .out(multiplexer_7_out), .sel(id_ex_1_ex_2[4]));
  Shifter #(.width(32)) shifter_1 (.in(id_ex_1_shmat_2), .\dist (5'b00010), .out(shifter_1_out));
  not not_4 (not_4_out, EQUL);
  Multiplexer #(.width(32), .enable("false")) multiplexer_8 (
    .in0({pc_4[31:28], id_ex_1_ir_2[25:11], shamt, id_ex_1_ir_2[5:0], 2'b00}), .in1(id_ex_1_a_2), .out(JMPA),
    .sel(JRr));
  MIPS_ALU mips_alu_1 (
    .X(id_ex_1_a_2), .Y(multiplexer_7_out), .AluOP(id_ex_1_ex_2[3:0]), .Equal(EQUL),
    .Result(mips_alu_1_result), .shamt(shamt));  // open: Result_2
  Adder #(.width(32)) adder_2 (.a(shifter_1_out), .b(pc_4), .out(\分支a ));  // open: cin, cout
  Counter #(.width(16), .max('hffff)) counter_4 (
    .count(and_3_out), .Q(\插入气泡数 ), .clk(CLK), .clr(RST));  // open: load, D, carry
  and and_3 (and_3_out, \数据相关 , sel);
  and and_4 (and_4_out, id_ex_1_mem_2[0], EQUL);
  and and_5 (and_5_out, id_ex_1_mem_2[1], not_4_out);
  or or_3 (\分支 , and_4_out, JMPp, and_5_out);
  Multiplexer #(.width(5), .enable("false")) multiplexer_9 (
    .in0(id_ex_1_ir_2[20:16]), .in1(id_ex_1_ir_2[15:11]), .out(multiplexer_9_out), .sel(id_ex_1_wb_2[3]));
  Multiplexer #(.width(5), .enable("false")) multiplexer_10 (
    .in0(multiplexer_9_out), .in1({5{1'b1}}), .out(EX_WR), .sel(id_ex_1_wb_2[2]));
  Adder #(.width(32)) adder_3 (.a(32'h4), .b(id_ex_1_pc_2), .out(pc_4));  // open: cin, cout
  EX_MEM ex_mem_1 (
    .WB({id_ex_1_wb_2[4:2], EX_WE, id_ex_1_wb_2[0]}), .MEM({JRr, JMPp, id_ex_1_mem_2}),
    .IR({id_ex_1_ir_2[31:11], shamt, id_ex_1_ir_2[5:0]}), .PC(id_ex_1_pc_2), .B(id_ex_1_b_2),
    .ALU(mips_alu_1_result), .\传输状态In_表明当前传输数据有效 (ID_EX), .CLK(CLK),
    .WB_2({ex_mem_1_wb_2[4:2], MEM_WE, ex_mem_1_wb_2[0]}), .MEM_2(ex_mem_1_mem_2), .IR_2(ex_mem_1_ir_2),
    .PC_2(ex_mem_1_pc_2), .B_2(ex_mem_1_b_2),
    .ALU_2({ex_mem_1_alu_2[31:12], ex_mem_1_alu_2_2, ex_mem_1_alu_2[1:0]}), .\传输状态Out_表明当前传输数据有效 (EX_MEM),
    .\使能端_低电平有效_stall_高电平有效 (not_3_out), .A(id_ex_1_a_2), .A_2(ex_mem_1_a_2));  // open: 同步清零_气泡_高电平有效
  Comparator #(.width(32)) comparator_1 (.a(R1), .b(32'h32), .eq(comparator_1_eq));  // open: gt, lt
  Multiplexer #(.width(5), .enable("false")) multiplexer_11 (
    .in0(ex_mem_1_ir_2[20:16]), .in1(ex_mem_1_ir_2[15:11]), .out(multiplexer_11_out), .sel(ex_mem_1_wb_2[3]));
  and and_6 (and_6_out, comparator_1_eq, sys);
  not not_5 (not_5_out, comparator_1_eq);
  \分支相关流水线  \u_分支相关流水线_1  ();
  Multiplexer #(.width(5), .enable("false")) multiplexer_12 (
    .in0(multiplexer_11_out), .in1({5{1'b1}}), .out(MEM_WR), .sel(ex_mem_1_wb_2[2]));
  not not_6 (not_6_out, and_6_out);
  and and_7 (and_7_out, not_5_out, sys);
  RAM #(.addrWidth(10), .dataWidth(32), .bus("separate")) ram_1 (
    .addr(ex_mem_1_alu_2_2), .din(ex_mem_1_b_2), .data(ram_1_data), .str(ex_mem_1_mem_2[2]), .sel(sel),
    .clk(CLK), .clr(RST));  // open: ld
  or or_4 (sel, Go, not_6_out);
  Register #(.width(32)) register_1 (.D(R2), .en(and_7_out), .Q(LedData), .clk(CLK), .clr(RST));
  MEM_WB mem_wb_1 (
    .WB({ex_mem_1_wb_2[4:2], MEM_WE, ex_mem_1_wb_2[0]}), .IR(ex_mem_1_ir_2), .PC(ex_mem_1_pc_2),
    .ALU({ex_mem_1_alu_2[31:12], ex_mem_1_alu_2_2, ex_mem_1_alu_2[1:0]}), .MD(ram_1_data),
    .\传输状态In_表明当前传输数据有效 (EX_MEM), .CLK(CLK), .WB_2({sys, mem_wb_1_wb_2[3:2], WE, mem_wb_1_wb_2[0]}),
    .IR_2(mem_wb_1_ir_2), .PC_2(mem_wb_1_pc_2), .ALU_2(mem_wb_1_alu_2), .MD_2(mem_wb_1_md_2),
    .\使能端_低电平有效_stall_高电平有效 (not_3_out), .A(ex_mem_1_a_2), .A_2(R1), .B(ex_mem_1_b_2), .B_2(R2));  // open: 传输状态Out_表明当前传输数据有效, 同步清零_气泡_高电平有效
  Adder #(.width(32)) adder_4 (.a(mem_wb_1_pc_2), .b(32'h4), .out(adder_4_out));  // open: cin, cout
  Multiplexer #(.width(32)) multiplexer_13 (
    .in0(mem_wb_1_alu_2), .in1(mem_wb_1_md_2), .out(multiplexer_13_out), .sel(mem_wb_1_wb_2[0]));  // open: en
  Multiplexer #(.width(32)) multiplexer_14 (
    .in0(multiplexer_13_out), .in1(adder_4_out), .out(RD), .sel(mem_wb_1_wb_2[2]));  // open: en
  Multiplexer #(.width(5), .enable("false")) multiplexer_15 (
    .in0(mem_wb_1_ir_2[20:16]), .in1(mem_wb_1_ir_2[15:11]), .out(multiplexer_15_out), .sel(mem_wb_1_wb_2[3]));
  Multiplexer #(.width(5), .enable("false")) multiplexer_16 (
    .in0(multiplexer_15_out), .in1({5{1'b1}}), .out(WR), .sel(mem_wb_1_wb_2[2]));

  // Other names for the same wires on the sheet: MEM[4:3] = {JR, JMP}

  // Notes on the sheet:
  //   中断源
  //   中断等待指示
  //   数码管输出
  //   contents of rom_1 (hex, n*v repeats v):
  //   20110001 8100005 20110001 20120002 20130003 8100009 20110001 20120002 20130003 810000d 20110001
  //   20120002 20130003 8100011 20110001 20120002 20130003 c1000f7 20100001 20110001 118fc0 112020
  //   20020022 c 118882 12200001 8100015 112020 20020022 c 20110001 118880 112020 20020022 c 12200001
  //   810001f 20110001 118fc0 112020 20020022 c 1188c3 112020 20020022 c 118903 112020 20020022 c 118903
  //   112020 20020022 c 118903 112020 20020022 c 118903 112020 20020022 c 118903 112020 20020022 c 118903
  //   112020 20020022 c 118903 112020 20020022 c 20100001 109fc0 139fc3 8021 2012000c 24160003 26100001
  //   3210000f 20080008 20090001 139900 2709825 132020 20020022 c 1094022 1500fff9 22100001 2018000f
  //   2188024 108700 20080008 20090001 139902 2709825 132021 20020022 c 1094022 1500fff9 108702 2c9b022
  //   12c00001 8100050 4020 1084027 84400 3508ffff 82021 20020022 c 2010ffff 20110000 ae300000 22100001
  //   22310004 ae300000 22100001 22310004 ae300000 22100001 22310004 ae300000 22100001 22310004 ae300000
  //   22100001 22310004 ae300000 22100001 22310004 ae300000 22100001 22310004 ae300000 22100001 22310004
  //   ae300000 22100001 22310004 ae300000 22100001 22310004 ae300000 22100001 22310004 ae300000 22100001
  //   22310004 ae300000 22100001 22310004 ae300000 22100001 22310004 ae300000 22100001 22310004 ae300000
  //   22100001 22310004 22100001 8020 2011003c 8e130000 8e340000 274402a 11000002 ae330000 ae140000
  //   2231fffc 1611fff8 102020 20020022 c 22100004 2011003c 1611fff2 20020032 c 20090000 200b0010 34118483
  //   20120404 118c00 129400 36318281 22520404 ad310000 2328820 21290004 216bffff 1560fffb 200b0020
  //   20090000 85310000 112020 20020022 c 21290002 216bffff 1560fff9 20020032 c 2011000f 112020 20020022 c
  //   2231ffff 621fffb 20020032 c 2008ffff 20117777 112020 20020022 c 200b0010 2288826 112020 20020022 c
  //   216bffff 1560fffa 20020032 c 20080001 20090003 20110876 118d00 112020 20020022 c 200b0008 1118807
  //   1318807 112020 20020022 c 216bffff 1560fff9 20020032 c 20100000 22100001 102020 20020022 c 22100002
  //   102020 20020022 c 22100003 102020 20020022 c 22100004 102020 20020022 c 22100005 102020 20020022 c
  //   22100006 102020 20020022 c 22100007 102020 20020022 c 22100008 102020 20020022 20020022 c 3e00008
  //   指令字
  //   JMP
  //   JR
  //   OP
  //   Func
  //   Func
  //   rs
  //   rt
  //   rd
  //   Bne
  //   MemToReg
  //   MemWrite
  //   AluOP
  //   AluSrcB
  //   RegWrite
  //   JAL
  //   RegDst
  //   流水调试日志用
  //   rt
  //   rt
  //   rd
  //   rt
  //   rd
endmodule

module \重定向流水线  (
);

  wire and_1_out, and_2_out, and_5_out, and_6_out, and_7_out, and_8_out, BGEZ, CLK, comparator_1_lt,
       comparator_2_eq, comparator_3_eq, comparator_4_eq, comparator_5_eq, comparator_6_eq, EQUL, EX_MEM,
       EX_WE, Go, ID_EX, IF_ID, IR1, IR2, IR3, JMP, JMPp, JR, JRr, LOAD_USE, MEM_WE, not_1_out, not_2_out,
       not_3_out, not_4_out, not_5_out, not_6_out, or_1_out, or_2_out, RST, sel, select, SignedExt, SRAV,
       sys, W1, W2, W3, WE, \分支 ;
  wire [1:0] R1_CON, R1_con_t, R1_con_t_t, R2_CON, R2_con_t;
  wire [2:0] id_ex_1_mem_2, MEM;
  wire [3:0] mem_wb_1_wb_2;
  wire [4:0] EX, ex_mem_1_mem_2, ex_mem_1_wb_2, EX_WR, id_ex_1_ex_2, id_ex_1_wb_2, ID_R1, ID_R2,
       mem_wb_1_ir_2_2, mem_wb_1_ir_2_3, MEM_WR, multiplexer_4_out, multiplexer_10_out, multiplexer_11_out,
       multiplexer_15_out, multiplexer_18_out, shamt, WB, WR;
  wire [5:0] ALU_OP, FUNC, id_ex_1_ir_2, OP;
  wire [11:0] EX_PC, ID_PC, IF_PC, MEM_PC, WB_PC;
  wire [15:0] \LoadUse次数 , multiplexer_19_out, \总周期数 , \插入气泡数 , \无条件分支数 , \条件分支成功数 ;
  wire [15:6] if_id_1_ir_2;
  wire [25:11] id_ex_1_ir_2_2;
  wire [25:16] if_id_1_ir_2_2;
  wire [31:0] adder_1_out, adder_4_out, alu_1, alu_2, alu_5, alu_a, alu_b, bit_extender_1_out,
       bit_extender_2_out, bit_extender_3_out, ex_mem_1_a_2, ex_mem_1_b_2, ex_mem_1_ir_2, ex_mem_1_pc_2,
       id_ex_1_pc_2, id_ex_1_shmat_2, if_id_1_pc_2, im, JMPA, LedData, mem_wb_1_alu_2, mem_wb_1_ir_2,
       mem_wb_1_md_2, mem_wb_1_pc_2, mips_alu_1_result, mips_regifile_1_r1, mips_regifile_1_r2,
       multiplexer_1_out, multiplexer_2_out, multiplexer_3_out, multiplexer_8_out, multiplexer_17_out,
       multiplexer_20_out, pc_4, PC_q, R1, R2, ram_1_data, RD, rom_1_data, shifter_1_out, \分支a ;

  Button \u_总复位  (.out(RST));
  Button _1 (.out(IR1));
  Button _2 (.out(IR2));
  Button _3 (.out(IR3));
  Button \u_继续运行  (.out(Go));
  LED led_1 (.in(W1));
  LED led_2 (.in(W2));
  LED led_3 (.in(W3));
  Multiplexer #(.width(32), .enable("false")) multiplexer_1 (
    .in0(adder_1_out), .in1(\分支a ), .out(multiplexer_1_out), .sel(\分支 ));
  Hex_Digit_Display hex_digit_display_1 (.value(LedData[31:28]));  // open: dp
  Hex_Digit_Display hex_digit_display_2 (.value(LedData[23:20]));  // open: dp
  Hex_Digit_Display hex_digit_display_3 (.value(LedData[27:24]));  // open: dp
  Counter #(.width(16), .max('hffff)) counter_1 (
    .count(sel), .Q(\总周期数 ), .clk(CLK), .clr(RST));  // open: load, D, carry
  Multiplexer #(.width(32), .enable("false")) multiplexer_2 (
    .in0(multiplexer_1_out), .in1(\分支a ), .out(multiplexer_2_out), .sel(BGEZ));
  Hex_Digit_Display hex_digit_display_4 (.value(LedData[15:12]));  // open: dp
  Hex_Digit_Display hex_digit_display_5 (.value(LedData[19:16]));  // open: dp
  Multiplexer #(.width(32), .enable("false")) multiplexer_3 (
    .in0(multiplexer_2_out), .in1(JMPA), .out(multiplexer_3_out), .sel(JMPp));
  and and_1 (and_1_out, sel, not_1_out);
  not not_1 (not_1_out, LOAD_USE);
  Hex_Digit_Display hex_digit_display_6 (.value(LedData[11:8]));  // open: dp
  Hex_Digit_Display hex_digit_display_7 (.value(LedData[7:4]));  // open: dp
  Clock clock_1 (.out(CLK));
  Register #(.width(32)) PC (.D(multiplexer_3_out), .en(and_1_out), .Q(PC_q), .clk(CLK), .clr(RST));
  Hex_Digit_Display hex_digit_display_8 (.value(LedData[3:0]));  // open: dp
  and and_2 (and_2_out, \分支 , not_2_out);
  not not_2 (not_2_out, JMPp);
  foward foward_1 (
    .OP(OP), .EX_WriteReg_num(EX_WR), .EX_RegWrite(EX_WE), .R1_con(R1_CON), .OP_alu(ALU_OP),
    .MEM_WriteReg_num(MEM_WR), .MEM_RegWrite(MEM_WE), .load_use(LOAD_USE), .Func(FUNC), .ID_R1_num(ID_R1),
    .ID_R2_num(ID_R2), .R2_con(R2_CON));
  Adder #(.width(32)) adder_1 (.a(PC_q), .b(32'h4), .out(adder_1_out));  // open: cin, cout
  // Probe on \总周期数 
  // Probe on \无条件分支数 
  // Probe on \条件分支成功数 
  // Probe on \插入气泡数 
  // Probe on \LoadUse次数 
  Counter #(.width(16), .max('hffff)) counter_2 (
    .count(and_2_out), .Q(\条件分支成功数 ), .clk(CLK), .clr(RST));  // open: load, D, carry
  ROM #(.addrWidth(10), .dataWidth(32)) rom_1 (.addr(PC_q[11:2]), .data(rom_1_data));  // open: sel
  // Probe on IF_PC
  IF_ID if_id_1 (
    .IR(rom_1_data), .PC(PC_q), .\传输状态In_表明当前传输数据有效 (1'b1), .CLK(CLK),
    .IR_2({OP, if_id_1_ir_2_2, if_id_1_ir_2, FUNC}), .PC_2(if_id_1_pc_2), .\传输状态Out_表明当前传输数据有效 (IF_ID),
    .\同步清零_气泡_高电平有效 (\分支 ), .\使能端_低电平有效_stall_高电平有效 (or_1_out));  // open: miss, miss_2, dataout, dataout_2
  or or_1 (or_1_out, not_3_out, LOAD_USE);
  // Probe on ID_PC
  assign bit_extender_1_out = {{16{if_id_1_ir_2[15]}}, {if_id_1_ir_2, FUNC}};  // Bit_Extender bit_extender_1
  assign bit_extender_2_out = {{16{1'b0}}, {if_id_1_ir_2, FUNC}};  // Bit_Extender bit_extender_2
  // Probe on MEM_PC
  // Probe on EX_PC
  Multiplexer #(.width(5), .enable("false")) multiplexer_4 (
    .in0(if_id_1_ir_2_2[25:21]), .in1({5{1'b1}}), .out(multiplexer_4_out), .sel(JR));
  Multiplexer #(.width(32), .enable("false")) multiplexer_5 (
    .in0(bit_extender_1_out), .in1(bit_extender_2_out), .out(im), .sel(SignedExt));
  not not_3 (not_3_out, sel);
  or or_2 (or_2_out, LOAD_USE, \分支 );
  // Probe on WB_PC
  Counter #(.width(16), .max('hffff)) counter_3 (
    .count(JMPp), .Q(\无条件分支数 ), .clk(CLK), .clr(RST));  // open: load, D, carry
  \硬布线控制器  \u_硬布线控制器_1  (
    .Func(FUNC), .OP(OP), .ALU_OP(EX[3:0]), .MemToReg(WB[0]), .MemWrite(MEM[2]), .ALU_SRC(EX[4]),
    .RegWrite(WB[1]), .SysCALL(WB[4]), .SignedExt(SignedExt), .RegDst(WB[3]), .JR(JR), .JMP(JMP),
    .Beq(MEM[0]), .JAL(WB[2]), .Bne(MEM[1]));
  Multiplexer #(.width(5), .enable("false")) multiplexer_6 (
    .in0(multiplexer_4_out), .in1(5'b00010), .out(ID_R1), .sel(WB[4]));
  Multiplexer #(.width(5), .enable("false")) multiplexer_7 (
    .in0(if_id_1_ir_2_2[20:16]), .in1(5'b00100), .out(ID_R2), .sel(WB[4]));
  MIPS_Regifile mips_regifile_1 (
    .Din(RD), .Clk(CLK), .R1(mips_regifile_1_r1), .R2(mips_regifile_1_r2), .WE(WE), .W_num(WR),
    .R1_num(ID_R1), .R2_num(ID_R2));
  Counter #(.width(16), .max('hffff)) counter_4 (
    .count(LOAD_USE), .Q(\LoadUse次数 ), .clk(CLK), .clr(RST));  // open: load, D, carry
  ID_EX id_ex_1 (
    .WB(WB), .MEM({JR, JMP, MEM}), .EX(EX), .IR({OP, if_id_1_ir_2_2, if_id_1_ir_2, FUNC}), .PC(if_id_1_pc_2),
    .A(mips_regifile_1_r1), .B(mips_regifile_1_r2), .SHMAT(im), .\传输状态In_表明当前传输数据有效 (IF_ID), .CLK(CLK),
    .WB_2({id_ex_1_wb_2[4:2], EX_WE, id_ex_1_wb_2[0]}), .MEM_2({JRr, JMPp, id_ex_1_mem_2}),
    .EX_2(id_ex_1_ex_2), .IR_2({ALU_OP, id_ex_1_ir_2_2, shamt, id_ex_1_ir_2}), .PC_2(id_ex_1_pc_2),
    .A_2(alu_1), .B_2(alu_5), .SHMAT_2(id_ex_1_shmat_2), .\传输状态Out_表明当前传输数据有效 (ID_EX),
    .\同步清零_气泡_高电平有效 (or_2_out), .\使能端_低电平有效_stall_高电平有效 (not_3_out), .R1(R1_CON), .R1_2(R1_con_t),
    .R2(R2_CON), .R2_2(R2_con_t));  // open: miss, miss_2, dataout, dataout_2
  Multiplexer #(.width(32), .enable("false")) multiplexer_8 (
    .in0(alu_b), .in1(id_ex_1_shmat_2), .out(multiplexer_8_out), .sel(id_ex_1_ex_2[4]));
  Shifter #(.width(32)) shifter_1 (.in(id_ex_1_shmat_2), .\dist (5'b00010), .out(shifter_1_out));
  Comparator #(.width(32)) comparator_1 (.a(alu_1), .b(32'h1), .lt(comparator_1_lt));  // open: gt, eq
  Comparator #(.width(6)) comparator_2 (.a(ALU_OP), .b(6'b000001), .eq(comparator_2_eq));  // open: gt, lt
  not not_4 (not_4_out, EQUL);
  Multiplexer #(.width(32), .enable("false")) multiplexer_9 (
    .in0({pc_4[31:28], id_ex_1_ir_2_2, shamt, id_ex_1_ir_2, 2'b00}), .in1(alu_1), .out(JMPA), .sel(JRr));
  MIPS_ALU mips_alu_1 (
    .X(alu_a), .Y(multiplexer_8_out), .AluOP(id_ex_1_ex_2[3:0]), .Equal(EQUL), .Result(mips_alu_1_result),
    .shamt(multiplexer_10_out));  // open: Result_2
  Multiplexer #(.width(5), .enable("false")) multiplexer_10 (
    .in0(shamt), .in1(alu_1[4:0]), .out(multiplexer_10_out), .sel(SRAV));
  Adder #(.width(32)) adder_2 (.a(shifter_1_out), .b(pc_4), .out(\分支a ));  // open: cin, cout
  Comparator #(.width(6)) comparator_3 (.a(ALU_OP), .b({6{1'b0}}), .eq(comparator_3_eq));  // open: gt, lt
  and and_3 (SRAV, comparator_3_eq, comparator_4_eq);
  Comparator #(.width(6)) comparator_4 (.a(id_ex_1_ir_2), .b(6'b000111), .eq(comparator_4_eq));  // open: gt, lt
  and and_4 (BGEZ, ~comparator_1_lt, comparator_2_eq);  // AND_Gate
  and and_5 (and_5_out, id_ex_1_mem_2[0], EQUL);
  and and_6 (and_6_out, id_ex_1_mem_2[1], not_4_out);
  or or_3 (\分支 , JMPp, and_5_out, BGEZ, and_6_out);
  Multiplexer #(.width(5), .enable("false")) multiplexer_11 (
    .in0(id_ex_1_ir_2_2[20:16]), .in1(id_ex_1_ir_2_2[15:11]), .out(multiplexer_11_out), .sel(id_ex_1_wb_2[3]));
  Multiplexer #(.width(5), .enable("false")) multiplexer_12 (
    .in0(multiplexer_11_out), .in1({5{1'b1}}), .out(EX_WR), .sel(id_ex_1_wb_2[2]));
  Adder #(.width(32)) adder_3 (.a(32'h4), .b(id_ex_1_pc_2), .out(pc_4));  // open: cin, cout
  EX_MEM ex_mem_1 (
    .WB({id_ex_1_wb_2[4:2], EX_WE, id_ex_1_wb_2[0]}), .MEM({JRr, JMPp, id_ex_1_mem_2}),
    .IR({ALU_OP, id_ex_1_ir_2_2, shamt, id_ex_1_ir_2}), .PC(id_ex_1_pc_2), .B(alu_b),
    .ALU(mips_alu_1_result), .\传输状态In_表明当前传输数据有效 (ID_EX), .CLK(CLK),
    .WB_2({ex_mem_1_wb_2[4:2], MEM_WE, ex_mem_1_wb_2[0]}), .MEM_2(ex_mem_1_mem_2), .IR_2(ex_mem_1_ir_2),
    .PC_2(ex_mem_1_pc_2), .B_2(ex_mem_1_b_2), .ALU_2(alu_2), .\传输状态Out_表明当前传输数据有效 (EX_MEM),
    .\使能端_低电平有效_stall_高电平有效 (not_3_out), .A(alu_a), .A_2(ex_mem_1_a_2));  // open: 同步清零_气泡_高电平有效
  Multiplexer #(.select(2), .width(32), .enable("false")) multiplexer_13 (
    .in0(alu_1), .in1(alu_2), .in2(RD), .in3(alu_2), .out(alu_a), .sel(R1_con_t_t));
  Multiplexer #(.select(2), .width(32), .enable("false")) multiplexer_14 (
    .in0(alu_5), .in1(alu_2), .in2(RD), .in3(alu_2), .out(alu_b), .sel(R2_con_t));
  Comparator #(.width(32)) comparator_5 (.a(R1), .b(32'h32), .eq(comparator_5_eq));  // open: gt, lt
  Multiplexer #(.width(5), .enable("false")) multiplexer_15 (
    .in0(ex_mem_1_ir_2[20:16]), .in1(ex_mem_1_ir_2[15:11]), .out(multiplexer_15_out), .sel(ex_mem_1_wb_2[3]));
  and and_7 (and_7_out, comparator_5_eq, sys);
  not not_5 (not_5_out, comparator_5_eq);
  Multiplexer #(.width(5), .enable("false")) multiplexer_16 (
    .in0(multiplexer_15_out), .in1({5{1'b1}}), .out(MEM_WR), .sel(ex_mem_1_wb_2[2]));
  not not_6 (not_6_out, and_7_out);
  and and_8 (and_8_out, not_5_out, sys);
  RAM #(.addrWidth(10), .dataWidth(32), .bus("separate")) ram_1 (
    .addr(alu_2[11:2]), .din(ex_mem_1_b_2), .data(ram_1_data), .str(ex_mem_1_mem_2[2]), .sel(sel), .clk(CLK),
    .clr(RST));  // open: ld
  or or_4 (sel, Go, not_6_out);
  Register #(.width(32)) register_1 (.D(R2), .en(and_8_out), .Q(LedData), .clk(CLK), .clr(RST));
  MEM_WB mem_wb_1 (
    .WB({ex_mem_1_wb_2[4:2], MEM_WE, ex_mem_1_wb_2[0]}), .IR(ex_mem_1_ir_2), .PC(ex_mem_1_pc_2), .ALU(alu_2),
    .MD(ram_1_data), .\传输状态In_表明当前传输数据有效 (EX_MEM), .CLK(CLK),
    .WB_2({sys, mem_wb_1_wb_2[3:2], WE, mem_wb_1_wb_2[0]}),
    .IR_2({mem_wb_1_ir_2[31:21], mem_wb_1_ir_2_3, mem_wb_1_ir_2_2, mem_wb_1_ir_2[10:0]}),
    .PC_2(mem_wb_1_pc_2), .ALU_2({mem_wb_1_alu_2[31:2], select, mem_wb_1_alu_2[0]}), .MD_2(mem_wb_1_md_2),
    .\使能端_低电平有效_stall_高电平有效 (not_3_out), .A(ex_mem_1_a_2), .A_2(R1), .B(ex_mem_1_b_2), .B_2(R2));  // open: 传输状态Out_表明当前传输数据有效, 同步清零_气泡_高电平有效
  Adder #(.width(32)) adder_4 (.a(mem_wb_1_pc_2), .b(32'h4), .out(adder_4_out));  // open: cin, cout
  Multiplexer #(.width(32)) multiplexer_17 (
    .in0({mem_wb_1_alu_2[31:2], select, mem_wb_1_alu_2[0]}), .in1(mem_wb_1_md_2), .out(multiplexer_17_out),
    .sel(mem_wb_1_wb_2[0]));  // open: en
  Multiplexer #(.width(5), .enable("false")) multiplexer_18 (
    .in0(mem_wb_1_ir_2_3), .in1(mem_wb_1_ir_2_2), .out(multiplexer_18_out), .sel(mem_wb_1_wb_2[3]));
  Multiplexer #(.width(16), .enable("false")) multiplexer_19 (
    .in0(multiplexer_17_out[15:0]), .in1(multiplexer_17_out[31:16]), .out(multiplexer_19_out), .sel(select));
  Comparator #(.width(6)) comparator_6 (.a(mem_wb_1_ir_2[31:26]), .b(6'b100001), .eq(comparator_6_eq));  // open: gt, lt
  Multiplexer #(.width(32), .enable("false")) multiplexer_20 (
    .in0(multiplexer_17_out), .in1(bit_extender_3_out), .out(multiplexer_20_out), .sel(comparator_6_eq));
  assign bit_extender_3_out = {{16{multiplexer_19_out[15]}}, multiplexer_19_out};  // Bit_Extender bit_extender_3
  Multiplexer #(.width(5), .enable("false")) multiplexer_21 (
    .in0(multiplexer_18_out), .in1({5{1'b1}}), .out(WR), .sel(mem_wb_1_wb_2[2]));
  Multiplexer #(.width(32)) multiplexer_22 (
    .in0(multiplexer_20_out), .in1(adder_4_out), .out(RD), .sel(mem_wb_1_wb_2[2]));  // open: en

  // Other names for the same wires on the sheet: MEM[4:3] = {JR, JMP}; R1_EX[31:0] = alu_1

  // Notes on the sheet:
  //   中断源
  //   中断等待指示
  //   数码管输出
  //   contents of rom_1 (hex, n*v repeats v):
  //   20110001 8100005 20110001 20120002 20130003 8100009 20110001 20120002 20130003 810000d 20110001
  //   20120002 20130003 8100011 20110001 20120002 20130003 c1000f7 20100001 20110001 118fc0 112020
  //   20020022 c 118882 12200001 8100015 112020 20020022 c 20110001 118880 112020 20020022 c 12200001
  //   810001f 20110001 118fc0 112020 20020022 c 1188c3 112020 20020022 c 118903 112020 20020022 c 118903
  //   112020 20020022 c 118903 112020 20020022 c 118903 112020 20020022 c 118903 112020 20020022 c 118903
  //   112020 20020022 c 118903 112020 20020022 c 20100001 109fc0 139fc3 8021 2012000c 24160003 26100001
  //   3210000f 20080008 20090001 139900 2709825 132020 20020022 c 1094022 1500fff9 22100001 2018000f
  //   2188024 108700 20080008 20090001 139902 2709825 132021 20020022 c 1094022 1500fff9 108702 2c9b022
  //   12c00001 8100050 4020 1084027 84400 3508ffff 82021 20020022 c 2010ffff 20110000 ae300000 22100001
  //   22310004 ae300000 22100001 22310004 ae300000 22100001 22310004 ae300000 22100001 22310004 ae300000
  //   22100001 22310004 ae300000 22100001 22310004 ae300000 22100001 22310004 ae300000 22100001 22310004
  //   ae300000 22100001 22310004 ae300000 22100001 22310004 ae300000 22100001 22310004 ae300000 22100001
  //   22310004 ae300000 22100001 22310004 ae300000 22100001 22310004 ae300000 22100001 22310004 ae300000
  //   22100001 22310004 22100001 8020 2011003c 8e130000 8e340000 274402a 11000002 ae330000 ae140000
  //   2231fffc 1611fff8 102020 20020022 c 22100004 2011003c 1611fff2 20020032 c 20090000 200b0010 34118483
  //   20120404 118c00 129400 36318281 22520404 ad310000 2328820 21290004 216bffff 1560fffb 200b0020
  //   20090000 85310000 112020 20020022 c 21290002 216bffff 1560fff9 20020032 c 2011000f 112020 20020022 c
  //   2231ffff 621fffb 20020032 c 2008ffff 20117777 112020 20020022 c 200b0010 2288826 112020 20020022 c
  //   216bffff 1560fffa 20020032 c 20080001 20090003 20110876 118d00 112020 20020022 c 200b0008 1118807
  //   1318807 112020 20020022 c 216bffff 1560fff9 20020032 c 20100000 22100001 102020 20020022 c 22100002
  //   102020 20020022 c 22100003 102020 20020022 c 22100004 102020 20020022 c 22100005 102020 20020022 c
  //   22100006 102020 20020022 c 22100007 102020 20020022 c 22100008 102020 20020022 20020022 c 3e00008
  //   指令字
  //   流水调试日志用
  //   JMP
  //   JR
  //   OP
  //   OP
  //   Func
  //   Func
  //   rs
  //   rt
  //   rd
  //   Bne
  //   MemToReg
  //   MemWrite
  //   AluOP
  //   AluSrcB
  //   RegWrite
  //   JAL
  //   RegDst
  //   Func
  //   rt
  //   rt
  //   rt
  //   rd
endmodule

module \流水  (
  input  [21:0] Din22,
  input  \传输状态In_表明当前传输数据有效 ,
  input  CLK,
  input  \同步清零_气泡_高电平有效 ,
  input  \使能端_低电平有效_stall_高电平有效 ,
  output [21:0] Dout22,
  output \传输状态Out_表明当前传输数据有效 
);

  wire multiplexer_2_out, not_1_out;
  wire [21:0] multiplexer_1_out;

  Multiplexer #(.width(22), .enable("false")) multiplexer_1 (
    .in0(Din22), .in1({22{1'b0}}), .out(multiplexer_1_out), .sel(\同步清零_气泡_高电平有效 ));
  Multiplexer #(.enable("false")) multiplexer_2 (
    .in0(\传输状态In_表明当前传输数据有效 ), .in1(1'b0), .out(multiplexer_2_out), .sel(\同步清零_气泡_高电平有效 ));
  Register #(.width(22)) register_1 (.D(multiplexer_1_out), .en(not_1_out), .Q(Dout22), .clk(CLK));  // open: clr
  Register #(.width(1)) register_2 (
    .D(multiplexer_2_out), .en(not_1_out), .Q(\传输状态Out_表明当前传输数据有效 ), .clk(CLK));  // open: clr
  not not_1 (not_1_out, \使能端_低电平有效_stall_高电平有效 );

  // Notes on the sheet:
  //   同步清零_气泡_高电平有效: pull=down
  //   使能端_低电平有效_stall_高电平有效: pull=down
endmodule

module foward (
  input  [5:0] OP,
  input  [4:0] EX_WriteReg_num,
  input  EX_RegWrite,
  input  [5:0] OP_alu,
  input  [4:0] MEM_WriteReg_num,
  input  MEM_RegWrite,
  input  [5:0] Func,
  input  [4:0] ID_R1_num,
  input  [4:0] ID_R2_num,
  output [1:0] R1_con,
  output load_use,
  output [1:0] R2_con
);

  wire and_5_out, and_6_out, comparator_1_eq, comparator_2_eq, comparator_3_eq, comparator_4_eq,
       comparator_5_eq, comparator_6_eq, comparator_7_eq, \源寄存器使用情况_1_r1_used , \源寄存器使用情况_1_r2_used ;

  \源寄存器使用情况  \u_源寄存器使用情况_1  (
    .OP0(OP[0]), .OP1(OP[1]), .OP2(OP[2]), .OP3(OP[3]), .OP4(OP[4]), .OP5(OP[5]), .F0(Func[0]), .F1(Func[1]),
    .F2(Func[2]), .F3(Func[3]), .F4(Func[4]), .F5(Func[5]), .R1_Used(\源寄存器使用情况_1_r1_used ),
    .R2_Used(\源寄存器使用情况_1_r2_used ));
  Comparator #(.width(5)) comparator_1 (.a(EX_WriteReg_num), .b(ID_R2_num), .eq(comparator_1_eq));  // open: gt, lt
  Comparator #(.width(5)) comparator_2 (.a(EX_WriteReg_num), .b(ID_R1_num), .eq(comparator_2_eq));  // open: gt, lt
  Comparator #(.width(5)) comparator_3 (.a(MEM_WriteReg_num), .b(ID_R1_num), .eq(comparator_3_eq));  // open: gt, lt
  Comparator #(.width(5)) comparator_4 (.a(MEM_WriteReg_num), .b(ID_R2_num), .eq(comparator_4_eq));  // open: gt, lt
  Comparator #(.width(5)) comparator_5 (.a({5{1'b0}}), .b(ID_R2_num), .eq(comparator_5_eq));  // open: gt, lt
  Comparator #(.width(5)) comparator_6 (.a({5{1'b0}}), .b(ID_R1_num), .eq(comparator_6_eq));  // open: gt, lt
  and and_1 (R1_con[0], ~comparator_6_eq, \源寄存器使用情况_1_r1_used , comparator_2_eq, EX_RegWrite);  // AND_Gate
  and and_2 (R1_con[1], ~comparator_6_eq, \源寄存器使用情况_1_r1_used , comparator_3_eq, MEM_RegWrite);  // AND_Gate
  and and_3 (R2_con[0], ~comparator_5_eq, \源寄存器使用情况_1_r2_used , EX_RegWrite, comparator_1_eq);  // AND_Gate
  and and_4 (R2_con[1], ~comparator_5_eq, \源寄存器使用情况_1_r2_used , MEM_RegWrite, comparator_4_eq);  // AND_Gate
  Comparator #(.width(6)) comparator_7 (.a(OP_alu), .b(6'b100011), .eq(comparator_7_eq));  // open: gt, lt
  Comparator #(.width(6)) comparator_8 (.a(OP_alu), .b(6'b100001));  // open: gt, eq, lt
  and and_5 (and_5_out, R1_con[0], comparator_7_eq);
  or or_1 (load_use, and_5_out, and_6_out);
  and and_6 (and_6_out, comparator_7_eq, R2_con[0]);

  // Other names for the same wires on the sheet: OP_CODE[5:0] = OP; OP_t[5:0] = OP_alu; R1[1:0] = R1_con;
  //   R2[1:0] = R2_con
endmodule

module \单级中断  (
);

  wire \_1号中断 , \_1号中断等待指示 , \_2号中断 , \_2号中断等待指示 , \_3号中断 , \_3号中断等待指示 , and_1_out, and_2_out, and_3_out,
       and_4_out, and_5_out, and_7_out, and_8_out, and_9_out, and_10_out, block, CLK, comparator_1_lt,
       comparator_2_eq, comparator_3_eq, comparator_4_gt, comparator_5_eq, comparator_6_eq, comparator_7_eq,
       comparator_8_eq, comparator_9_eq, ERET, Go, JAL, JMP, JR, mips_alu_1_equal, not_1_out, not_2_out,
       not_3_out, not_4_out, RegDst, RST, sel, select, SignedExt, SRAV, sys, \中断信号 , \中断信号_1_out_5 ,
       \中断信号_2_out_5 , \中断信号_3_out_5 , \硬布线控制器_1_alu_src , \硬布线控制器_1_beq , \硬布线控制器_1_bne ,
       \硬布线控制器_1_memtoreg , \硬布线控制器_1_memwrite , \硬布线控制器_1_regwrite ;
  wire [0:0] or_1_out;
  wire [1:0] NUM, priority_encoder_1_out, \中断级别 ;
  wire [3:0] PC31_28, \硬布线控制器_1_alu_op ;
  wire [4:0] multiplexer_7_out, multiplexer_8_out, multiplexer_9_out, multiplexer_10_out, multiplexer_11_out,
       multiplexer_14_out;
  wire [5:0] FUNC, OP;
  wire [15:0] multiplexer_18_out, \总周期数 , \无条件分支数 , \条件分支成功数 ;
  wire [25:6] Jaddress;
  wire [27:0] PC_q;
  wire [31:0] adder_1_out, adder_2_out, bit_extender_1_out, bit_extender_2_out, bit_extender_3_out, IR_PC,
       JLast, LedData, mips_alu_1_result, multiplexer_1_out, multiplexer_2_out, multiplexer_3_out,
       multiplexer_5_out, multiplexer_12_out, multiplexer_13_out, multiplexer_15_out, multiplexer_16_out,
       multiplexer_17_out, multiplexer_19_out, PC, PC_0_q, PC_1_q, PC_2_q, PC_STORE, R1, R2, ram_1_data,
       shifter_1_out;

  Button \u_总复位  (.out(RST));
  Button u_Go (.out(Go));
  Clock clock_1 (.out(CLK));
  Comparator #(.width(32)) comparator_1 (.a(R1), .b({32{1'b0}}), .lt(comparator_1_lt));  // open: gt, eq
  Comparator #(.width(6)) comparator_2 (.a(OP), .b(6'b000001), .eq(comparator_2_eq));  // open: gt, lt
  Hex_Digit_Display hex_digit_display_1 (.value(LedData[27:24]));  // open: dp
  Hex_Digit_Display hex_digit_display_2 (.value(LedData[31:28]));  // open: dp
  Multiplexer #(.width(32), .enable("false")) multiplexer_1 (
    .in0(adder_1_out), .in1(adder_2_out), .out(multiplexer_1_out), .sel(and_1_out));
  and and_1 (and_1_out, ~comparator_1_lt, comparator_2_eq);  // AND_Gate
  Hex_Digit_Display hex_digit_display_3 (.value(LedData[23:20]));  // open: dp
  Hex_Digit_Display hex_digit_display_4 (.value(LedData[19:16]));  // open: dp
  Multiplexer #(.select(2), .width(32), .enable("false")) multiplexer_2 (
    .in0(multiplexer_1_out), .in1(adder_2_out), .in2(JLast), .out(multiplexer_2_out), .sel({JMP, or_1_out[0]}));  // open: in3
  Register #(.width(32)) PC_0 (.D(PC), .Q(PC_0_q), .clk(and_2_out));  // open: en, clr
  and and_2 (and_2_out, \中断信号 , \_1号中断 );
  Register #(.width(32)) PC_1 (.D(PC), .Q(PC_1_q), .clk(and_3_out));  // open: en, clr
  and and_3 (and_3_out, \中断信号 , \_2号中断 );
  Register #(.width(32)) PC_2 (.D(PC), .Q(PC_2_q), .clk(and_4_out));  // open: en, clr
  and and_4 (and_4_out, \中断信号 , \_3号中断 );
  Hex_Digit_Display hex_digit_display_5 (.value(LedData[11:8]));  // open: dp
  Hex_Digit_Display hex_digit_display_6 (.value(LedData[15:12]));  // open: dp
  Multiplexer #(.width(32), .enable("false")) multiplexer_3 (
    .in0(multiplexer_2_out), .in1(IR_PC), .out(multiplexer_3_out), .sel(\中断信号 ));
  Hex_Digit_Display hex_digit_display_7 (.value(LedData[7:4]));  // open: dp
  Hex_Digit_Display hex_digit_display_8 (.value(LedData[3:0]));  // open: dp
  Multiplexer #(.width(32), .enable("false")) multiplexer_4 (
    .in0(multiplexer_3_out), .in1(PC_STORE), .out(PC), .sel(ERET));
  Register #(.width(32)) u_PC_STORE (.D(multiplexer_5_out), .Q(PC_STORE), .clk(ERET));  // open: en, clr
  Multiplexer #(.select(2), .width(32), .enable("false")) multiplexer_5 (
    .in1(PC_0_q), .in2(PC_1_q), .in3(PC_2_q), .out(multiplexer_5_out), .sel(NUM));  // open: in0
  \中断信号  \u_中断信号_1  (.in_2(\_1号中断 ), .out_6(\_1号中断等待指示 ), .in_3(ERET), .in_1(CLK), .out_5(\中断信号_1_out_5 ), .in_4(RST));
  \中断信号  \u_中断信号_2  (.in_2(\_2号中断 ), .out_6(\_2号中断等待指示 ), .in_3(ERET), .in_1(CLK), .out_5(\中断信号_2_out_5 ), .in_4(RST));
  \中断信号  \u_中断信号_3  (.in_2(\_3号中断 ), .out_6(\_3号中断等待指示 ), .in_3(ERET), .in_1(CLK), .out_5(\中断信号_3_out_5 ), .in_4(RST));
  Register #(.width(32)) u_PC (.D(PC), .en(sel), .Q({PC31_28, PC_q}), .clk(CLK), .clr(RST));
  and and_5 (and_5_out, ~\中断信号_1_out_5 , ~\中断信号_2_out_5 , ~\中断信号_3_out_5 );  // AND_Gate
  // Probe on \总周期数 
  // Probe on \无条件分支数 
  // Probe on \条件分支成功数 
  Adder #(.width(32)) adder_1 (.a({PC31_28, PC_q}), .b(32'h4), .out(adder_1_out));  // open: cin, cout
  Register #(.width(1)) register_1 (.D(and_5_out), .Q(block), .clk(CLK));  // open: en, clr
  Button _1 (.out(\_1号中断 ));
  Button _2 (.out(\_2号中断 ));
  Button _3 (.out(\_3号中断 ));
  ROM #(.addrWidth(10), .dataWidth(32)) rom_1 (.addr(PC_q[11:2]), .data({OP, Jaddress, FUNC}));  // open: sel
  Multiplexer #(.width(32), .enable("false")) multiplexer_6 (
    .in0({PC31_28, Jaddress, FUNC, 2'b00}), .in1(R1), .out(JLast), .sel(JR));
  Multiplexer #(.width(5), .enable("false")) multiplexer_7 (
    .in0(Jaddress[25:21]), .in1({5{1'b1}}), .out(multiplexer_7_out), .sel(JR));
  assign bit_extender_1_out = {{16{Jaddress[15]}}, {Jaddress[15:6], FUNC}};  // Bit_Extender bit_extender_1
  assign bit_extender_2_out = {{16{1'b0}}, {Jaddress[15:6], FUNC}};  // Bit_Extender bit_extender_2
  LED _1_2 (.in(\_1号中断等待指示 ));
  LED _2_2 (.in(\_2号中断等待指示 ));
  LED _3_2 (.in(\_3号中断等待指示 ));
  \硬布线控制器  \u_硬布线控制器_1  (
    .Func(FUNC), .OP(OP), .ALU_OP(\硬布线控制器_1_alu_op ), .MemToReg(\硬布线控制器_1_memtoreg ),
    .MemWrite(\硬布线控制器_1_memwrite ), .ALU_SRC(\硬布线控制器_1_alu_src ), .RegWrite(\硬布线控制器_1_regwrite ),
    .SysCALL(sys), .SignedExt(SignedExt), .RegDst(RegDst), .JR(JR), .JMP(JMP), .Beq(\硬布线控制器_1_beq ),
    .JAL(JAL), .Bne(\硬布线控制器_1_bne ));
  Multiplexer #(.width(5), .enable("false")) multiplexer_8 (
    .in0(multiplexer_7_out), .in1(5'b00010), .out(multiplexer_8_out), .sel(sys));
  Multiplexer #(.width(5), .enable("false")) multiplexer_9 (
    .in0(Jaddress[20:16]), .in1(5'b00100), .out(multiplexer_9_out), .sel(sys));
  Multiplexer #(.width(5), .enable("false")) multiplexer_10 (
    .in0(Jaddress[20:16]), .in1(Jaddress[15:11]), .out(multiplexer_10_out), .sel(RegDst));
  Multiplexer #(.width(5), .enable("false")) multiplexer_11 (
    .in0(multiplexer_10_out), .in1({5{1'b1}}), .out(multiplexer_11_out), .sel(JAL));
  Multiplexer #(.width(32), .enable("false")) multiplexer_12 (
    .in0(bit_extender_1_out), .in1(bit_extender_2_out), .out(multiplexer_12_out), .sel(SignedExt));
  Counter #(.width(16), .max('hffff)) counter_1 (
    .count(sel), .Q(\总周期数 ), .clk(CLK), .clr(RST));  // open: load, D, carry
  Priority_Encoder #(.select(2)) priority_encoder_1 (
    .in0(1'b1), .in1(\中断信号_1_out_5 ), .in2(\中断信号_2_out_5 ), .in3(\中断信号_3_out_5 ), .out(priority_encoder_1_out));  // open: gs, en_out, en_in
  MIPS_Regifile mips_regifile_1 (
    .Din(multiplexer_16_out), .Clk(CLK), .R1(R1), .R2(R2), .WE(\硬布线控制器_1_regwrite ),
    .W_num(multiplexer_11_out), .R1_num(multiplexer_8_out), .R2_num(multiplexer_9_out));
  // Probe on \中断级别 
  Multiplexer #(.width(32), .enable("false")) multiplexer_13 (
    .in0(R2), .in1(multiplexer_12_out), .out(multiplexer_13_out), .sel(\硬布线控制器_1_alu_src ));
  Shifter #(.width(32)) shifter_1 (.in(multiplexer_12_out), .\dist (5'b00010), .out(shifter_1_out));
  MIPS_ALU mips_alu_1 (
    .X(R1), .Y(multiplexer_13_out), .AluOP(\硬布线控制器_1_alu_op ), .Equal(mips_alu_1_equal),
    .Result({mips_alu_1_result[31:2], select, mips_alu_1_result[0]}), .shamt(multiplexer_14_out));  // open: Result_2
  Multiplexer #(.width(5), .enable("false")) multiplexer_14 (
    .in0(Jaddress[10:6]), .in1(R1[4:0]), .out(multiplexer_14_out), .sel(SRAV));
  Comparator #(.width(32)) comparator_3 (.a(R1), .b(32'h32), .eq(comparator_3_eq));  // open: gt, lt
  and and_6 (\中断信号 , block, comparator_4_gt);
  Comparator #(.width(2), .mode("unsigned")) comparator_4 (
    .a(priority_encoder_1_out), .b(2'b00), .gt(comparator_4_gt));  // open: eq, lt
  Register #(.width(2)) register_2 (.D(priority_encoder_1_out), .Q(NUM), .clk(\中断信号 ));  // open: en, clr
  and and_7 (and_7_out, \硬布线控制器_1_beq , mips_alu_1_equal);
  and and_8 (and_8_out, \硬布线控制器_1_bne , not_1_out);
  not not_1 (not_1_out, mips_alu_1_equal);
  Adder #(.width(32)) adder_2 (.a(shifter_1_out), .b(adder_1_out), .out(adder_2_out));  // open: cin, cout
  and and_9 (and_9_out, comparator_3_eq, sys);
  not not_2 (not_2_out, comparator_3_eq);
  and and_10 (and_10_out, not_2_out, sys);
  Register #(.width(32)) PC_IR (.D(multiplexer_15_out), .Q(IR_PC), .clk(\中断信号 ));  // open: en, clr
  Multiplexer #(.select(2), .width(32), .enable("false")) multiplexer_15 (
    .in1(32'h4), .in2(32'h1c8), .in3(32'h38c), .out(multiplexer_15_out), .sel(priority_encoder_1_out));  // open: in0
  or or_1 (or_1_out[0], and_7_out, and_8_out);
  Multiplexer #(.width(32), .enable("false")) multiplexer_16 (
    .in0(multiplexer_19_out), .in1(adder_1_out), .out(multiplexer_16_out), .sel(JAL));
  not not_3 (not_3_out, and_9_out);
  Register #(.width(32)) register_3 (.D(R2), .en(and_10_out), .Q(LedData), .clk(CLK), .clr(RST));
  Counter #(.width(16), .max('hffff)) counter_2 (
    .count(or_1_out[0]), .Q(\条件分支成功数 ), .clk(CLK), .clr(RST));  // open: load, D, carry
  RAM #(.addrWidth(10), .dataWidth(32), .bus("separate")) ram_1 (
    .addr(mips_alu_1_result[11:2]), .din(R2), .data(ram_1_data), .str(\硬布线控制器_1_memwrite ), .sel(sel),
    .clk(CLK), .ld(not_4_out), .clr(RST));
  not not_4 (not_4_out, \硬布线控制器_1_memwrite );
  or or_2 (sel, Go, not_3_out);
  Multiplexer #(.width(32), .enable("false")) multiplexer_17 (
    .in0({mips_alu_1_result[31:2], select, mips_alu_1_result[0]}), .in1(ram_1_data),
    .out(multiplexer_17_out), .sel(\硬布线控制器_1_memtoreg ));
  Multiplexer #(.width(16), .enable("false")) multiplexer_18 (
    .in0(multiplexer_17_out[15:0]), .in1(multiplexer_17_out[31:16]), .out(multiplexer_18_out), .sel(select));
  Counter #(.width(16), .max('hffff)) counter_3 (
    .count(JMP), .Q(\无条件分支数 ), .clk(CLK), .clr(RST));  // open: load, D, carry
  Comparator #(.width(6)) comparator_5 (.a(OP), .b(6'b010000), .eq(comparator_5_eq));  // open: gt, lt
  Comparator #(.width(6)) comparator_6 (.a(FUNC), .b(6'b011000), .eq(comparator_6_eq));  // open: gt, lt
  Comparator #(.width(6)) comparator_7 (.a(OP), .b({6{1'b0}}), .eq(comparator_7_eq));  // open: gt, lt
  Comparator #(.width(6)) comparator_8 (.a(FUNC), .b(6'b000111), .eq(comparator_8_eq));  // open: gt, lt
  Comparator #(.width(6)) comparator_9 (.a(OP), .b(6'b100001), .eq(comparator_9_eq));  // open: gt, lt
  Multiplexer #(.width(32), .enable("false")) multiplexer_19 (
    .in0(multiplexer_17_out), .in1(bit_extender_3_out), .out(multiplexer_19_out), .sel(comparator_9_eq));
  assign bit_extender_3_out = {{16{multiplexer_18_out[15]}}, multiplexer_18_out};  // Bit_Extender bit_extender_3
  and and_11 (ERET, comparator_5_eq, comparator_6_eq);
  and and_12 (SRAV, comparator_7_eq, comparator_8_eq);

  // Other names for the same wires on the sheet: Jaddress[5:0] = FUNC; shamt[4:0] = Jaddress[10:6]

  // Notes on the sheet:
  //   数码管输出应该用寄存器锁存，否则显示数据只能一闪而过
  //   可以通过项目增加Logisim库的方式将前几次实验完成的电路作为子电路引入到本电路中使用
  //   数码管输出
  //   总复位信号应将除ROM以外所有存储组件全部清零
  //   指令存储器
  //   指令字
  //   contents of rom_1 (hex, n*v repeats v):
  //   8000d54 23bdfffc afa10000 23bdfffc afa20000 23bdfffc afa30000 23bdfffc afa40000 23bdfffc afa50000
  //   23bdfffc afa60000 23bdfffc afa70000 23bdfffc afa80000 23bdfffc afa90000 23bdfffc afaa0000 23bdfffc
  //   afab0000 23bdfffc afac0000 23bdfffc afad0000 23bdfffc afae0000 23bdfffc afaf0000 23bdfffc afb00000
  //   23bdfffc afb10000 23bdfffc afb20000 23bdfffc afb30000 23bdfffc afb40000 23bdfffc afb50000 23bdfffc
  //   afb60000 23bdfffc afb70000 23bdfffc afb80000 23bdfffc afb90000 20160001 20140006 20150001 168020
  //   108100 2149825 132020 20020022 c 1600fffa 295a022 1680fff7 8fb90000 23bd0004 8fb80000 23bd0004
  //   8fb70000 23bd0004 8fb60000 23bd0004 8fb50000 23bd0004 8fb40000 23bd0004 8fb30000 23bd0004 8fb20000
  //   23bd0004 8fb10000 23bd0004 8fb00000 23bd0004 8faf0000 23bd0004 8fae0000 23bd0004 8fad0000 23bd0004
  //   8fac0000 23bd0004 8fab0000 23bd0004 8faa0000 23bd0004 8fa90000 23bd0004 8fa80000 23bd0004 8fa70000
  //   23bd0004 8fa60000 23bd0004 8fa50000 23bd0004 8fa40000 23bd0004 8fa30000 23bd0004 8fa20000 23bd0004
  //   8fa10000 23bd0004 42000018 23bdfffc afa10000 23bdfffc afa20000 23bdfffc afa30000 23bdfffc afa40000
  //   23bdfffc afa50000 23bdfffc afa60000 23bdfffc afa70000 23bdfffc afa80000 23bdfffc afa90000 23bdfffc
  //   afaa0000 23bdfffc afab0000 23bdfffc afac0000 23bdfffc afad0000 23bdfffc afae0000 23bdfffc afaf0000
  //   23bdfffc afb00000 23bdfffc afb10000 23bdfffc afb20000 23bdfffc afb30000 23bdfffc afb40000 23bdfffc
  //   afb50000 23bdfffc afb60000 23bdfffc afb70000 23bdfffc afb80000 23bdfffc afb90000 20160002 20140006
  //   20150001 168020 108100 2149825 132020 20020022 c 1600fffa 295a022 1680fff7 8fb90000 23bd0004
  //   8fb80000 23bd0004 8fb70000 23bd0004 8fb60000 23bd0004 8fb50000 23bd0004 8fb40000 23bd0004 8fb30000
  //   23bd0004 8fb20000 23bd0004 8fb10000 23bd0004 8fb00000 23bd0004 8faf0000 23bd0004 8fae0000 23bd0004
  //   8fad0000 23bd0004 8fac0000 23bd0004 8fab0000 23bd0004 8faa0000 23bd0004 8fa90000 23bd0004 8fa80000
  //   23bd0004 8fa70000 23bd0004 8fa60000 23bd0004 8fa50000 23bd0004 8fa40000 23bd0004 8fa30000 23bd0004
  //   8fa20000 23bd0004 8fa10000 23bd0004 42000018 23bdfffc afa10000 23bdfffc afa20000 23bdfffc afa30000
  //   23bdfffc afa40000 23bdfffc afa50000 23bdfffc afa60000 23bdfffc afa70000 23bdfffc afa80000 23bdfffc
  //   afa90000 23bdfffc afaa0000 23bdfffc afab0000 23bdfffc afac0000 23bdfffc afad0000 23bdfffc afae0000
  //   23bdfffc afaf0000 23bdfffc afb00000 23bdfffc afb10000 23bdfffc afb20000 23bdfffc afb30000 23bdfffc
  //   afb40000 23bdfffc afb50000 23bdfffc afb60000 23bdfffc afb70000 23bdfffc afb80000 23bdfffc afb90000
  //   20160003 20140006 20150001 168020 108100 2149825 132020 20020022 c 1600fffa 295a022 1680fff7
  //   8fb90000 23bd0004 8fb80000 23bd0004 8fb70000 23bd0004 8fb60000 23bd0004 8fb50000 23bd0004 8fb40000
  //   23bd0004 8fb30000 23bd0004 8fb20000 23bd0004 8fb10000 23bd0004 8fb00000 23bd0004 8faf0000 23bd0004
  //   8fae0000 23bd0004 8fad0000 23bd0004 8fac0000 23bd0004 8fab0000 23bd0004 8faa0000 23bd0004 8fa90000
  //   23bd0004 8fa80000 23bd0004 8fa70000 23bd0004 8fa60000 23bd0004 8fa50000 23bd0004 8fa40000 23bd0004
  //   8fa30000 23bd0004 8fa20000 23bd0004 8fa10000 23bd0004 42000018 20110200 20020022 112020 c 2231ffff
  //   1620fffc 20020032 c 2002000a c
  //   JMP
  //   JR
  //   OP
  //   OP
  //   Func
  //   Func
  //   rs
  //   rt
  //   rd
  //   中断信号源及指示电路规范（优先级3>2>1>CPU(0）)
  //   Beq
  //   Bne
  //   MemToReg
  //   MemWrite
  //   AluOP
  //   AluSrcB
  //   RegWrite
  //   JAL
  //   RegDst
  //   Syscall
endmodule

module \中断信号  (
  input  in_1,
  input  in_2,
  input  in_3,
  input  in_4,
  output out_5,
  output out_6
);

  wire and_1_out, d_ff_1_q, or_2_out;

  or or_1 (out_6, out_5, d_ff_1_q);
  D_Flip_Flop d_ff_1 (.clk(in_2), .D(1'b1), .Q(d_ff_1_q), .reset(out_5));  // open: Qn, preset, en
  or or_2 (or_2_out, d_ff_1_q, out_5);
  and and_1 (and_1_out, or_2_out, ~in_3);  // AND_Gate
  D_Flip_Flop d_ff_2 (.clk(in_1), .D(and_1_out), .Q(out_5), .reset(in_4));  // open: Qn, preset, en
endmodule

module \分支预测  (
);

  wire and_1_out, and_2_out, and_4_out, and_5_out, and_6_out, and_7_out, and_8_out, and_9_out, and_12_out,
       and_13_out, and_14_out, and_15_out, and_16_out, and_17_out, BGEZ, cache_1_miss, CLK, comparator_2_lt,
       comparator_3_eq, comparator_4_eq, comparator_5_eq, comparator_6_eq, comparator_7_eq, EQUL, EX_MEM,
       ex_miss, EX_WE, Go, ID_EX, IF_ID, if_id_1_miss_2, IR1, IR2, IR3, JMP, JMPp, JR, JRr, LOAD_USE, MEM_WE,
       miss, not_1_out, not_3_out, not_4_out, not_5_out, not_6_out, or_1_out, or_2_out, or_3_out, or_5_out,
       ready, RST, sel, select, SignedExt, SRAV, sys, target, W1, W2, W3, WE, xor_1_out, xor_2_out, \分支 ;
  wire [1:0] R1_CON, R1_con_t, R1_con_t_t, R2_CON, R2_con_t;
  wire [2:0] id_ex_1_mem_2, MEM;
  wire [3:0] mem_wb_1_wb_2;
  wire [4:0] EX, ex_mem_1_mem_2, ex_mem_1_wb_2, EX_WR, id_ex_1_ex_2, id_ex_1_wb_2, ID_R1, ID_R2, MEM_WR,
       multiplexer_7_out, multiplexer_13_out, multiplexer_14_out, multiplexer_18_out, multiplexer_21_out,
       shamt, WB, WR;
  wire [5:0] ALU_OP, FUNC, id_ex_1_ir_2, OP;
  wire [9:0] multiplexer_2_out, pc;
  wire [11:0] EX_PC, ID_PC, IF_PC, MEM_PC, WB_PC;
  wire [15:0] \LoadUse次数 , multiplexer_22_out, \分支预测错误 , \总周期数 , \无条件分支数 , \条件分支成功数 ;
  wire [15:6] if_id_1_ir_2;
  wire [25:11] id_ex_1_ir_2_2;
  wire [25:16] if_id_1_ir_2_2;
  wire [31:0] adder_1_out, adder_4_out, alu_1, alu_2, alu_5, alu_a, alu_b, bit_extender_1_out,
       bit_extender_2_out, bit_extender_3_out, dataout, ex_data, ex_mem_1_a_2, ex_mem_1_b_2, ex_mem_1_ir_2,
       ex_mem_1_pc_2, id_ex_1_shmat_2, if_id_1_dataout_2, if_id_1_pc_2, im, JMPA, LedData, mem_wb_1_alu_2,
       mem_wb_1_ir_2, mem_wb_1_md_2, mem_wb_1_pc_2, mips_alu_1_result, mips_regifile_1_r1,
       mips_regifile_1_r2, multiplexer_1_out, multiplexer_3_out, multiplexer_4_out, multiplexer_5_out,
       multiplexer_6_out, multiplexer_11_out, multiplexer_20_out, multiplexer_23_out, pc_4, pc_ex, PC_q, R1,
       R2, ram_1_data, RD, rom_1_data, shifter_1_out, \分支a ;

  Button \u_总复位  (.out(RST));
  Button _1 (.out(IR1));
  Button _2 (.out(IR2));
  Button _3 (.out(IR3));
  Button \u_继续运行  (.out(Go));
  LED led_1 (.in(W1));
  LED led_2 (.in(W2));
  LED led_3 (.in(W3));
  Hex_Digit_Display hex_digit_display_1 (.value(LedData[31:28]));  // open: dp
  xor xor_1 (xor_1_out, ex_miss, \分支 );
  and and_1 (and_1_out, ex_miss, ~target, \分支 );  // AND_Gate
  Multiplexer #(.select(2), .width(32), .enable("false")) multiplexer_1 (
    .in0(adder_1_out), .in1(multiplexer_6_out), .in2(pc_4), .in3(multiplexer_5_out), .out(multiplexer_1_out),
    .sel({ex_miss, \分支 }));
  Hex_Digit_Display hex_digit_display_2 (.value(LedData[27:24]));  // open: dp
  Hex_Digit_Display hex_digit_display_3 (.value(LedData[23:20]));  // open: dp
  Counter #(.width(16), .max('hffff)) counter_1 (
    .count(sel), .Q(\总周期数 ), .clk(CLK), .clr(RST));  // open: load, D, carry
  Multiplexer #(.width(10), .enable("false")) multiplexer_2 (
    .in0(pc), .in1(pc_ex[11:2]), .out(multiplexer_2_out), .sel(ready));
  and and_2 (and_2_out, ~xor_1_out, ~and_1_out);  // AND_Gate
  Multiplexer #(.width(32), .enable("false")) multiplexer_3 (
    .in0(multiplexer_1_out), .in1(\分支a ), .out(multiplexer_3_out), .sel(BGEZ));
  and and_3 (ready, \分支 , ~ex_miss);  // AND_Gate
  Hex_Digit_Display hex_digit_display_4 (.value(LedData[19:16]));  // open: dp
  Hex_Digit_Display hex_digit_display_5 (.value(LedData[15:12]));  // open: dp
  and and_4 (and_4_out, and_2_out, miss);
  Multiplexer #(.width(32), .enable("false")) multiplexer_4 (
    .in0(multiplexer_3_out), .in1(dataout), .out(multiplexer_4_out), .sel(and_4_out));
  and and_5 (and_5_out, sel, ~LOAD_USE);  // AND_Gate
  Multiplexer #(.width(32), .enable("false")) multiplexer_5 (
    .in0(multiplexer_6_out), .in1(adder_1_out), .out(multiplexer_5_out), .sel(and_6_out));
  and and_6 (and_6_out, ex_miss, target);
  Hex_Digit_Display hex_digit_display_6 (.value(LedData[11:8]));  // open: dp
  Hex_Digit_Display hex_digit_display_7 (.value(LedData[7:4]));  // open: dp
  Clock clock_1 (.out(CLK));
  Register #(.width(32)) u_PC (
    .D(multiplexer_4_out), .en(and_5_out), .Q({PC_q[31:12], pc, PC_q[1:0]}), .clk(CLK), .clr(RST));
  Hex_Digit_Display hex_digit_display_8 (.value(LedData[3:0]));  // open: dp
  foward foward_1 (
    .OP(OP), .EX_WriteReg_num(EX_WR), .EX_RegWrite(EX_WE), .R1_con(R1_CON), .OP_alu(ALU_OP),
    .MEM_WriteReg_num(MEM_WR), .MEM_RegWrite(MEM_WE), .load_use(LOAD_USE), .Func(FUNC), .ID_R1_num(ID_R1),
    .ID_R2_num(ID_R2), .R2_con(R2_CON));
  cache cache_1 (
    .BlockDataIn(multiplexer_4_out), .Addr(multiplexer_2_out), .BlkDataReady(ready), .CLK(CLK),
    .Enable(1'b1), .Miss(cache_1_miss), .DataOut(dataout));
  Multiplexer #(.width(32), .enable("false")) multiplexer_6 (
    .in0(\分支a ), .in1(JMPA), .out(multiplexer_6_out), .sel(JMPp));
  and and_7 (and_7_out, \分支 , not_1_out);
  not not_1 (not_1_out, JMPp);
  not not_2 (miss, cache_1_miss);
  Adder #(.width(32)) adder_1 (.a({PC_q[31:12], pc, PC_q[1:0]}), .b(32'h4), .out(adder_1_out));  // open: cin, cout
  Comparator #(.width(32)) comparator_1 (.a(ex_data), .b(multiplexer_6_out), .eq(target));  // open: gt, lt
  // Probe on \总周期数 
  // Probe on \无条件分支数 
  // Probe on \条件分支成功数 
  // Probe on \LoadUse次数 
  // Probe on \LoadUse次数 
  // Probe on \分支预测错误 
  Counter #(.width(16), .max('hffff)) counter_2 (
    .count(and_7_out), .Q(\条件分支成功数 ), .clk(CLK), .clr(RST));  // open: load, D, carry
  ROM #(.addrWidth(10), .dataWidth(32)) rom_1 (.addr(pc), .data(rom_1_data));  // open: sel
  and and_8 (and_8_out, ~target, ex_miss);  // AND_Gate
  // Probe on IF_PC
  IF_ID if_id_1 (
    .IR(rom_1_data), .PC({PC_q[31:12], pc, PC_q[1:0]}), .\传输状态In_表明当前传输数据有效 (1'b1), .CLK(CLK),
    .IR_2({OP, if_id_1_ir_2_2, if_id_1_ir_2, FUNC}), .PC_2(if_id_1_pc_2), .\传输状态Out_表明当前传输数据有效 (IF_ID),
    .\同步清零_气泡_高电平有效 (or_2_out), .\使能端_低电平有效_stall_高电平有效 (or_1_out), .miss(miss), .miss_2(if_id_1_miss_2),
    .dataout(dataout), .dataout_2(if_id_1_dataout_2));
  or or_1 (or_1_out, not_3_out, LOAD_USE);
  or or_2 (or_2_out, and_8_out, xor_2_out);
  xor xor_2 (xor_2_out, ex_miss, \分支 );
  // Probe on ID_PC
  assign bit_extender_1_out = {{16{if_id_1_ir_2[15]}}, {if_id_1_ir_2, FUNC}};  // Bit_Extender bit_extender_1
  assign bit_extender_2_out = {{16{1'b0}}, {if_id_1_ir_2, FUNC}};  // Bit_Extender bit_extender_2
  // Probe on EX_PC
  // Probe on MEM_PC
  Multiplexer #(.width(5), .enable("false")) multiplexer_7 (
    .in0(if_id_1_ir_2_2[25:21]), .in1({5{1'b1}}), .out(multiplexer_7_out), .sel(JR));
  Multiplexer #(.width(32), .enable("false")) multiplexer_8 (
    .in0(bit_extender_1_out), .in1(bit_extender_2_out), .out(im), .sel(SignedExt));
  not not_3 (not_3_out, sel);
  or or_3 (or_3_out, LOAD_USE, or_2_out);
  // Probe on WB_PC
  Counter #(.width(16), .max('hffff)) counter_3 (
    .count(JMPp), .Q(\无条件分支数 ), .clk(CLK), .clr(RST));  // open: load, D, carry
  \硬布线控制器  \u_硬布线控制器_1  (
    .Func(FUNC), .OP(OP), .ALU_OP(EX[3:0]), .MemToReg(WB[0]), .MemWrite(MEM[2]), .ALU_SRC(EX[4]),
    .RegWrite(WB[1]), .SysCALL(WB[4]), .SignedExt(SignedExt), .RegDst(WB[3]), .JR(JR), .JMP(JMP),
    .Beq(MEM[0]), .JAL(WB[2]), .Bne(MEM[1]));
  Multiplexer #(.width(5), .enable("false")) multiplexer_9 (
    .in0(multiplexer_7_out), .in1(5'b00010), .out(ID_R1), .sel(WB[4]));
  Multiplexer #(.width(5), .enable("false")) multiplexer_10 (
    .in0(if_id_1_ir_2_2[20:16]), .in1(5'b00100), .out(ID_R2), .sel(WB[4]));
  MIPS_Regifile mips_regifile_1 (
    .Din(RD), .Clk(CLK), .R1(mips_regifile_1_r1), .R2(mips_regifile_1_r2), .WE(WE), .W_num(WR),
    .R1_num(ID_R1), .R2_num(ID_R2));
  ID_EX id_ex_1 (
    .WB(WB), .MEM({JR, JMP, MEM}), .EX(EX), .IR({OP, if_id_1_ir_2_2, if_id_1_ir_2, FUNC}), .PC(if_id_1_pc_2),
    .A(mips_regifile_1_r1), .B(mips_regifile_1_r2), .SHMAT(im), .\传输状态In_表明当前传输数据有效 (IF_ID), .CLK(CLK),
    .WB_2({id_ex_1_wb_2[4:2], EX_WE, id_ex_1_wb_2[0]}), .MEM_2({JRr, JMPp, id_ex_1_mem_2}),
    .EX_2(id_ex_1_ex_2), .IR_2({ALU_OP, id_ex_1_ir_2_2, shamt, id_ex_1_ir_2}), .PC_2(pc_ex), .A_2(alu_1),
    .B_2(alu_5), .SHMAT_2(id_ex_1_shmat_2), .\传输状态Out_表明当前传输数据有效 (ID_EX), .\同步清零_气泡_高电平有效 (or_3_out),
    .\使能端_低电平有效_stall_高电平有效 (not_3_out), .R1(R1_CON), .R1_2(R1_con_t), .R2(R2_CON), .R2_2(R2_con_t),
    .miss(if_id_1_miss_2), .miss_2(ex_miss), .dataout(if_id_1_dataout_2), .dataout_2(ex_data));
  and and_9 (and_9_out, sel, LOAD_USE);
  Multiplexer #(.width(32), .enable("false")) multiplexer_11 (
    .in0(alu_b), .in1(id_ex_1_shmat_2), .out(multiplexer_11_out), .sel(id_ex_1_ex_2[4]));
  Shifter #(.width(32)) shifter_1 (.in(id_ex_1_shmat_2), .\dist (5'b00010), .out(shifter_1_out));
  Counter #(.width(16), .max('hffff)) counter_4 (
    .count(and_9_out), .Q(\LoadUse次数 ), .clk(CLK), .clr(RST));  // open: load, D, carry
  Comparator #(.width(32)) comparator_2 (.a(alu_1), .b(32'h1), .lt(comparator_2_lt));  // open: gt, eq
  Comparator #(.width(6)) comparator_3 (.a(ALU_OP), .b(6'b000001), .eq(comparator_3_eq));  // open: gt, lt
  not not_4 (not_4_out, EQUL);
  Multiplexer #(.width(32), .enable("false")) multiplexer_12 (
    .in0({pc_4[31:28], id_ex_1_ir_2_2, shamt, id_ex_1_ir_2, 2'b00}), .in1(alu_1), .out(JMPA), .sel(JRr));
  MIPS_ALU mips_alu_1 (
    .X(alu_a), .Y(multiplexer_11_out), .AluOP(id_ex_1_ex_2[3:0]), .Equal(EQUL), .Result(mips_alu_1_result),
    .shamt(multiplexer_13_out));  // open: Result_2
  Multiplexer #(.width(5), .enable("false")) multiplexer_13 (
    .in0(shamt), .in1(alu_1[4:0]), .out(multiplexer_13_out), .sel(SRAV));
  Adder #(.width(32)) adder_2 (.a(shifter_1_out), .b(pc_4), .out(\分支a ));  // open: cin, cout
  Comparator #(.width(6)) comparator_4 (.a(ALU_OP), .b({6{1'b0}}), .eq(comparator_4_eq));  // open: gt, lt
  and and_10 (SRAV, comparator_4_eq, comparator_5_eq);
  Comparator #(.width(6)) comparator_5 (.a(id_ex_1_ir_2), .b(6'b000111), .eq(comparator_5_eq));  // open: gt, lt
  and and_11 (BGEZ, ~comparator_2_lt, comparator_3_eq);  // AND_Gate
  and and_12 (and_12_out, id_ex_1_mem_2[0], EQUL);
  and and_13 (and_13_out, id_ex_1_mem_2[1], not_4_out);
  and and_14 (and_14_out, ex_miss, ~target);  // AND_Gate
  and and_15 (and_15_out, ex_miss, ~\分支 );  // AND_Gate
  or or_4 (\分支 , JMPp, and_12_out, BGEZ, and_13_out);
  Multiplexer #(.width(5), .enable("false")) multiplexer_14 (
    .in0(id_ex_1_ir_2_2[20:16]), .in1(id_ex_1_ir_2_2[15:11]), .out(multiplexer_14_out), .sel(id_ex_1_wb_2[3]));
  Multiplexer #(.width(5), .enable("false")) multiplexer_15 (
    .in0(multiplexer_14_out), .in1({5{1'b1}}), .out(EX_WR), .sel(id_ex_1_wb_2[2]));
  or or_5 (or_5_out, ready, and_14_out, and_15_out);
  Adder #(.width(32)) adder_3 (.a(32'h4), .b(pc_ex), .out(pc_4));  // open: cin, cout
  EX_MEM ex_mem_1 (
    .WB({id_ex_1_wb_2[4:2], EX_WE, id_ex_1_wb_2[0]}), .MEM({JRr, JMPp, id_ex_1_mem_2}),
    .IR({ALU_OP, id_ex_1_ir_2_2, shamt, id_ex_1_ir_2}), .PC(pc_ex), .B(alu_b), .ALU(mips_alu_1_result),
    .\传输状态In_表明当前传输数据有效 (ID_EX), .CLK(CLK), .WB_2({ex_mem_1_wb_2[4:2], MEM_WE, ex_mem_1_wb_2[0]}),
    .MEM_2(ex_mem_1_mem_2), .IR_2(ex_mem_1_ir_2), .PC_2(ex_mem_1_pc_2), .B_2(ex_mem_1_b_2), .ALU_2(alu_2),
    .\传输状态Out_表明当前传输数据有效 (EX_MEM), .\使能端_低电平有效_stall_高电平有效 (not_3_out), .A(alu_a), .A_2(ex_mem_1_a_2));  // open: 同步清零_气泡_高电平有效
  Multiplexer #(.select(2), .width(32), .enable("false")) multiplexer_16 (
    .in0(alu_1), .in1(alu_2), .in2(RD), .in3(alu_2), .out(alu_a), .sel(R1_con_t_t));
  Multiplexer #(.select(2), .width(32), .enable("false")) multiplexer_17 (
    .in0(alu_5), .in1(alu_2), .in2(RD), .in3(alu_2), .out(alu_b), .sel(R2_con_t));
  Counter #(.width(16), .max('hffff)) counter_5 (
    .count(or_5_out), .Q(\分支预测错误 ), .clk(CLK), .clr(RST));  // open: load, D, carry
  Comparator #(.width(32)) comparator_6 (.a(R1), .b(32'h32), .eq(comparator_6_eq));  // open: gt, lt
  Multiplexer #(.width(5), .enable("false")) multiplexer_18 (
    .in0(ex_mem_1_ir_2[20:16]), .in1(ex_mem_1_ir_2[15:11]), .out(multiplexer_18_out), .sel(ex_mem_1_wb_2[3]));
  and and_16 (and_16_out, comparator_6_eq, sys);
  not not_5 (not_5_out, comparator_6_eq);
  Multiplexer #(.width(5), .enable("false")) multiplexer_19 (
    .in0(multiplexer_18_out), .in1({5{1'b1}}), .out(MEM_WR), .sel(ex_mem_1_wb_2[2]));
  not not_6 (not_6_out, and_16_out);
  and and_17 (and_17_out, not_5_out, sys);
  RAM #(.addrWidth(10), .dataWidth(32), .bus("separate")) ram_1 (
    .addr(alu_2[11:2]), .din(ex_mem_1_b_2), .data(ram_1_data), .str(ex_mem_1_mem_2[2]), .sel(sel), .clk(CLK),
    .clr(RST));  // open: ld
  or or_6 (sel, Go, not_6_out);
  Register #(.width(32)) register_1 (.D(R2), .en(and_17_out), .Q(LedData), .clk(CLK), .clr(RST));
  MEM_WB mem_wb_1 (
    .WB({ex_mem_1_wb_2[4:2], MEM_WE, ex_mem_1_wb_2[0]}), .IR(ex_mem_1_ir_2), .PC(ex_mem_1_pc_2), .ALU(alu_2),
    .MD(ram_1_data), .\传输状态In_表明当前传输数据有效 (EX_MEM), .CLK(CLK),
    .WB_2({sys, mem_wb_1_wb_2[3:2], WE, mem_wb_1_wb_2[0]}), .IR_2(mem_wb_1_ir_2), .PC_2(mem_wb_1_pc_2),
    .ALU_2({mem_wb_1_alu_2[31:2], select, mem_wb_1_alu_2[0]}), .MD_2(mem_wb_1_md_2),
    .\使能端_低电平有效_stall_高电平有效 (not_3_out), .A(ex_mem_1_a_2), .A_2(R1), .B(ex_mem_1_b_2), .B_2(R2));  // open: 传输状态Out_表明当前传输数据有效, 同步清零_气泡_高电平有效
  Adder #(.width(32)) adder_4 (.a(mem_wb_1_pc_2), .b(32'h4), .out(adder_4_out));  // open: cin, cout
  Multiplexer #(.width(32)) multiplexer_20 (
    .in0({mem_wb_1_alu_2[31:2], select, mem_wb_1_alu_2[0]}), .in1(mem_wb_1_md_2), .out(multiplexer_20_out),
    .sel(mem_wb_1_wb_2[0]));  // open: en
  Multiplexer #(.width(5), .enable("false")) multiplexer_21 (
    .in0(mem_wb_1_ir_2[20:16]), .in1(mem_wb_1_ir_2[15:11]), .out(multiplexer_21_out), .sel(mem_wb_1_wb_2[3]));
  Multiplexer #(.width(16), .enable("false")) multiplexer_22 (
    .in0(multiplexer_20_out[15:0]), .in1(multiplexer_20_out[31:16]), .out(multiplexer_22_out), .sel(select));
  Comparator #(.width(6)) comparator_7 (.a(mem_wb_1_ir_2[31:26]), .b(6'b100001), .eq(comparator_7_eq));  // open: gt, lt
  Multiplexer #(.width(32), .enable("false")) multiplexer_23 (
    .in0(multiplexer_20_out), .in1(bit_extender_3_out), .out(multiplexer_23_out), .sel(comparator_7_eq));
  assign bit_extender_3_out = {{16{multiplexer_22_out[15]}}, multiplexer_22_out};  // Bit_Extender bit_extender_3
  Multiplexer #(.width(5), .enable("false")) multiplexer_24 (
    .in0(multiplexer_21_out), .in1({5{1'b1}}), .out(WR), .sel(mem_wb_1_wb_2[2]));
  Multiplexer #(.width(32)) multiplexer_25 (
    .in0(multiplexer_23_out), .in1(adder_4_out), .out(RD), .sel(mem_wb_1_wb_2[2]));  // open: en

  // Other names for the same wires on the sheet: MEM[4:3] = {JR, JMP}; R1_EX[31:0] = alu_1; pc_pre[9:0] = pc_ex[11:2];
  //   插入气泡数[15:0] = \LoadUse次数 

  // Notes on the sheet:
  //   中断源
  //   中断等待指示
  //   数码管输出
  //   contents of rom_1 (hex, n*v repeats v):
  //   20110001 8100005 20110001 20120002 20130003 8100009 20110001 20120002 20130003 810000d 20110001
  //   20120002 20130003 8100011 20110001 20120002 20130003 c1000f7 20100001 20110001 118fc0 112020
  //   20020022 c 118882 12200001 8100015 112020 20020022 c 20110001 118880 112020 20020022 c 12200001
  //   810001f 20110001 118fc0 112020 20020022 c 1188c3 112020 20020022 c 118903 112020 20020022 c 118903
  //   112020 20020022 c 118903 112020 20020022 c 118903 112020 20020022 c 118903 112020 20020022 c 118903
  //   112020 20020022 c 118903 112020 20020022 c 20100001 109fc0 139fc3 8021 2012000c 24160003 26100001
  //   3210000f 20080008 20090001 139900 2709825 132020 20020022 c 1094022 1500fff9 22100001 2018000f
  //   2188024 108700 20080008 20090001 139902 2709825 132021 20020022 c 1094022 1500fff9 108702 2c9b022
  //   12c00001 8100050 4020 1084027 84400 3508ffff 82021 20020022 c 2010ffff 20110000 ae300000 22100001
  //   22310004 ae300000 22100001 22310004 ae300000 22100001 22310004 ae300000 22100001 22310004 ae300000
  //   22100001 22310004 ae300000 22100001 22310004 ae300000 22100001 22310004 ae300000 22100001 22310004
  //   ae300000 22100001 22310004 ae300000 22100001 22310004 ae300000 22100001 22310004 ae300000 22100001
  //   22310004 ae300000 22100001 22310004 ae300000 22100001 22310004 ae300000 22100001 22310004 ae300000
  //   22100001 22310004 22100001 8020 2011003c 8e130000 8e340000 274402a 11000002 ae330000 ae140000
  //   2231fffc 1611fff8 102020 20020022 c 22100004 2011003c 1611fff2 20020032 c 20090000 200b0010 34118483
  //   20120404 118c00 129400 36318281 22520404 ad310000 2328820 21290004 216bffff 1560fffb 200b0020
  //   20090000 85310000 112020 20020022 c 21290002 216bffff 1560fff9 20020032 c 2011000f 112020 20020022 c
  //   2231ffff 621fffb 20020032 c 2008ffff 20117777 112020 20020022 c 200b0010 2288826 112020 20020022 c
  //   216bffff 1560fffa 20020032 c 20080001 20090003 20110876 118d00 112020 20020022 c 200b0008 1118807
  //   1318807 112020 20020022 c 216bffff 1560fff9 20020032 c 20100000 22100001 102020 20020022 c 22100002
  //   102020 20020022 c 22100003 102020 20020022 c 22100004 102020 20020022 c 22100005 102020 20020022 c
  //   22100006 102020 20020022 c 22100007 102020 20020022 c 22100008 102020 20020022 20020022 c 3e00008
  //   指令字
  //   流水调试日志用
  //   JMP
  //   JR
  //   OP
  //   OP
  //   Func
  //   Func
  //   rs
  //   rt
  //   rd
  //   Bne
  //   MemToReg
  //   MemWrite
  //   AluOP
  //   AluSrcB
  //   RegWrite
  //   JAL
  //   RegDst
  //   Func
  //   rt
  //   rt
  //   rt
  //   rd
endmodule

// Cache
module cache (
  input  [31:0] BlockDataIn,
  input  [9:0] Addr,
  input  BlkDataReady,
  input  CLK,
  input  Enable,
  output Miss,
  output [31:0] DataOut
);

  wire and_1_out, and_2_out, and_3_out, and_4_out, and_5_out, and_6_out, and_7_out, and_8_out, and_9_out,
       and_10_out, and_11_out, and_12_out, and_13_out, and_14_out, and_15_out, and_16_out, and_25_out,
       and_26_out, comparator_1_eq, comparator_2_eq, comparator_3_eq, comparator_4_eq, comparator_5_eq,
       comparator_6_eq, comparator_7_eq, comparator_8_eq, L0, L1, L2, L3, L4, L5, L6, L7, not_1_out,
       not_2_out, not_3_out, not_4_out, not_5_out, not_6_out, not_7_out, not_8_out, R0, R1, R2, R3, R4, R5,
       R6, R7, V0, V1, V2, V3, V4, V5, V6, V7;
  wire [2:0] max3_1_max_num, max3_2_max_num, max3_3_max_num, max3_4_max_num, max3_5_max_num, max3_6_max_num,
       max3_7_max_num, priority_encoder_1_out, swic;
  wire [9:0] Tag0, Tag1, Tag2, Tag3, Tag4, Tag5, Tag6, Tag7;
  wire [15:0] C0, C1, C2, C3, C4, C5, C6, C7, max3_1_max, max3_2_max, max3_3_max, max3_4_max, max3_5_max,
       max3_7_max;
  wire [31:0] register_17_q, register_18_q, register_19_q, register_20_q, register_21_q, register_22_q,
       register_23_q, register_24_q;

  Register #(.width(1)) register_1 (.D(1'b1), .en(and_1_out), .Q(V0), .clk(CLK));  // open: clr
  and and_1 (and_1_out, Enable, R0);
  Register #(.width(1)) register_2 (.D(1'b1), .en(and_2_out), .Q(V1), .clk(CLK));  // open: clr
  and and_2 (and_2_out, Enable, R1);
  Register #(.width(1)) register_3 (.D(1'b1), .en(and_3_out), .Q(V2), .clk(CLK));  // open: clr
  and and_3 (and_3_out, Enable, R2);
  Register #(.width(1)) register_4 (.D(1'b1), .en(and_4_out), .Q(V3), .clk(CLK));  // open: clr
  and and_4 (and_4_out, Enable, R3);
  Register #(.width(1)) register_5 (.D(1'b1), .en(and_5_out), .Q(V4), .clk(CLK));  // open: clr
  and and_5 (and_5_out, Enable, R4);
  Register #(.width(1)) register_6 (.D(1'b1), .en(and_6_out), .Q(V5), .clk(CLK));  // open: clr
  and and_6 (and_6_out, Enable, R5);
  Register #(.width(1)) register_7 (.D(1'b1), .en(and_7_out), .Q(V6), .clk(CLK));  // open: clr
  and and_7 (and_7_out, Enable, R6);
  Register #(.width(1)) register_8 (.D(1'b1), .en(and_8_out), .Q(V7), .clk(CLK));  // open: clr
  and and_8 (and_8_out, Enable, R7);
  Register #(.width(10)) register_9 (.D(Addr), .en(and_1_out), .Q(Tag0), .clk(CLK));  // open: clr
  Register #(.width(10)) register_10 (.D(Addr), .en(and_2_out), .Q(Tag1), .clk(CLK));  // open: clr
  Register #(.width(10)) register_11 (.D(Addr), .en(and_3_out), .Q(Tag2), .clk(CLK));  // open: clr
  Register #(.width(10)) register_12 (.D(Addr), .en(and_4_out), .Q(Tag3), .clk(CLK));  // open: clr
  Register #(.width(10)) register_13 (.D(Addr), .en(and_5_out), .Q(Tag4), .clk(CLK));  // open: clr
  Register #(.width(10)) register_14 (.D(Addr), .en(and_6_out), .Q(Tag5), .clk(CLK));  // open: clr
  Register #(.width(10)) register_15 (.D(Addr), .en(and_7_out), .Q(Tag6), .clk(CLK));  // open: clr
  Register #(.width(10)) register_16 (.D(Addr), .en(and_8_out), .Q(Tag7), .clk(CLK));  // open: clr
  Counter #(.width(16), .max('hffff)) counter_1 (.Q(C0), .clk(CLK), .clr(and_9_out));  // open: load, D, count, carry
  Counter #(.width(16), .max('hffff)) counter_2 (.Q(C1), .clk(CLK), .clr(and_10_out));  // open: load, D, count, carry
  Counter #(.width(16), .max('hffff)) counter_3 (.Q(C2), .clk(CLK), .clr(and_11_out));  // open: load, D, count, carry
  Counter #(.width(16), .max('hffff)) counter_4 (.Q(C3), .clk(CLK), .clr(and_12_out));  // open: load, D, count, carry
  Counter #(.width(16), .max('hffff)) counter_5 (.Q(C4), .clk(CLK), .clr(and_13_out));  // open: load, D, count, carry
  Counter #(.width(16), .max('hffff)) counter_6 (.Q(C5), .clk(CLK), .clr(and_14_out));  // open: load, D, count, carry
  Counter #(.width(16), .max('hffff)) counter_7 (.Q(C6), .clk(CLK), .clr(and_15_out));  // open: load, D, count, carry
  Counter #(.width(16), .max('hffff)) counter_8 (.Q(C7), .clk(CLK), .clr(and_16_out));  // open: load, D, count, carry
  Register #(.width(32)) register_17 (.D(BlockDataIn), .en(and_1_out), .Q(register_17_q), .clk(CLK));  // open: clr
  assign DataOut = and_9_out ? register_17_q : 32'bz;  // Controlled_Buffer controlled_buffer_1
  and and_9 (and_9_out, L0, Enable);
  assign DataOut = and_10_out ? register_18_q : 32'bz;  // Controlled_Buffer controlled_buffer_2
  Register #(.width(32)) register_18 (.D(BlockDataIn), .en(and_2_out), .Q(register_18_q), .clk(CLK));  // open: clr
  and and_10 (and_10_out, L1, Enable);
  assign DataOut = and_11_out ? register_19_q : 32'bz;  // Controlled_Buffer controlled_buffer_3
  Register #(.width(32)) register_19 (.D(BlockDataIn), .en(and_3_out), .Q(register_19_q), .clk(CLK));  // open: clr
  and and_11 (and_11_out, L2, Enable);
  assign DataOut = and_12_out ? register_20_q : 32'bz;  // Controlled_Buffer controlled_buffer_4
  Register #(.width(32)) register_20 (.D(BlockDataIn), .en(and_4_out), .Q(register_20_q), .clk(CLK));  // open: clr
  and and_12 (and_12_out, L3, Enable);
  assign DataOut = and_13_out ? register_21_q : 32'bz;  // Controlled_Buffer controlled_buffer_5
  Register #(.width(32)) register_21 (.D(BlockDataIn), .en(and_5_out), .Q(register_21_q), .clk(CLK));  // open: clr
  and and_13 (and_13_out, L4, Enable);
  assign DataOut = and_14_out ? register_22_q : 32'bz;  // Controlled_Buffer controlled_buffer_6
  Register #(.width(32)) register_22 (.D(BlockDataIn), .en(and_6_out), .Q(register_22_q), .clk(CLK));  // open: clr
  and and_14 (and_14_out, L5, Enable);
  assign DataOut = and_15_out ? register_23_q : 32'bz;  // Controlled_Buffer controlled_buffer_7
  Register #(.width(32)) register_23 (.D(BlockDataIn), .en(and_7_out), .Q(register_23_q), .clk(CLK));  // open: clr
  and and_15 (and_15_out, L6, Enable);
  assign DataOut = and_16_out ? register_24_q : 32'bz;  // Controlled_Buffer controlled_buffer_8
  Register #(.width(32)) register_24 (.D(BlockDataIn), .en(and_8_out), .Q(register_24_q), .clk(CLK));  // open: clr
  and and_16 (and_16_out, L7, Enable);
  Comparator #(.width(10)) comparator_1 (.a(Addr), .b(Tag0), .eq(comparator_1_eq));  // open: gt, lt
  Comparator #(.width(10)) comparator_2 (.a(Addr), .b(Tag1), .eq(comparator_2_eq));  // open: gt, lt
  Comparator #(.width(10)) comparator_3 (.a(Addr), .b(Tag2), .eq(comparator_3_eq));  // open: gt, lt
  Comparator #(.width(10)) comparator_4 (.a(Addr), .b(Tag3), .eq(comparator_4_eq));  // open: gt, lt
  Comparator #(.width(10)) comparator_5 (.a(Addr), .b(Tag4), .eq(comparator_5_eq));  // open: gt, lt
  Comparator #(.width(10)) comparator_6 (.a(Addr), .b(Tag5), .eq(comparator_6_eq));  // open: gt, lt
  Comparator #(.width(10)) comparator_7 (.a(Addr), .b(Tag6), .eq(comparator_7_eq));  // open: gt, lt
  Comparator #(.width(10)) comparator_8 (.a(Addr), .b(Tag7), .eq(comparator_8_eq));  // open: gt, lt
  not not_1 (not_1_out, V0);
  not not_2 (not_2_out, V1);
  not not_3 (not_3_out, V2);
  not not_4 (not_4_out, V3);
  not not_5 (not_5_out, V4);
  not not_6 (not_6_out, V5);
  not not_7 (not_7_out, V6);
  not not_8 (not_8_out, V7);
  and and_17 (L0, comparator_1_eq, V0);
  and and_18 (L1, comparator_2_eq, V1);
  and and_19 (L2, comparator_3_eq, V2);
  and and_20 (L3, comparator_4_eq, V3);
  and and_21 (L4, comparator_5_eq, V4);
  and and_22 (L5, comparator_6_eq, V5);
  and and_23 (L6, comparator_7_eq, V6);
  and and_24 (L7, comparator_8_eq, V7);
  Priority_Encoder priority_encoder_1 (
    .in0(not_1_out), .in1(not_2_out), .in2(not_3_out), .in3(not_4_out), .in4(not_5_out), .in5(not_6_out),
    .in6(not_7_out), .in7(not_8_out), .out(priority_encoder_1_out));  // open: en_in, gs, en_out
  Max3 max3_1 (.Y(C1), .X(C0), .Y_num(3'b001), .X_num(3'b000), .MAX(max3_1_max), .Max_num(max3_1_max_num));
  Max3 max3_2 (.Y(C3), .X(C2), .Y_num(3'b011), .X_num(3'b010), .MAX(max3_2_max), .Max_num(max3_2_max_num));
  Max3 max3_3 (.Y(C5), .X(C4), .Y_num(3'b101), .X_num(3'b100), .MAX(max3_3_max), .Max_num(max3_3_max_num));
  Max3 max3_4 (.Y(C7), .X(C6), .Y_num(3'b111), .X_num(3'b110), .MAX(max3_4_max), .Max_num(max3_4_max_num));
  and and_25 (and_25_out, BlkDataReady, Enable);
  Max3 max3_5 (
    .Y(max3_2_max), .X(max3_1_max), .Y_num(max3_2_max_num), .X_num(max3_1_max_num), .MAX(max3_5_max),
    .Max_num(max3_5_max_num));
  Max3 max3_6 (
    .Y(max3_7_max), .X(max3_5_max), .Y_num(max3_7_max_num), .X_num(max3_5_max_num), .Max_num(max3_6_max_num));  // open: MAX
  Max3 max3_7 (
    .Y(max3_4_max), .X(max3_3_max), .Y_num(max3_4_max_num), .X_num(max3_3_max_num), .MAX(max3_7_max),
    .Max_num(max3_7_max_num));
  Demultiplexer #(.select(3)) demultiplexer_1 (
    .out0(R0), .out1(R1), .out2(R2), .out3(R3), .out4(R4), .out5(R5), .out6(R6), .out7(R7), .in(and_25_out),
    .sel(swic));  // open: en
  nor nor_1 (Miss, L0, L1, L2, L3, L4, L5, L6, L7);
  Multiplexer #(.width(3)) multiplexer_1 (
    .in0(priority_encoder_1_out), .in1(max3_6_max_num), .out(swic), .sel(and_26_out));  // open: en
  and and_26 (and_26_out, V0, V1, V2, V3, V4, V5, V6, V7);

  // Other names for the same wires on the sheet: Blk[31:0] = BlockDataIn; BlkReady = BlkDataReady; En = Enable;
  //   SlotData[31:0] = DataOut; tag[9:0] = Addr; 字节地址[9:0] = Addr

  // Notes on the sheet:
  //   输入引脚区
  //   请勿增改引脚，请勿修改子电路封装
  //   电路功能：利用上面给定的隧道构建8行的Cache，cache映射方式自选
  //   请在下方利用上方输入输出引脚的隧道信号构建电路，ctrl+d复制选择部件
  //   输出引脚区
endmodule

module Max3 (
  input  [15:0] Y,
  input  [15:0] X,
  input  [2:0] Y_num,
  input  [2:0] X_num,
  output [15:0] MAX,
  output [2:0] Max_num
);

  wire comparator_1_eq, comparator_1_gt, or_1_out;

  Multiplexer #(.width(16), .enable("false")) multiplexer_1 (.in0(Y), .in1(X), .out(MAX), .sel(or_1_out));
  Comparator #(.width(16), .mode("unsigned")) comparator_1 (
    .a(X), .b(Y), .gt(comparator_1_gt), .eq(comparator_1_eq));  // open: lt
  or or_1 (or_1_out, comparator_1_gt, comparator_1_eq);
  Multiplexer #(.width(3), .enable("false")) multiplexer_2 (.in0(Y_num), .in1(X_num), .out(Max_num), .sel(or_1_out));

  // Notes on the sheet:
  //   输出两个输入中的较大值，并输出较大值的3位编号
endmodule
module \流水中断  (
);

  wire \_1号中断 , \_1号中断等待指示 , \_2号中断 , \_2号中断等待指示 , \_3号中断 , \_3号中断等待指示 , and_1_out, and_2_out, and_3_out,
       and_4_out, and_5_out, and_6_out, and_10_out, and_11_out, and_12_out, and_13_out, BGEZ, block, CLK,
       comparator_1_gt, comparator_2_lt, comparator_3_eq, comparator_4_eq, comparator_5_eq, comparator_6_eq,
       comparator_7_eq, comparator_8_eq, comparator_9_eq, EQUL, ERET, EX_MEM, EX_WE, Go, ID_EX, IF_ID, IR1,
       IR2, IR3, JMP, JMPp, JR, JRr, LOAD_USE, MEM_WE, not_1_out, not_2_out, not_3_out, not_4_out, not_5_out,
       not_6_out, or_1_out, or_2_out, register_3_q, RST, sel, select, SignedExt, SRAV, sys, W1, W2, W3, WE,
       \中断信号 , \中断信号_1_out_5 , \中断信号_2_out_5 , \中断信号_3_out_5 , \分支 , \分支_IR ;
  wire [1:0] NUM, priority_encoder_1_out, R1_CON, R1_con_t, R1_con_t_t, R2_CON, R2_con_t, \中断级别 ;
  wire [2:0] id_ex_1_mem_2, MEM;
  wire [3:0] mem_wb_1_wb_2;
  wire [4:0] EX, ex_mem_1_mem_2, ex_mem_1_wb_2, EX_WR, id_ex_1_ex_2, id_ex_1_wb_2, ID_R1, ID_R2, MEM_WR,
       multiplexer_8_out, multiplexer_15_out, multiplexer_16_out, multiplexer_20_out, multiplexer_23_out,
       shamt, WB, WR;
  wire [5:0] ALU_OP, FUNC, id_ex_1_ir_2, OP;
  wire [11:0] EX_PC, ID_PC, IF_PC, MEM_PC, WB_PC;
  wire [15:0] \LoadUse次数 , multiplexer_24_out, \总周期数 , \插入气泡数 , \无条件分支数 , \条件分支成功数 ;
  wire [15:6] if_id_1_ir_2;
  wire [25:11] id_ex_1_ir_2_2;
  wire [25:16] if_id_1_ir_2_2;
  wire [31:0] adder_1_out, alu_1, alu_2, alu_5, alu_a, alu_b, bit_extender_1_out, bit_extender_2_out,
       bit_extender_3_out, ex_mem_1_a_2, ex_mem_1_b_2, ex_mem_1_ir_2, ex_mem_1_pc_2, id_ex_1_pc_2,
       id_ex_1_shmat_2, im, IR_ADD, IR_PC, JMPA, LedData, mem_wb_1_alu_2, mem_wb_1_ir_2, mem_wb_1_md_2,
       mem_wb_1_pc_2, mips_alu_1_result, mips_regifile_1_r1, mips_regifile_1_r2, multiplexer_1_out,
       multiplexer_2_out, multiplexer_3_out, multiplexer_4_out, multiplexer_5_out, multiplexer_6_out,
       multiplexer_12_out, multiplexer_13_out, multiplexer_22_out, multiplexer_25_out, PC_0_q, PC_1_q,
       PC_2_q, pc_4, PC_q, PC_STORE, R1, R2, ram_1_data, RD, rom_1_data, shifter_1_out, W_PC, \分支a ;

  Button \u_总复位  (.out(RST));
  Button _1 (.out(IR1));
  Button _2 (.out(IR2));
  Button _3 (.out(IR3));
  Button \u_继续运行  (.out(Go));
  LED led_1 (.in(W1));
  LED led_2 (.in(W2));
  LED led_3 (.in(W3));
  Multiplexer #(.width(32), .enable("false")) multiplexer_1 (
    .in0(multiplexer_2_out), .in1(\分支a ), .out(multiplexer_1_out), .sel(\分支 ));
  Multiplexer #(.width(32), .enable("false")) multiplexer_2 (
    .in0(multiplexer_3_out), .in1(PC_STORE), .out(multiplexer_2_out), .sel(ERET));
  Hex_Digit_Display hex_digit_display_1 (.value(LedData[31:28]));  // open: dp
  Multiplexer #(.width(32), .enable("false")) multiplexer_3 (
    .in0(adder_1_out), .in1(IR_PC), .out(multiplexer_3_out), .sel(\中断信号 ));
  Hex_Digit_Display hex_digit_display_2 (.value(LedData[27:24]));  // open: dp
  Hex_Digit_Display hex_digit_display_3 (.value(LedData[23:20]));  // open: dp
  Counter #(.width(16), .max('hffff)) counter_1 (
    .count(sel), .Q(\总周期数 ), .clk(CLK), .clr(RST));  // open: load, D, carry
  Multiplexer #(.width(32), .enable("false")) multiplexer_4 (
    .in0(multiplexer_1_out), .in1(\分支a ), .out(multiplexer_4_out), .sel(BGEZ));
  Register #(.width(32)) PC_0 (.D(W_PC), .Q(PC_0_q), .clk(and_1_out));  // open: en, clr
  and and_1 (and_1_out, \中断信号 , \_1号中断 );
  Register #(.width(32)) PC_1 (.D(W_PC), .Q(PC_1_q), .clk(and_2_out));  // open: en, clr
  and and_2 (and_2_out, \中断信号 , \_2号中断 );
  Register #(.width(32)) PC_2 (.D(W_PC), .Q(PC_2_q), .clk(and_3_out));  // open: en, clr
  and and_3 (and_3_out, \中断信号 , \_3号中断 );
  Hex_Digit_Display hex_digit_display_4 (.value(LedData[19:16]));  // open: dp
  Hex_Digit_Display hex_digit_display_5 (.value(LedData[15:12]));  // open: dp
  Multiplexer #(.width(32), .enable("false")) multiplexer_5 (
    .in0(multiplexer_4_out), .in1(JMPA), .out(multiplexer_5_out), .sel(JMPp));
  and and_4 (and_4_out, sel, not_1_out);
  not not_1 (not_1_out, LOAD_USE);
  Hex_Digit_Display hex_digit_display_6 (.value(LedData[7:4]));  // open: dp
  Hex_Digit_Display hex_digit_display_7 (.value(LedData[11:8]));  // open: dp
  Clock clock_1 (.out(CLK));
  Register #(.width(32)) PC (.D(multiplexer_5_out), .en(and_4_out), .Q(PC_q), .clk(CLK), .clr(RST));
  Multiplexer #(.select(2), .width(32), .enable("false")) multiplexer_6 (
    .in1(PC_0_q), .in2(PC_1_q), .in3(PC_2_q), .out(multiplexer_6_out), .sel(NUM));  // open: in0
  \中断信号  \u_中断信号_1  (.in_2(\_1号中断 ), .out_6(\_1号中断等待指示 ), .in_3(ERET), .in_1(CLK), .out_5(\中断信号_1_out_5 ), .in_4(RST));
  \中断信号  \u_中断信号_2  (.in_2(\_2号中断 ), .out_6(\_2号中断等待指示 ), .in_3(ERET), .in_1(CLK), .out_5(\中断信号_2_out_5 ), .in_4(RST));
  \中断信号  \u_中断信号_3  (.in_2(\_3号中断 ), .out_6(\_3号中断等待指示 ), .in_3(ERET), .in_1(CLK), .out_5(\中断信号_3_out_5 ), .in_4(RST));
  Hex_Digit_Display hex_digit_display_8 (.value(LedData[3:0]));  // open: dp
  Multiplexer #(.width(32), .enable("false")) multiplexer_7 (
    .in0(multiplexer_6_out), .in1(IR_ADD), .out(PC_STORE), .sel(\分支_IR ));
  and and_5 (and_5_out, \分支 , not_2_out);
  not not_2 (not_2_out, JMPp);
  foward foward_1 (
    .OP(OP), .EX_WriteReg_num(EX_WR), .EX_RegWrite(EX_WE), .R1_con(R1_CON), .OP_alu(ALU_OP),
    .MEM_WriteReg_num(MEM_WR), .MEM_RegWrite(MEM_WE), .load_use(LOAD_USE), .Func(FUNC), .ID_R1_num(ID_R1),
    .ID_R2_num(ID_R2), .R2_con(R2_CON));
  Adder #(.width(32)) adder_1 (.a(PC_q), .b(32'h4), .out(adder_1_out));  // open: cin, cout
  and and_6 (and_6_out, ~\中断信号_1_out_5 , ~\中断信号_2_out_5 , ~\中断信号_3_out_5 );  // AND_Gate
  // Probe on \总周期数 
  // Probe on \无条件分支数 
  // Probe on \条件分支成功数 
  // Probe on \插入气泡数 
  // Probe on \LoadUse次数 
  Counter #(.width(16), .max('hffff)) counter_2 (
    .count(and_5_out), .Q(\条件分支成功数 ), .clk(CLK), .clr(RST));  // open: load, D, carry
  ROM #(.addrWidth(10), .dataWidth(32)) rom_1 (.addr(PC_q[11:2]), .data(rom_1_data));  // open: sel
  // Probe on IF_PC
  IF_ID if_id_1 (
    .IR(rom_1_data), .PC(PC_q), .\传输状态In_表明当前传输数据有效 (1'b1), .CLK(CLK),
    .IR_2({OP, if_id_1_ir_2_2, if_id_1_ir_2, FUNC}), .PC_2(IR_ADD), .\传输状态Out_表明当前传输数据有效 (IF_ID),
    .\同步清零_气泡_高电平有效 (\分支 ), .\使能端_低电平有效_stall_高电平有效 (or_1_out));  // open: miss, miss_2, dataout, dataout_2
  or or_1 (or_1_out, not_3_out, LOAD_USE);
  Register #(.width(1)) register_1 (.D(and_6_out), .Q(block), .clk(CLK), .clr(ERET));  // open: en
  // Probe on ID_PC
  assign bit_extender_1_out = {{16{if_id_1_ir_2[15]}}, {if_id_1_ir_2, FUNC}};  // Bit_Extender bit_extender_1
  assign bit_extender_2_out = {{16{1'b0}}, {if_id_1_ir_2, FUNC}};  // Bit_Extender bit_extender_2
  // Probe on EX_PC
  // Probe on MEM_PC
  Multiplexer #(.width(5), .enable("false")) multiplexer_8 (
    .in0(if_id_1_ir_2_2[25:21]), .in1({5{1'b1}}), .out(multiplexer_8_out), .sel(JR));
  Multiplexer #(.width(32), .enable("false")) multiplexer_9 (
    .in0(bit_extender_1_out), .in1(bit_extender_2_out), .out(im), .sel(SignedExt));
  not not_3 (not_3_out, sel);
  or or_2 (or_2_out, LOAD_USE, \分支 );
  Priority_Encoder #(.select(2)) priority_encoder_1 (
    .in0(1'b1), .in1(\中断信号_1_out_5 ), .in2(\中断信号_2_out_5 ), .in3(\中断信号_3_out_5 ), .out(priority_encoder_1_out));  // open: gs, en_out, en_in
  // Probe on WB_PC
  Counter #(.width(16), .max('hffff)) counter_3 (
    .count(JMPp), .Q(\无条件分支数 ), .clk(CLK), .clr(RST));  // open: load, D, carry
  \硬布线控制器  \u_硬布线控制器_1  (
    .Func(FUNC), .OP(OP), .ALU_OP(EX[3:0]), .MemToReg(WB[0]), .MemWrite(MEM[2]), .ALU_SRC(EX[4]),
    .RegWrite(WB[1]), .SysCALL(WB[4]), .SignedExt(SignedExt), .RegDst(WB[3]), .JR(JR), .JMP(JMP),
    .Beq(MEM[0]), .JAL(WB[2]), .Bne(MEM[1]));
  Multiplexer #(.width(5), .enable("false")) multiplexer_10 (
    .in0(multiplexer_8_out), .in1(5'b00010), .out(ID_R1), .sel(WB[4]));
  Multiplexer #(.width(5), .enable("false")) multiplexer_11 (
    .in0(if_id_1_ir_2_2[20:16]), .in1(5'b00100), .out(ID_R2), .sel(WB[4]));
  Button _1_2 (.out(\_1号中断 ));
  Button _2_2 (.out(\_2号中断 ));
  Button _3_2 (.out(\_3号中断 ));
  MIPS_Regifile mips_regifile_1 (
    .Din(RD), .Clk(CLK), .R1(mips_regifile_1_r1), .R2(mips_regifile_1_r2), .WE(WE), .W_num(WR),
    .R1_num(ID_R1), .R2_num(ID_R2));
  Comparator #(.width(2), .mode("unsigned")) comparator_1 (
    .a(priority_encoder_1_out), .b(2'b00), .gt(comparator_1_gt));  // open: eq, lt
  Register #(.width(2)) register_2 (.D(priority_encoder_1_out), .Q(NUM), .clk(\中断信号 ));  // open: en, clr
  LED _1_3 (.in(\_1号中断等待指示 ));
  LED _2_3 (.in(\_2号中断等待指示 ));
  LED _3_3 (.in(\_3号中断等待指示 ));
  Counter #(.width(16), .max('hffff)) counter_4 (
    .count(LOAD_USE), .Q(\LoadUse次数 ), .clk(CLK), .clr(RST));  // open: load, D, carry
  ID_EX id_ex_1 (
    .WB(WB), .MEM({JR, JMP, MEM}), .EX(EX), .IR({OP, if_id_1_ir_2_2, if_id_1_ir_2, FUNC}), .PC(IR_ADD),
    .A(mips_regifile_1_r1), .B(mips_regifile_1_r2), .SHMAT(im), .\传输状态In_表明当前传输数据有效 (IF_ID), .CLK(CLK),
    .WB_2({id_ex_1_wb_2[4:2], EX_WE, id_ex_1_wb_2[0]}), .MEM_2({JRr, JMPp, id_ex_1_mem_2}),
    .EX_2(id_ex_1_ex_2), .IR_2({ALU_OP, id_ex_1_ir_2_2, shamt, id_ex_1_ir_2}), .PC_2(id_ex_1_pc_2),
    .A_2(alu_1), .B_2(alu_5), .SHMAT_2(id_ex_1_shmat_2), .\传输状态Out_表明当前传输数据有效 (ID_EX),
    .\同步清零_气泡_高电平有效 (or_2_out), .\使能端_低电平有效_stall_高电平有效 (not_3_out), .R1(R1_CON), .R1_2(R1_con_t),
    .R2(R2_CON), .R2_2(R2_con_t));  // open: miss, miss_2, dataout, dataout_2
  Multiplexer #(.select(2), .width(32), .enable("false")) multiplexer_12 (
    .in1(32'h4), .in2(32'h1c8), .in3(32'h38c), .out(multiplexer_12_out), .sel(priority_encoder_1_out));  // open: in0
  Register #(.width(32)) PC_IR (.D(multiplexer_12_out), .Q(IR_PC), .clk(\中断信号 ));  // open: en, clr
  and and_7 (\中断信号 , block, comparator_1_gt);
  Multiplexer #(.width(32), .enable("false")) multiplexer_13 (
    .in0(alu_b), .in1(id_ex_1_shmat_2), .out(multiplexer_13_out), .sel(id_ex_1_ex_2[4]));
  Shifter #(.width(32)) shifter_1 (.in(id_ex_1_shmat_2), .\dist (5'b00010), .out(shifter_1_out));
  // Probe on \中断级别 
  Comparator #(.width(32)) comparator_2 (.a(alu_1), .b(32'h1), .lt(comparator_2_lt));  // open: gt, eq
  Comparator #(.width(6)) comparator_3 (.a(ALU_OP), .b(6'b000001), .eq(comparator_3_eq));  // open: gt, lt
  not not_4 (not_4_out, EQUL);
  Multiplexer #(.width(32), .enable("false")) multiplexer_14 (
    .in0({pc_4[31:28], id_ex_1_ir_2_2, shamt, id_ex_1_ir_2, 2'b00}), .in1(alu_1), .out(JMPA), .sel(JRr));
  MIPS_ALU mips_alu_1 (
    .X(alu_a), .Y(multiplexer_13_out), .AluOP(id_ex_1_ex_2[3:0]), .Equal(EQUL), .Result(mips_alu_1_result),
    .shamt(multiplexer_15_out));  // open: Result_2
  Multiplexer #(.width(5), .enable("false")) multiplexer_15 (
    .in0(shamt), .in1(alu_1[4:0]), .out(multiplexer_15_out), .sel(SRAV));
  Adder #(.width(32)) adder_2 (.a(shifter_1_out), .b(pc_4), .out(\分支a ));  // open: cin, cout
  Comparator #(.width(6)) comparator_4 (.a(ALU_OP), .b({6{1'b0}}), .eq(comparator_4_eq));  // open: gt, lt
  and and_8 (SRAV, comparator_4_eq, comparator_5_eq);
  Comparator #(.width(6)) comparator_5 (.a(id_ex_1_ir_2), .b(6'b000111), .eq(comparator_5_eq));  // open: gt, lt
  and and_9 (BGEZ, ~comparator_2_lt, comparator_3_eq);  // AND_Gate
  and and_10 (and_10_out, id_ex_1_mem_2[0], EQUL);
  and and_11 (and_11_out, id_ex_1_mem_2[1], not_4_out);
  or or_3 (\分支 , JMPp, and_10_out, BGEZ, and_11_out);
  Multiplexer #(.width(5), .enable("false")) multiplexer_16 (
    .in0(id_ex_1_ir_2_2[20:16]), .in1(id_ex_1_ir_2_2[15:11]), .out(multiplexer_16_out), .sel(id_ex_1_wb_2[3]));
  Multiplexer #(.width(5), .enable("false")) multiplexer_17 (
    .in0(multiplexer_16_out), .in1({5{1'b1}}), .out(EX_WR), .sel(id_ex_1_wb_2[2]));
  Register #(.width(1)) register_3 (.D(\分支 ), .Q(register_3_q));  // open: en, clk, clr
  Adder #(.width(32)) adder_3 (.a(32'h4), .b(id_ex_1_pc_2), .out(pc_4));  // open: cin, cout
  EX_MEM ex_mem_1 (
    .WB({id_ex_1_wb_2[4:2], EX_WE, id_ex_1_wb_2[0]}), .MEM({JRr, JMPp, id_ex_1_mem_2}),
    .IR({ALU_OP, id_ex_1_ir_2_2, shamt, id_ex_1_ir_2}), .PC(id_ex_1_pc_2), .B(alu_b),
    .ALU(mips_alu_1_result), .\传输状态In_表明当前传输数据有效 (ID_EX), .CLK(CLK),
    .WB_2({ex_mem_1_wb_2[4:2], MEM_WE, ex_mem_1_wb_2[0]}), .MEM_2(ex_mem_1_mem_2), .IR_2(ex_mem_1_ir_2),
    .PC_2(ex_mem_1_pc_2), .B_2(ex_mem_1_b_2), .ALU_2(alu_2), .\传输状态Out_表明当前传输数据有效 (EX_MEM),
    .\使能端_低电平有效_stall_高电平有效 (not_3_out), .A(alu_a), .A_2(ex_mem_1_a_2));  // open: 同步清零_气泡_高电平有效
  Multiplexer #(.select(2), .width(32), .enable("false")) multiplexer_18 (
    .in0(alu_1), .in1(alu_2), .in2(RD), .in3(alu_2), .out(alu_a), .sel(R1_con_t_t));
  Multiplexer #(.select(2), .width(32), .enable("false")) multiplexer_19 (
    .in0(alu_5), .in1(alu_2), .in2(RD), .in3(alu_2), .out(alu_b), .sel(R2_con_t));
  Register #(.width(1)) register_4 (.D(register_3_q), .Q(\分支_IR ));  // open: en, clk, clr
  Comparator #(.width(32)) comparator_6 (.a(R1), .b(32'h32), .eq(comparator_6_eq));  // open: gt, lt
  Multiplexer #(.width(5), .enable("false")) multiplexer_20 (
    .in0(ex_mem_1_ir_2[20:16]), .in1(ex_mem_1_ir_2[15:11]), .out(multiplexer_20_out), .sel(ex_mem_1_wb_2[3]));
  and and_12 (and_12_out, comparator_6_eq, sys);
  not not_5 (not_5_out, comparator_6_eq);
  Multiplexer #(.width(5), .enable("false")) multiplexer_21 (
    .in0(multiplexer_20_out), .in1({5{1'b1}}), .out(MEM_WR), .sel(ex_mem_1_wb_2[2]));
  not not_6 (not_6_out, and_12_out);
  and and_13 (and_13_out, not_5_out, sys);
  RAM #(.addrWidth(10), .dataWidth(32), .bus("separate")) ram_1 (
    .addr(alu_2[11:2]), .din(ex_mem_1_b_2), .data(ram_1_data), .str(ex_mem_1_mem_2[2]), .sel(sel), .clk(CLK),
    .clr(RST));  // open: ld
  or or_4 (sel, Go, not_6_out);
  Register #(.width(32)) register_5 (.D(R2), .en(and_13_out), .Q(LedData), .clk(CLK), .clr(RST));
  MEM_WB mem_wb_1 (
    .WB({ex_mem_1_wb_2[4:2], MEM_WE, ex_mem_1_wb_2[0]}), .IR(ex_mem_1_ir_2), .PC(ex_mem_1_pc_2), .ALU(alu_2),
    .MD(ram_1_data), .\传输状态In_表明当前传输数据有效 (EX_MEM), .CLK(CLK),
    .WB_2({sys, mem_wb_1_wb_2[3:2], WE, mem_wb_1_wb_2[0]}), .IR_2(mem_wb_1_ir_2), .PC_2(mem_wb_1_pc_2),
    .ALU_2({mem_wb_1_alu_2[31:2], select, mem_wb_1_alu_2[0]}), .MD_2(mem_wb_1_md_2),
    .\使能端_低电平有效_stall_高电平有效 (not_3_out), .A(ex_mem_1_a_2), .A_2(R1), .B(ex_mem_1_b_2), .B_2(R2));  // open: 传输状态Out_表明当前传输数据有效, 同步清零_气泡_高电平有效
  Adder #(.width(32)) adder_4 (.a(mem_wb_1_pc_2), .b(32'h4), .out(W_PC));  // open: cin, cout
  Multiplexer #(.width(32)) multiplexer_22 (
    .in0({mem_wb_1_alu_2[31:2], select, mem_wb_1_alu_2[0]}), .in1(mem_wb_1_md_2), .out(multiplexer_22_out),
    .sel(mem_wb_1_wb_2[0]));  // open: en
  Multiplexer #(.width(5), .enable("false")) multiplexer_23 (
    .in0(mem_wb_1_ir_2[20:16]), .in1(mem_wb_1_ir_2[15:11]), .out(multiplexer_23_out), .sel(mem_wb_1_wb_2[3]));
  Multiplexer #(.width(16), .enable("false")) multiplexer_24 (
    .in0(multiplexer_22_out[15:0]), .in1(multiplexer_22_out[31:16]), .out(multiplexer_24_out), .sel(select));
  Comparator #(.width(6)) comparator_7 (.a(mem_wb_1_ir_2[31:26]), .b(6'b010000), .eq(comparator_7_eq));  // open: gt, lt
  Comparator #(.width(6)) comparator_8 (.a(mem_wb_1_ir_2[5:0]), .b(6'b011000), .eq(comparator_8_eq));  // open: gt, lt
  Comparator #(.width(6)) comparator_9 (.a(mem_wb_1_ir_2[31:26]), .b(6'b100001), .eq(comparator_9_eq));  // open: gt, lt
  Multiplexer #(.width(32), .enable("false")) multiplexer_25 (
    .in0(multiplexer_22_out), .in1(bit_extender_3_out), .out(multiplexer_25_out), .sel(comparator_9_eq));
  assign bit_extender_3_out = {{16{multiplexer_24_out[15]}}, multiplexer_24_out};  // Bit_Extender bit_extender_3
  Multiplexer #(.width(5), .enable("false")) multiplexer_26 (
    .in0(multiplexer_23_out), .in1({5{1'b1}}), .out(WR), .sel(mem_wb_1_wb_2[2]));
  and and_14 (ERET, comparator_7_eq, comparator_8_eq);
  Multiplexer #(.width(32)) multiplexer_27 (
    .in0(multiplexer_25_out), .in1(W_PC), .out(RD), .sel(mem_wb_1_wb_2[2]));  // open: en

  // Other names for the same wires on the sheet: MEM[4:3] = {JR, JMP}; R1_EX[31:0] = alu_1

  // Notes on the sheet:
  //   中断源
  //   中断等待指示
  //   数码管输出
  //   contents of rom_1 (hex, n*v repeats v):
  //   8000d54 23bdfffc afa10000 23bdfffc afa20000 23bdfffc afa30000 23bdfffc afa40000 23bdfffc afa50000
  //   23bdfffc afa60000 23bdfffc afa70000 23bdfffc afa80000 23bdfffc afa90000 23bdfffc afaa0000 23bdfffc
  //   afab0000 23bdfffc afac0000 23bdfffc afad0000 23bdfffc afae0000 23bdfffc afaf0000 23bdfffc afb00000
  //   23bdfffc afb10000 23bdfffc afb20000 23bdfffc afb30000 23bdfffc afb40000 23bdfffc afb50000 23bdfffc
  //   afb60000 23bdfffc afb70000 23bdfffc afb80000 23bdfffc afb90000 20160001 20140006 20150001 168020
  //   108100 2149825 132020 20020022 c 1600fffa 295a022 1680fff7 8fb90000 23bd0004 8fb80000 23bd0004
  //   8fb70000 23bd0004 8fb60000 23bd0004 8fb50000 23bd0004 8fb40000 23bd0004 8fb30000 23bd0004 8fb20000
  //   23bd0004 8fb10000 23bd0004 8fb00000 23bd0004 8faf0000 23bd0004 8fae0000 23bd0004 8fad0000 23bd0004
  //   8fac0000 23bd0004 8fab0000 23bd0004 8faa0000 23bd0004 8fa90000 23bd0004 8fa80000 23bd0004 8fa70000
  //   23bd0004 8fa60000 23bd0004 8fa50000 23bd0004 8fa40000 23bd0004 8fa30000 23bd0004 8fa20000 23bd0004
  //   8fa10000 23bd0004 42000018 23bdfffc afa10000 23bdfffc afa20000 23bdfffc afa30000 23bdfffc afa40000
  //   23bdfffc afa50000 23bdfffc afa60000 23bdfffc afa70000 23bdfffc afa80000 23bdfffc afa90000 23bdfffc
  //   afaa0000 23bdfffc afab0000 23bdfffc afac0000 23bdfffc afad0000 23bdfffc afae0000 23bdfffc afaf0000
  //   23bdfffc afb00000 23bdfffc afb10000 23bdfffc afb20000 23bdfffc afb30000 23bdfffc afb40000 23bdfffc
  //   afb50000 23bdfffc afb60000 23bdfffc afb70000 23bdfffc afb80000 23bdfffc afb90000 20160002 20140006
  //   20150001 168020 108100 2149825 132020 20020022 c 1600fffa 295a022 1680fff7 8fb90000 23bd0004
  //   8fb80000 23bd0004 8fb70000 23bd0004 8fb60000 23bd0004 8fb50000 23bd0004 8fb40000 23bd0004 8fb30000
  //   23bd0004 8fb20000 23bd0004 8fb10000 23bd0004 8fb00000 23bd0004 8faf0000 23bd0004 8fae0000 23bd0004
  //   8fad0000 23bd0004 8fac0000 23bd0004 8fab0000 23bd0004 8faa0000 23bd0004 8fa90000 23bd0004 8fa80000
  //   23bd0004 8fa70000 23bd0004 8fa60000 23bd0004 8fa50000 23bd0004 8fa40000 23bd0004 8fa30000 23bd0004
  //   8fa20000 23bd0004 8fa10000 23bd0004 42000018 23bdfffc afa10000 23bdfffc afa20000 23bdfffc afa30000
  //   23bdfffc afa40000 23bdfffc afa50000 23bdfffc afa60000 23bdfffc afa70000 23bdfffc afa80000 23bdfffc
  //   afa90000 23bdfffc afaa0000 23bdfffc afab0000 23bdfffc afac0000 23bdfffc afad0000 23bdfffc afae0000
  //   23bdfffc afaf0000 23bdfffc afb00000 23bdfffc afb10000 23bdfffc afb20000 23bdfffc afb30000 23bdfffc
  //   afb40000 23bdfffc afb50000 23bdfffc afb60000 23bdfffc afb70000 23bdfffc afb80000 23bdfffc afb90000
  //   20160003 20140006 20150001 168020 108100 2149825 132020 20020022 c 1600fffa 295a022 1680fff7
  //   8fb90000 23bd0004 8fb80000 23bd0004 8fb70000 23bd0004 8fb60000 23bd0004 8fb50000 23bd0004 8fb40000
  //   23bd0004 8fb30000 23bd0004 8fb20000 23bd0004 8fb10000 23bd0004 8fb00000 23bd0004 8faf0000 23bd0004
  //   8fae0000 23bd0004 8fad0000 23bd0004 8fac0000 23bd0004 8fab0000 23bd0004 8faa0000 23bd0004 8fa90000
  //   23bd0004 8fa80000 23bd0004 8fa70000 23bd0004 8fa60000 23bd0004 8fa50000 23bd0004 8fa40000 23bd0004
  //   8fa30000 23bd0004 8fa20000 23bd0004 8fa10000 23bd0004 42000018 20110200 20020022 112020 c 2231ffff
  //   1620fffc 20020032 c 2002000a c
  //   指令字
  //   流水调试日志用
  //   JMP
  //   JR
  //   OP
  //   OP
  //   Func
  //   Func
  //   rs
  //   rt
  //   rd
  //   Bne
  //   MemToReg
  //   MemWrite
  //   AluOP
  //   AluSrcB
  //   RegWrite
  //   JAL
  //   RegDst
  //   中断信号源及指示电路规范（优先级3>2>1>CPU(0）)
  //   Func
  //   rt
  //   rt
  //   rt
  //   rd
  //   OP
endmodule

module \多级中断  (
);

  wire \_1号中断 , \_1号中断等待指示 , \_2号中断 , \_2号中断等待指示 , \_3号中断 , \_3号中断等待指示 , and_1_out, and_5_out, and_6_out,
       and_7_out, and_8_out, and_9_out, and_10_out, and_11_out, block1, block2, block3, CLK, comparator_1_lt,
       comparator_2_eq, comparator_3_eq, comparator_5_eq, comparator_6_eq, comparator_7_eq, comparator_8_eq,
       comparator_9_eq, decoder_1_out1, decoder_1_out2, decoder_1_out3, ERET, Go, JAL, JMP, JR,
       mips_alu_1_equal, not_1_out, not_2_out, not_3_out, not_4_out, not_5_out, not_6_out, not_7_out, RegDst,
       register_1_q, register_2_q, register_3_q, register_4_q, register_5_q, RET1, RET2, RET3, RST, sel,
       select, SignedExt, SRAV, sys, \中断信号 , \中断信号_1_out_5 , \中断信号_2_out_5 , \中断信号_3_out_5 ,
       \硬布线控制器_1_alu_src , \硬布线控制器_1_beq , \硬布线控制器_1_bne , \硬布线控制器_1_memtoreg , \硬布线控制器_1_memwrite ,
       \硬布线控制器_1_regwrite ;
  wire [0:0] or_1_out;
  wire [1:0] block, priority_encoder_2_out, \中断级别 ;
  wire [3:0] PC31_28, \硬布线控制器_1_alu_op ;
  wire [4:0] multiplexer_7_out, multiplexer_8_out, multiplexer_9_out, multiplexer_10_out, multiplexer_11_out,
       multiplexer_14_out;
  wire [5:0] FUNC, OP;
  wire [15:0] multiplexer_18_out, \总周期数 , \无条件分支数 , \条件分支成功数 ;
  wire [25:6] Jaddress;
  wire [27:0] PC_q;
  wire [31:0] adder_1_out, adder_2_out, bit_extender_1_out, bit_extender_2_out, bit_extender_3_out, IR_PC,
       JLast, LedData, mips_alu_1_result, multiplexer_1_out, multiplexer_2_out, multiplexer_3_out,
       multiplexer_12_out, multiplexer_13_out, multiplexer_15_out, multiplexer_17_out, multiplexer_19_out,
       PC, PC_0_q, PC_1_q, PC_2_q, PC_STORE, R1, R2, ram_1_data, shifter_1_out;

  Button \u_总复位  (.out(RST));
  Button u_Go (.out(Go));
  Clock clock_1 (.out(CLK));
  Comparator #(.width(32)) comparator_1 (.a(R1), .b({32{1'b0}}), .lt(comparator_1_lt));  // open: gt, eq
  Comparator #(.width(6)) comparator_2 (.a(OP), .b(6'b000001), .eq(comparator_2_eq));  // open: gt, lt
  Hex_Digit_Display hex_digit_display_1 (.value(LedData[31:28]));  // open: dp
  Hex_Digit_Display hex_digit_display_2 (.value(LedData[27:24]));  // open: dp
  Multiplexer #(.width(32), .enable("false")) multiplexer_1 (
    .in0(adder_1_out), .in1(adder_2_out), .out(multiplexer_1_out), .sel(and_1_out));
  and and_1 (and_1_out, ~comparator_1_lt, comparator_2_eq);  // AND_Gate
  Hex_Digit_Display hex_digit_display_3 (.value(LedData[23:20]));  // open: dp
  Hex_Digit_Display hex_digit_display_4 (.value(LedData[19:16]));  // open: dp
  Multiplexer #(.select(2), .width(32), .enable("false")) multiplexer_2 (
    .in0(multiplexer_1_out), .in1(adder_2_out), .in2(JLast), .out(multiplexer_2_out), .sel({JMP, or_1_out[0]}));  // open: in3
  Register #(.width(32)) PC_0 (.D(PC), .Q(PC_0_q), .clk(block1));  // open: en, clr
  Register #(.width(32)) PC_1 (.D(PC), .Q(PC_1_q), .clk(block2));  // open: en, clr
  Register #(.width(32)) PC_2 (.D(PC), .Q(PC_2_q), .clk(block3));  // open: en, clr
  Hex_Digit_Display hex_digit_display_5 (.value(LedData[15:12]));  // open: dp
  Hex_Digit_Display hex_digit_display_6 (.value(LedData[11:8]));  // open: dp
  Multiplexer #(.width(32), .enable("false")) multiplexer_3 (
    .in0(multiplexer_2_out), .in1(IR_PC), .out(multiplexer_3_out), .sel(\中断信号 ));
  Hex_Digit_Display hex_digit_display_7 (.value(LedData[7:4]));  // open: dp
  Hex_Digit_Display hex_digit_display_8 (.value(LedData[3:0]));  // open: dp
  Multiplexer #(.width(32), .enable("false")) multiplexer_4 (
    .in0(multiplexer_3_out), .in1(PC_STORE), .out(PC), .sel(ERET));
  Decoder #(.select(2)) decoder_1 (
    .out1(decoder_1_out1), .out2(decoder_1_out2), .out3(decoder_1_out3), .sel(block));  // open: out0, en
  Multiplexer #(.select(2), .width(32), .enable("false")) multiplexer_5 (
    .in1(PC_0_q), .in2(PC_1_q), .in3(PC_2_q), .out(PC_STORE), .sel(block));  // open: in0
  \中断信号  \u_中断信号_1  (.in_2(block1), .out_6(\_1号中断等待指示 ), .in_3(RET1), .in_1(CLK), .out_5(\中断信号_1_out_5 ), .in_4(RST));
  \中断信号  \u_中断信号_2  (.in_2(block2), .out_6(\_2号中断等待指示 ), .in_3(RET2), .in_1(CLK), .out_5(\中断信号_2_out_5 ), .in_4(RST));
  \中断信号  \u_中断信号_3  (.in_2(block3), .out_6(\_3号中断等待指示 ), .in_3(RET3), .in_1(CLK), .out_5(\中断信号_3_out_5 ), .in_4(RST));
  and and_2 (RET1, ERET, decoder_1_out1);
  and and_3 (RET2, ERET, decoder_1_out2);
  and and_4 (RET3, ERET, decoder_1_out3);
  Register #(.width(32)) u_PC (.D(PC), .en(sel), .Q({PC31_28, PC_q}), .clk(CLK), .clr(RST));
  // Probe on \总周期数 
  // Probe on \无条件分支数 
  // Probe on \条件分支成功数 
  Adder #(.width(32)) adder_1 (.a({PC31_28, PC_q}), .b(32'h4), .out(adder_1_out));  // open: cin, cout
  Button _1 (.out(\_1号中断 ));
  Button _2 (.out(\_2号中断 ));
  Button _3 (.out(\_3号中断 ));
  ROM #(.addrWidth(10), .dataWidth(32)) rom_1 (.addr(PC_q[11:2]), .data({OP, Jaddress, FUNC}));  // open: sel
  Multiplexer #(.width(32), .enable("false")) multiplexer_6 (
    .in0({PC31_28, Jaddress, FUNC, 2'b00}), .in1(R1), .out(JLast), .sel(JR));
  Register #(.width(1)) register_1 (.D(1'b1), .Q(register_1_q), .clk(\_1号中断 ), .clr(RET1));  // open: en
  not not_1 (not_1_out, \_3号中断等待指示 );
  Multiplexer #(.width(5), .enable("false")) multiplexer_7 (
    .in0(Jaddress[25:21]), .in1({5{1'b1}}), .out(multiplexer_7_out), .sel(JR));
  assign bit_extender_1_out = {{16{Jaddress[15]}}, {Jaddress[15:6], FUNC}};  // Bit_Extender bit_extender_1
  assign bit_extender_2_out = {{16{1'b0}}, {Jaddress[15:6], FUNC}};  // Bit_Extender bit_extender_2
  Register #(.width(1)) register_2 (.D(register_1_q), .en(not_1_out), .Q(register_2_q), .clk(CLK), .clr(RET1));
  not not_2 (not_2_out, \_2号中断等待指示 );
  Register #(.width(1)) register_3 (.D(1'b1), .Q(register_3_q), .clk(\_2号中断 ), .clr(RET2));  // open: en
  not not_3 (not_3_out, \_3号中断等待指示 );
  LED _1_2 (.in(\_1号中断等待指示 ));
  LED _2_2 (.in(\_2号中断等待指示 ));
  LED _3_2 (.in(\_3号中断等待指示 ));
  \硬布线控制器  \u_硬布线控制器_1  (
    .Func(FUNC), .OP(OP), .ALU_OP(\硬布线控制器_1_alu_op ), .MemToReg(\硬布线控制器_1_memtoreg ),
    .MemWrite(\硬布线控制器_1_memwrite ), .ALU_SRC(\硬布线控制器_1_alu_src ), .RegWrite(\硬布线控制器_1_regwrite ),
    .SysCALL(sys), .SignedExt(SignedExt), .RegDst(RegDst), .JR(JR), .JMP(JMP), .Beq(\硬布线控制器_1_beq ),
    .JAL(JAL), .Bne(\硬布线控制器_1_bne ));
  Multiplexer #(.width(5), .enable("false")) multiplexer_8 (
    .in0(multiplexer_7_out), .in1(5'b00010), .out(multiplexer_8_out), .sel(sys));
  Multiplexer #(.width(5), .enable("false")) multiplexer_9 (
    .in0(Jaddress[20:16]), .in1(5'b00100), .out(multiplexer_9_out), .sel(sys));
  Multiplexer #(.width(5), .enable("false")) multiplexer_10 (
    .in0(Jaddress[20:16]), .in1(Jaddress[15:11]), .out(multiplexer_10_out), .sel(RegDst));
  Multiplexer #(.width(5), .enable("false")) multiplexer_11 (
    .in0(multiplexer_10_out), .in1({5{1'b1}}), .out(multiplexer_11_out), .sel(JAL));
  Multiplexer #(.width(32), .enable("false")) multiplexer_12 (
    .in0(bit_extender_1_out), .in1(bit_extender_2_out), .out(multiplexer_12_out), .sel(SignedExt));
  Counter #(.width(16), .max('hffff)) counter_1 (
    .count(sel), .Q(\总周期数 ), .clk(CLK), .clr(RST));  // open: load, D, carry
  Register #(.width(1)) register_4 (.D(register_2_q), .en(not_2_out), .Q(register_4_q), .clk(CLK), .clr(RET1));
  Register #(.width(1)) register_5 (.D(register_3_q), .en(not_3_out), .Q(register_5_q), .clk(CLK), .clr(RET2));
  MIPS_Regifile mips_regifile_1 (
    .Din(multiplexer_15_out), .Clk(CLK), .R1(R1), .R2(R2), .WE(\硬布线控制器_1_regwrite ),
    .W_num(multiplexer_11_out), .R1_num(multiplexer_8_out), .R2_num(multiplexer_9_out));
  and and_5 (and_5_out, register_4_q, ~\中断信号_1_out_5 );  // AND_Gate
  and and_6 (and_6_out, register_5_q, ~\中断信号_2_out_5 );  // AND_Gate
  and and_7 (and_7_out, \_3号中断 , ~\中断信号_3_out_5 );  // AND_Gate
  // Probe on \中断级别 
  Multiplexer #(.width(32), .enable("false")) multiplexer_13 (
    .in0(R2), .in1(multiplexer_12_out), .out(multiplexer_13_out), .sel(\硬布线控制器_1_alu_src ));
  Shifter #(.width(32)) shifter_1 (.in(multiplexer_12_out), .\dist (5'b00010), .out(shifter_1_out));
  Priority_Encoder #(.select(2)) priority_encoder_1 (
    .in0(1'b1), .in1(\中断信号_1_out_5 ), .in2(\中断信号_2_out_5 ), .in3(\中断信号_3_out_5 ), .out(block));  // open: gs, en_out, en_in
  MIPS_ALU mips_alu_1 (
    .X(R1), .Y(multiplexer_13_out), .AluOP(\硬布线控制器_1_alu_op ), .Equal(mips_alu_1_equal),
    .Result({mips_alu_1_result[31:2], select, mips_alu_1_result[0]}), .shamt(multiplexer_14_out));  // open: Result_2
  Multiplexer #(.width(5), .enable("false")) multiplexer_14 (
    .in0(Jaddress[10:6]), .in1(R1[4:0]), .out(multiplexer_14_out), .sel(SRAV));
  Comparator #(.width(32)) comparator_3 (.a(R1), .b(32'h32), .eq(comparator_3_eq));  // open: gt, lt
  and and_8 (and_8_out, \硬布线控制器_1_beq , mips_alu_1_equal);
  and and_9 (and_9_out, \硬布线控制器_1_bne , not_4_out);
  not not_4 (not_4_out, mips_alu_1_equal);
  Adder #(.width(32)) adder_2 (.a(shifter_1_out), .b(adder_1_out), .out(adder_2_out));  // open: cin, cout
  and and_10 (and_10_out, comparator_3_eq, sys);
  not not_5 (not_5_out, comparator_3_eq);
  and and_11 (and_11_out, not_5_out, sys);
  Priority_Encoder #(.select(2), .disabled(0)) priority_encoder_2 (
    .in0(1'b1), .in1(and_5_out), .in2(and_6_out), .in3(and_7_out), .out(priority_encoder_2_out));  // open: gs, en_out, en_in
  or or_1 (or_1_out[0], and_8_out, and_9_out);
  Multiplexer #(.width(32), .enable("false")) multiplexer_15 (
    .in0(multiplexer_19_out), .in1(adder_1_out), .out(multiplexer_15_out), .sel(JAL));
  not not_6 (not_6_out, and_10_out);
  Register #(.width(32)) register_6 (.D(R2), .en(and_11_out), .Q(LedData), .clk(CLK), .clr(RST));
  Multiplexer #(.select(2), .width(32), .enable("false")) multiplexer_16 (
    .in1(32'h4), .in2(32'h1c8), .in3(32'h38c), .out(IR_PC), .sel(priority_encoder_2_out));  // open: in0
  Demultiplexer #(.select(2), .disabled(0)) demultiplexer_1 (
    .out1(block1), .out2(block2), .out3(block3), .in(1'b1), .sel(priority_encoder_2_out), .en(\中断信号 ));  // open: out0
  Comparator #(.width(2), .mode("unsigned")) comparator_4 (
    .a(priority_encoder_2_out), .b(block), .gt(\中断信号 ));  // open: eq, lt
  Counter #(.width(16), .max('hffff)) counter_2 (
    .count(or_1_out[0]), .Q(\条件分支成功数 ), .clk(CLK), .clr(RST));  // open: load, D, carry
  RAM #(.addrWidth(10), .dataWidth(32), .bus("separate")) ram_1 (
    .addr(mips_alu_1_result[11:2]), .din(R2), .data(ram_1_data), .str(\硬布线控制器_1_memwrite ), .sel(sel),
    .clk(CLK), .ld(not_7_out), .clr(RST));
  not not_7 (not_7_out, \硬布线控制器_1_memwrite );
  or or_2 (sel, Go, not_6_out);
  Multiplexer #(.width(32), .enable("false")) multiplexer_17 (
    .in0({mips_alu_1_result[31:2], select, mips_alu_1_result[0]}), .in1(ram_1_data),
    .out(multiplexer_17_out), .sel(\硬布线控制器_1_memtoreg ));
  Multiplexer #(.width(16), .enable("false")) multiplexer_18 (
    .in0(multiplexer_17_out[15:0]), .in1(multiplexer_17_out[31:16]), .out(multiplexer_18_out), .sel(select));
  Counter #(.width(16), .max('hffff)) counter_3 (
    .count(JMP), .Q(\无条件分支数 ), .clk(CLK), .clr(RST));  // open: load, D, carry
  Comparator #(.width(6)) comparator_5 (.a(OP), .b(6'b010000), .eq(comparator_5_eq));  // open: gt, lt
  Comparator #(.width(6)) comparator_6 (.a(FUNC), .b(6'b011000), .eq(comparator_6_eq));  // open: gt, lt
  Comparator #(.width(6)) comparator_7 (.a(OP), .b({6{1'b0}}), .eq(comparator_7_eq));  // open: gt, lt
  Comparator #(.width(6)) comparator_8 (.a(FUNC), .b(6'b000111), .eq(comparator_8_eq));  // open: gt, lt
  Comparator #(.width(6)) comparator_9 (.a(OP), .b(6'b100001), .eq(comparator_9_eq));  // open: gt, lt
  Multiplexer #(.width(32), .enable("false")) multiplexer_19 (
    .in0(multiplexer_17_out), .in1(bit_extender_3_out), .out(multiplexer_19_out), .sel(comparator_9_eq));
  assign bit_extender_3_out = {{16{multiplexer_18_out[15]}}, multiplexer_18_out};  // Bit_Extender bit_extender_3
  and and_12 (ERET, comparator_5_eq, comparator_6_eq);
  and and_13 (SRAV, comparator_7_eq, comparator_8_eq);

  // Other names for the same wires on the sheet: Jaddress[5:0] = FUNC; shamt[4:0] = Jaddress[10:6]

  // Notes on the sheet:
  //   数码管输出应该用寄存器锁存，否则显示数据只能一闪而过
  //   可以通过项目增加Logisim库的方式将前几次实验完成的电路作为子电路引入到本电路中使用
  //   数码管输出
  //   总复位信号应将除ROM以外所有存储组件全部清零
  //   指令存储器
  //   指令字
  //   contents of rom_1 (hex, n*v repeats v):
  //   8000d54 23bdfffc afa10000 23bdfffc afa20000 23bdfffc afa30000 23bdfffc afa40000 23bdfffc afa50000
  //   23bdfffc afa60000 23bdfffc afa70000 23bdfffc afa80000 23bdfffc afa90000 23bdfffc afaa0000 23bdfffc
  //   afab0000 23bdfffc afac0000 23bdfffc afad0000 23bdfffc afae0000 23bdfffc afaf0000 23bdfffc afb00000
  //   23bdfffc afb10000 23bdfffc afb20000 23bdfffc afb30000 23bdfffc afb40000 23bdfffc afb50000 23bdfffc
  //   afb60000 23bdfffc afb70000 23bdfffc afb80000 23bdfffc afb90000 20160001 20140006 20150001 168020
  //   108100 2149825 132020 20020022 c 1600fffa 295a022 1680fff7 8fb90000 23bd0004 8fb80000 23bd0004
  //   8fb70000 23bd0004 8fb60000 23bd0004 8fb50000 23bd0004 8fb40000 23bd0004 8fb30000 23bd0004 8fb20000
  //   23bd0004 8fb10000 23bd0004 8fb00000 23bd0004 8faf0000 23bd0004 8fae0000 23bd0004 8fad0000 23bd0004
  //   8fac0000 23bd0004 8fab0000 23bd0004 8faa0000 23bd0004 8fa90000 23bd0004 8fa80000 23bd0004 8fa70000
  //   23bd000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
  //   JMP
  //   JR
  //   OP
  //   OP
  //   Func
  //   Func
  //   rs
  //   rt
  //   rd
  //   中断信号源及指示电路规范（优先级3>2>1>CPU(0）)
  //   Beq
  //   Bne
  //   MemToReg
  //   MemWrite
  //   AluOP
  //   AluSrcB
  //   RegWrite
  //   JAL
  //   RegDst
  //   Syscall
endmodule
